// Logisim project alu.circ as structural Verilog
// FA
module \一位全加器FA封装1  (
  input  Cin,
  input  Xi,
  input  Yi,
  output Cout,
  output Si
);

  wire AND_2_out, AND_out, XOR_2_out;

  or OR (Cout, AND_out, AND_2_out);
  and AND (AND_out, Xi, Yi);
  and AND_2 (AND_2_out, Cin, XOR_2_out);
  xor XOR (Si, Cin, XOR_2_out);
  xor XOR_2 (XOR_2_out, Xi, Yi);

  // Notes on the sheet:
  //   Si = Xi ^ Yi ^ Cin
  //   Cout = Xi Yi + Cin (Xi ^ Yi)
endmodule

module \一位全加器FA封装2  (
  input  Cin,
  input  Xi,
  input  Yi,
  output Cout,
  output Si
);

  wire AND_2_out, AND_out, XOR_2_out;

  or OR (Cout, AND_out, AND_2_out);
  and AND (AND_out, Xi, Yi);
  and AND_2 (AND_2_out, Cin, XOR_2_out);
  xor XOR (Si, Cin, XOR_2_out);
  xor XOR_2 (XOR_2_out, Xi, Yi);

  // Notes on the sheet:
  //   Si = Xi ^ Yi ^ Cin
  //   Cout = Xi Yi + Cin (Xi ^ Yi)
endmodule

module \一位全加器FA封装3  (
  input  Cin,
  input  Xi,
  input  Yi,
  output Cout,
  output Si
);

  wire AND_2_out, AND_out, XOR_2_out;

  or OR (Cout, AND_out, AND_2_out);
  and AND (AND_out, Xi, Yi);
  and AND_2 (AND_2_out, Cin, XOR_2_out);
  xor XOR (Si, Cin, XOR_2_out);
  xor XOR_2 (XOR_2_out, Xi, Yi);

  // Notes on the sheet:
  //   Si = Xi ^ Yi ^ Cin
  //   Cout = Xi Yi + Cin (Xi ^ Yi)
endmodule

// ADD
module \_8位串行加法器  (
  input  [7:0] X,
  input  [7:0] Y,
  input  Cin,
  output [7:0] S,
  output Cout,
  output Overflow
);

  wire \一位全加器fa封装1_2_cout , \一位全加器fa封装1_3_cout , \一位全加器fa封装1_4_cout , \一位全加器fa封装1_5_cout ,
       \一位全加器fa封装1_6_cout , \一位全加器fa封装1_7_cout , \一位全加器fa封装1_8_cout ;

  xor xor_1 (Overflow, Cout, \一位全加器fa封装1_2_cout );
  \一位全加器FA封装1  \u_一位全加器fa封装1_1  (.Cout(Cout), .Si(S[7]), .Cin(\一位全加器fa封装1_2_cout ), .Xi(X[7]), .Yi(Y[7]));
  \一位全加器FA封装1  \u_一位全加器fa封装1_2  (
    .Cout(\一位全加器fa封装1_2_cout ), .Si(S[6]), .Cin(\一位全加器fa封装1_3_cout ), .Xi(X[6]), .Yi(Y[6]));
  \一位全加器FA封装1  \u_一位全加器fa封装1_3  (
    .Cout(\一位全加器fa封装1_3_cout ), .Si(S[5]), .Cin(\一位全加器fa封装1_4_cout ), .Xi(X[5]), .Yi(Y[5]));
  \一位全加器FA封装1  \u_一位全加器fa封装1_4  (
    .Cout(\一位全加器fa封装1_4_cout ), .Si(S[4]), .Cin(\一位全加器fa封装1_5_cout ), .Xi(X[4]), .Yi(Y[4]));
  \一位全加器FA封装1  \u_一位全加器fa封装1_5  (
    .Cout(\一位全加器fa封装1_5_cout ), .Si(S[3]), .Cin(\一位全加器fa封装1_6_cout ), .Xi(X[3]), .Yi(Y[3]));
  \一位全加器FA封装1  \u_一位全加器fa封装1_6  (
    .Cout(\一位全加器fa封装1_6_cout ), .Si(S[2]), .Cin(\一位全加器fa封装1_7_cout ), .Xi(X[2]), .Yi(Y[2]));
  // Probe on X
  // Probe on Y
  // Probe on S
  \一位全加器FA封装1  \u_一位全加器fa封装1_7  (
    .Cout(\一位全加器fa封装1_7_cout ), .Si(S[1]), .Cin(\一位全加器fa封装1_8_cout ), .Xi(X[1]), .Yi(Y[1]));
  // Probe on X
  // Probe on Y
  // Probe on S
  \一位全加器FA封装1  \u_一位全加器fa封装1_8  (.Cout(\一位全加器fa封装1_8_cout ), .Si(S[0]), .Cin(Cin), .Xi(X[0]), .Yi(Y[0]));

  // Other names for the same wires on the sheet: OF = Overflow

  // Notes on the sheet:
  //   输入引脚区
  //   符号位
  //   输出引脚区
  //   +
  //   =
  //   有符号加法
  //   +
  //   =
  //   无符号加法
endmodule

// CAS
module \_8位可控加减法器  (
  input  [7:0] X,
  input  [7:0] Y,
  input  Cin,
  input  Sub,
  output [7:0] S,
  output Cout,
  output Overflow
);

  wire xor_2_out, xor_3_out, xor_4_out, xor_5_out, xor_6_out, xor_7_out, xor_8_out, xor_9_out, xor_10_out,
       \一位全加器fa封装1_2_cout , \一位全加器fa封装1_3_cout , \一位全加器fa封装1_4_cout , \一位全加器fa封装1_5_cout ,
       \一位全加器fa封装1_6_cout , \一位全加器fa封装1_7_cout , \一位全加器fa封装1_8_cout ;
  wire [8:0] C;

  xor xor_1 (Overflow, Cout, \一位全加器fa封装1_2_cout );
  \一位全加器FA封装1  \u_一位全加器fa封装1_1  (.Cout(Cout), .Si(S[7]), .Cin(\一位全加器fa封装1_2_cout ), .Xi(X[7]), .Yi(xor_2_out));
  xor xor_2 (xor_2_out, Y[7], Sub);
  \一位全加器FA封装1  \u_一位全加器fa封装1_2  (
    .Cout(\一位全加器fa封装1_2_cout ), .Si(S[6]), .Cin(\一位全加器fa封装1_3_cout ), .Xi(X[6]), .Yi(xor_3_out));
  xor xor_3 (xor_3_out, Y[6], Sub);
  \一位全加器FA封装1  \u_一位全加器fa封装1_3  (
    .Cout(\一位全加器fa封装1_3_cout ), .Si(S[5]), .Cin(\一位全加器fa封装1_4_cout ), .Xi(X[5]), .Yi(xor_4_out));
  xor xor_4 (xor_4_out, Y[5], Sub);
  \一位全加器FA封装1  \u_一位全加器fa封装1_4  (
    .Cout(\一位全加器fa封装1_4_cout ), .Si(S[4]), .Cin(\一位全加器fa封装1_5_cout ), .Xi(X[4]), .Yi(xor_5_out));
  xor xor_5 (xor_5_out, Y[4], Sub);
  \一位全加器FA封装1  \u_一位全加器fa封装1_5  (
    .Cout(\一位全加器fa封装1_5_cout ), .Si(S[3]), .Cin(\一位全加器fa封装1_6_cout ), .Xi(X[3]), .Yi(xor_6_out));
  xor xor_6 (xor_6_out, Y[3], Sub);
  \一位全加器FA封装1  \u_一位全加器fa封装1_6  (
    .Cout(\一位全加器fa封装1_6_cout ), .Si(S[2]), .Cin(\一位全加器fa封装1_7_cout ), .Xi(X[2]), .Yi(xor_7_out));
  xor xor_7 (xor_7_out, Y[2], Sub);
  // Probe on X
  // Probe on Y
  // Probe on S
  \一位全加器FA封装1  \u_一位全加器fa封装1_7  (
    .Cout(\一位全加器fa封装1_7_cout ), .Si(S[1]), .Cin(\一位全加器fa封装1_8_cout ), .Xi(X[1]), .Yi(xor_8_out));
  xor xor_8 (xor_8_out, Y[1], Sub);
  DotMatrix #(.matrixcols(3), .matrixrows(3)) dotmatrix_1 (.col0(C[8:6]), .col1(C[5:3]), .col2(C[2:0]));
  \一位全加器FA封装1  \u_一位全加器fa封装1_8  (.Cout(\一位全加器fa封装1_8_cout ), .Si(S[0]), .Cin(xor_9_out), .Xi(X[0]), .Yi(xor_10_out));
  xor xor_9 (xor_9_out, Cin, Sub);
  xor xor_10 (xor_10_out, Y[0], Sub);
  // Probe on X
  // Probe on Y
  // Probe on S
  Multiplexer #(.width(9), .enable("false")) multiplexer_1 (.in0(9'hba), .in1(9'h92), .out(C), .sel(Sub));

  // Other names for the same wires on the sheet: OF = Overflow

  // Notes on the sheet:
  //   输入引脚区
  //   符号位
  //   输出引脚区
  //   =
  //   有符号
  //   =
  //   无符号
endmodule

// CLA74182
module CLA74182 (
  input  G4,
  input  P4,
  input  G3,
  input  P3,
  input  G2,
  input  P2,
  input  G1,
  input  P1,
  input  Cin,
  output C4,
  output C3,
  output C2,
  output C1,
  output G_star,
  output P_star
);

  _74182 u_74182_1 (
    .G4(G4), .P4(P4), .G(G_star), .G3(G3), .P3(P3), .P(P_star), .G2(G2), .P2(P2), .C4(C4), .G1(G1), .P1(P1),
    .C(Cin), .C3(C3), .C2(C2), .C1(C1));

  // Notes on the sheet:
  //   输入引脚区
  //   请根据以上引脚以及隧道信号设计完成74LS182先行进位电路
  //   输出引脚区
  //   请勿增改引脚定义
endmodule

// 4位快速加法器
module \_4位快速加法器  (
  input  [3:0] X,
  input  [3:0] Y,
  input  Cin,
  output [3:0] S,
  output Cout,
  output G_star,
  output P_star
);

  wire and_1_out, and_2_out, and_3_out, and_4_out, and_5_out, C1, C2, C3, C4, xor_1_out, xor_3_out,
       xor_5_out, xor_7_out;

  and and_1 (and_1_out, X[3], Y[3]);
  xor xor_1 (xor_1_out, X[3], Y[3]);
  and and_2 (and_2_out, X[2], Y[2]);
  CLA74182 cla74182_1 (
    .G4(and_1_out), .P4(xor_1_out), .G3(and_2_out), .P3(xor_3_out), .G2(and_3_out), .P2(xor_5_out),
    .G1(and_4_out), .P1(xor_7_out), .Cin(Cin), .C4(C4), .C3(C3), .C2(C2), .C1(C1), .G_star(G_star),
    .P_star(P_star));
  xor xor_2 (S[3], X[3], Y[3], C3);
  xor xor_3 (xor_3_out, X[2], Y[2]);
  xor xor_4 (S[2], X[2], Y[2], C2);
  xor xor_5 (xor_5_out, X[1], Y[1]);
  and and_3 (and_3_out, X[1], Y[1]);
  and and_4 (and_4_out, X[0], Y[0]);
  xor xor_6 (S[1], X[1], Y[1], C1);
  xor xor_7 (xor_7_out, X[0], Y[0]);
  and and_5 (and_5_out, Cin, P_star);
  xor xor_8 (S[0], X[0], Y[0], Cin);
  // Probe on X
  // Probe on Y
  // Probe on S
  or or_1 (Cout, and_5_out, G_star);
  // Probe on X
  // Probe on Y
  // Probe on S

  // Notes on the sheet:
  //   输入引脚区
  //   输出引脚区
  //   +
  //   =
  //   有符号加法
  //   +
  //   =
  //   无符号加法
endmodule

// 16位快速加法器
module \_16位快速加法器  (
  input  [15:0] X,
  input  [15:0] Y,
  input  Cin,
  output [15:0] S,
  output Cout,
  output G_star,
  output P_star
);

  wire C1, C2, C3, \n4位快速加法器_1_cout , \n4位快速加法器_1_g_star , \n4位快速加法器_1_p_star , \n4位快速加法器_2_g_star ,
       \n4位快速加法器_2_p_star , \n4位快速加法器_3_g_star , \n4位快速加法器_3_p_star , \n4位快速加法器_4_g_star ,
       \n4位快速加法器_4_p_star ;

  \_4位快速加法器  \u_4位快速加法器_1  (
    .X(X[15:12]), .Y(Y[15:12]), .Cin(C3), .S(S[15:12]), .Cout(\n4位快速加法器_1_cout ),
    .G_star(\n4位快速加法器_1_g_star ), .P_star(\n4位快速加法器_1_p_star ));
  \_4位快速加法器  \u_4位快速加法器_2  (
    .X(Y[11:8]), .Y(X[11:8]), .Cin(C2), .S(S[11:8]), .G_star(\n4位快速加法器_2_g_star ),
    .P_star(\n4位快速加法器_2_p_star ));  // open: Cout
  // XOR_Gate xor_1 is placed but not wired
  // Probe on X
  // Probe on Y
  // Probe on S
  \_4位快速加法器  \u_4位快速加法器_3  (
    .X(Y[7:4]), .Y(X[7:4]), .Cin(C1), .S(S[7:4]), .G_star(\n4位快速加法器_3_g_star ), .P_star(\n4位快速加法器_3_p_star ));  // open: Cout
  // Probe on X
  // Probe on Y
  // Probe on S
  CLA74182 cla74182_1 (
    .G4(\n4位快速加法器_1_g_star ), .P4(\n4位快速加法器_1_p_star ), .G3(\n4位快速加法器_2_g_star ), .P3(\n4位快速加法器_2_p_star ),
    .G2(\n4位快速加法器_3_g_star ), .P2(\n4位快速加法器_3_p_star ), .G1(\n4位快速加法器_4_g_star ), .P1(\n4位快速加法器_4_p_star ),
    .Cin(Cin), .C4(Cout), .C3(C3), .C2(C2), .C1(C1), .G_star(G_star), .P_star(P_star));
  \_4位快速加法器  \u_4位快速加法器_4  (
    .X(X[3:0]), .Y(Y[3:0]), .Cin(Cin), .S(S[3:0]), .G_star(\n4位快速加法器_4_g_star ), .P_star(\n4位快速加法器_4_p_star ));  // open: Cout

  // Other names for the same wires on the sheet: S0[3:0] = S[3:0]; S1[3:0] = S[7:4]; S2[3:0] = S[11:8];
  //   S3[3:0] = S[15:12]; X0[3:0] = X[3:0]; X1[3:0] = X[7:4]; X2[3:0] = X[11:8]; X3[3:0] = X[15:12]; Y0[3:0] = Y[3:0];
  //   Y1[3:0] = Y[7:4]; Y2[3:0] = Y[11:8]; Y3[3:0] = Y[15:12]

  // Notes on the sheet:
  //   输入引脚区
  //   输出引脚区
  //   +
  //   =
  //   有符号加法
  //   +
  //   =
  //   无符号加法
endmodule

// 32位加法器
module \_32位快速加法器  (
  input  Cin,
  input  [31:0] X,
  input  [31:0] Y,
  output Cout,
  output [31:0] S,
  output Overflow
);

  wire and_1_out, and_2_out, c1, c2, c3, \n4位快速加法器_1_g_star , \n4位快速加法器_1_p_star , \n4位快速加法器_2_cout ,
       \n4位快速加法器_3_g_star , \n4位快速加法器_3_p_star , \n4位快速加法器_4_cout , \n4位快速加法器_5_g_star , \n4位快速加法器_5_p_star ,
       \n4位快速加法器_6_cout , \n4位快速加法器_7_cout , \n4位快速加法器_7_g_star , \n4位快速加法器_7_p_star , \n4位快速加法器_8_cout ,
       \n16位快速加法器_1_cout , \n16位快速加法器_1_g_star , \n16位快速加法器_2_cout , not_1_out, not_2_out, not_3_out;
  wire [3:0] \n4位快速加法器_1_s , \n4位快速加法器_5_s ;
  wire [11:0] \n4位快速加法器_4_s , \n4位快速加法器_8_s ;

  \_4位快速加法器  \u_4位快速加法器_1  (
    .X(X[31:28]), .Y(Y[31:28]), .Cin(\n4位快速加法器_2_cout ), .S(\n4位快速加法器_1_s ), .G_star(\n4位快速加法器_1_g_star ),
    .P_star(\n4位快速加法器_1_p_star ));  // open: Cout
  // Probe on X[19:16]
  \_16位快速加法器  \u_16位快速加法器_1  (
    .X(X[31:16]), .Y(Y[31:16]), .Cin(\n16位快速加法器_2_cout ), .S(S[31:16]), .Cout(\n16位快速加法器_1_cout ),
    .G_star(\n16位快速加法器_1_g_star ));  // open: P_star
  \_4位快速加法器  \u_4位快速加法器_2  (
    .X(X[27:24]), .Y(Y[27:24]), .Cin(c3), .S(\n4位快速加法器_4_s [11:8]), .Cout(\n4位快速加法器_2_cout ));  // open: G_star, P_star
  \_16位快速加法器  \u_16位快速加法器_2  (
    .X(X[15:0]), .Y(Y[15:0]), .Cin(Cin), .S(S[15:0]), .Cout(\n16位快速加法器_2_cout ));  // open: G_star, P_star
  // Probe on X
  // Probe on Y
  // Probe on S
  \_4位快速加法器  \u_4位快速加法器_3  (
    .X(X[23:20]), .Y(Y[23:20]), .Cin(\n4位快速加法器_4_cout ), .S(\n4位快速加法器_4_s [7:4]),
    .G_star(\n4位快速加法器_3_g_star ), .P_star(\n4位快速加法器_3_p_star ));  // open: Cout
  // Probe on X
  // Probe on Y
  // Probe on S
  \_4位快速加法器  \u_4位快速加法器_4  (
    .X(X[19:16]), .Y(Y[19:16]), .Cin(c2), .S(\n4位快速加法器_4_s [3:0]), .Cout(\n4位快速加法器_4_cout ));  // open: G_star, P_star
  not not_1 (not_1_out, Y[31]);
  not not_2 (not_2_out, X[31]);
  \_4位快速加法器  \u_4位快速加法器_5  (
    .X(X[15:12]), .Y(Y[15:12]), .Cin(\n4位快速加法器_6_cout ), .S(\n4位快速加法器_5_s ), .G_star(\n4位快速加法器_5_g_star ),
    .P_star(\n4位快速加法器_5_p_star ));  // open: Cout
  or or_1 (Overflow, and_1_out, and_2_out);
  and and_1 (and_1_out, not_2_out, not_1_out, S[31]);
  and and_2 (and_2_out, X[31], Y[31], not_3_out);
  not not_3 (not_3_out, S[31]);
  \CLA74182封装2  \cla74182封装2_1  (
    .G4(\n4位快速加法器_1_g_star ), .P4(\n4位快速加法器_1_p_star ), .G3(\n4位快速加法器_3_g_star ), .P3(\n4位快速加法器_3_p_star ),
    .G2(\n4位快速加法器_5_g_star ), .P2(\n4位快速加法器_5_p_star ), .G1(\n4位快速加法器_7_g_star ), .P1(\n4位快速加法器_7_p_star ),
    .Cin(\n4位快速加法器_8_cout ), .C4(Cout), .C3(c3), .C2(c2), .C1(c1));  // open: G_star, P_star
  \_4位快速加法器  \u_4位快速加法器_6  (
    .X(X[11:8]), .Y(Y[11:8]), .Cin(c1), .S(\n4位快速加法器_8_s [11:8]), .Cout(\n4位快速加法器_6_cout ));  // open: G_star, P_star
  \_4位快速加法器  \u_4位快速加法器_7  (
    .X(X[7:4]), .Y(Y[7:4]), .Cin(\n4位快速加法器_8_cout ), .S(\n4位快速加法器_8_s [7:4]), .Cout(\n4位快速加法器_7_cout ),
    .G_star(\n4位快速加法器_7_g_star ), .P_star(\n4位快速加法器_7_p_star ));
  \_4位快速加法器  \u_4位快速加法器_8  (
    .X(X[3:0]), .Y(Y[3:0]), .Cin(Cin), .S(\n4位快速加法器_8_s [3:0]), .Cout(\n4位快速加法器_8_cout ));  // open: G_star, P_star

  // Other names for the same wires on the sheet: S0[15:0] = S[15:0]; S1[15:0] = S[31:16]; o = S[31];
  //   X0[15:0] = X[15:0]; x01[3:0] = X[3:0]; x02[3:0] = X[7:4]; x03[3:0] = X[11:8]; x04[3:0] = X[15:12];
  //   X1[15:0] = X[31:16]; x11[3:0] = X[19:16]; x12[3:0] = X[23:20]; x13[3:0] = X[27:24]; x14[3:0] = X[31:28];
  //   x1_t = X[31]; Y0[15:0] = Y[15:0]; y01[3:0] = Y[3:0]; y02[3:0] = Y[7:4]; y03[3:0] = Y[11:8]; y04[3:0] = Y[15:12];
  //   Y1[15:0] = Y[31:16]; y11[3:0] = Y[19:16]; y12[3:0] = Y[23:20]; y13[3:0] = Y[27:24]; y14[3:0] = Y[31:28];
  //   y1_t = Y[31]

  // Notes on the sheet:
  //   输入引脚区
  //   输出引脚区
  //   +
  //   =
  //   有符号加法
  //   +
  //   =
  //   无符号加法
endmodule

module \补码一位乘法器  (
  input  [7:0] X,
  input  [7:0] Y,
  input  in_3,
  output [15:0] \乘积 ,
  output [15:0] \乘积_2 
);

  wire CLK, comparator_1_eq, comparator_2_eq, comparator_3_eq, EN, EN1, INIT, Y1, Y2, Yn_1_2_q;
  wire [3:0] counter_1_q, counter_2_q, counter_3_q;
  wire [7:0] M, NUM, register_q, shift_register_1_q7, X_star, Y_2_q;

  // Probe on M
  Shift_Register shift_register_1 (
    .shift(EN), .in(M[7]), .clk(CLK), .load(1'b1), .d0(M[7]), .q0(shift_register_1_q7[7]), .d1(M[7]),
    .q1(shift_register_1_q7[6]), .d2(M[6]), .q2(shift_register_1_q7[5]), .d3(M[5]),
    .q3(shift_register_1_q7[4]), .d4(M[4]), .q4(shift_register_1_q7[3]), .d5(M[3]),
    .q5(shift_register_1_q7[2]), .d6(M[2]), .q6(shift_register_1_q7[1]), .d7(M[1]),
    .q7(shift_register_1_q7[0]));  // open: out, clr
  Counter #(.width(4), .max('hf)) counter_1 (
    .D(4'b0000), .count(INIT), .Q(counter_1_q), .clk(CLK), .clr(in_3));  // open: load, carry
  Counter #(.width(4), .max('hf)) counter_2 (
    .D(4'b0000), .count(EN), .Q(counter_2_q), .clk(CLK), .clr(in_3));  // open: load, carry
  Counter #(.width(4), .max('hf)) counter_3 (
    .D(4'b0000), .count(EN1), .Q(counter_3_q), .clk(CLK), .clr(in_3));  // open: load, carry
  // Probe on X
  // Probe on \乘积 [15:8]
  Register register (.D(\乘积 [15:8]), .en(EN), .Q(register_q), .clk(CLK), .clr(in_3));
  // Probe on Y
  \_8位串行加法器  \u_8位串行加法器_1  (.X(register_q), .Y(NUM), .Cin(1'b0), .S(M));  // open: Cout, Overflow
  Shift_Register shift_register_2 (
    .shift(EN1), .in(M[0]), .clk(CLK), .d0(1'b0), .q0(\乘积 [7]), .d1(1'b0), .q1(\乘积 [6]), .d2(1'b0),
    .q2(\乘积 [5]), .d3(1'b0), .q3(\乘积 [4]), .d4(1'b0), .q4(\乘积 [3]), .d5(1'b0), .q5(\乘积 [2]), .d6(1'b0),
    .q6(\乘积 [1]), .d7(1'b0), .q7(\乘积 [0]));  // open: out, load, clr
  Comparator #(.width(4)) comparator_1 (.a(counter_1_q), .b(4'b0001), .eq(comparator_1_eq));  // open: gt, lt
  Comparator #(.width(4)) comparator_2 (.a(counter_2_q), .b(4'b1000), .eq(comparator_2_eq));  // open: gt, lt
  not not_1 (EN1, comparator_3_eq);
  Comparator #(.width(4)) comparator_3 (.a(counter_3_q), .b(4'b1001), .eq(comparator_3_eq));  // open: gt, lt
  // Probe on \乘积 
  Shifter #(.shift("ar")) shifter_1 (.in(M), .\dist (3'b001), .out(\乘积 [15:8]));
  not not_2 (INIT, comparator_1_eq);
  not not_3 (EN, comparator_2_eq);
  // Probe on \乘积 [7:0]
  Register Y_2 (.D(\乘积 [7:0]), .Q(Y_2_q), .clk(CLK));  // open: en, clr
  Clock clock_1 (.out(CLK));
  // Probe on Yn_1_2_q
  \_8位可控加减法器  \u_8位可控加减法器_1  (.X({8{1'b0}}), .Y(X), .Cin(1'b0), .Sub(1'b1), .S(X_star));  // open: Cout, Overflow
  Shift_Register #(.length(9)) shift_register_3 (
    .shift(EN), .in(1'b0), .clk(CLK), .out(Y2), .load(INIT), .d0(Y[7]), .d1(Y[6]), .d2(Y[5]), .d3(Y[4]),
    .d4(Y[3]), .d5(Y[2]), .d6(Y[1]), .d7(Y[0]), .q7(Y1), .d8(1'b0));  // open: clr, q0, q1, q2, q3, q4, q5, q6, q8
  // Probe on X_star
  Register #(.width(1)) Yn_1_2 (.D(Y2), .en(EN), .Q(Yn_1_2_q), .clk(CLK));  // open: clr
  // Probe on NUM
  Multiplexer #(.select(2), .width(8)) multiplexer_1 (
    .in0({8{1'b0}}), .in1(X), .in2(X_star), .in3({8{1'b0}}), .out(NUM), .sel({Y1, Y2}));  // open: en

  assign \乘积_2  = \乘积 ;

  // Other names for the same wires on the sheet: RS = in_3; TEMP1[7:0] = \乘积 [7:0]; TEMP[7:0] = \乘积 [15:8]
endmodule

// 与门阵列
module \_8位乘法与门阵列  (
  input  [7:0] X,
  input  [7:0] Y,
  output [7:0] XY0,
  output [7:0] XY1,
  output [7:0] XY2,
  output [7:0] XY3,
  output [7:0] XY4,
  output [7:0] XY5,
  output [7:0] XY6,
  output [7:0] XY7
);

  and and_1 (XY0[7], X[7], Y[0]);
  and and_2 (XY1[7], X[7], Y[1]);
  and and_3 (XY2[7], X[7], Y[2]);
  and and_4 (XY3[7], X[7], Y[3]);
  and and_5 (XY4[7], X[7], Y[4]);
  and and_6 (XY5[7], X[7], Y[5]);
  and and_7 (XY6[7], X[7], Y[6]);
  and and_8 (XY7[7], X[7], Y[7]);
  and and_9 (XY0[6], X[6], Y[0]);
  and and_10 (XY1[6], X[6], Y[1]);
  and and_11 (XY2[6], X[6], Y[2]);
  and and_12 (XY3[6], X[6], Y[3]);
  and and_13 (XY4[6], X[6], Y[4]);
  and and_14 (XY5[6], X[6], Y[5]);
  and and_15 (XY6[6], X[6], Y[6]);
  and and_16 (XY7[6], X[6], Y[7]);
  and and_17 (XY0[5], X[5], Y[0]);
  and and_18 (XY1[5], X[5], Y[1]);
  and and_19 (XY2[5], X[5], Y[2]);
  and and_20 (XY3[5], X[5], Y[3]);
  and and_21 (XY4[5], X[5], Y[4]);
  and and_22 (XY5[5], X[5], Y[5]);
  and and_23 (XY6[5], X[5], Y[6]);
  and and_24 (XY7[5], X[5], Y[7]);
  and and_25 (XY0[3], X[3], Y[0]);
  and and_26 (XY0[4], X[4], Y[0]);
  and and_27 (XY1[3], X[3], Y[1]);
  and and_28 (XY1[4], X[4], Y[1]);
  and and_29 (XY2[4], X[4], Y[2]);
  and and_30 (XY2[3], X[3], Y[2]);
  and and_31 (XY3[4], X[4], Y[3]);
  and and_32 (XY3[3], X[3], Y[3]);
  and and_33 (XY4[3], X[3], Y[4]);
  and and_34 (XY4[4], X[4], Y[4]);
  and and_35 (XY5[3], X[3], Y[5]);
  and and_36 (XY5[4], X[4], Y[5]);
  and and_37 (XY6[4], X[4], Y[6]);
  and and_38 (XY6[3], X[3], Y[6]);
  and and_39 (XY7[4], X[4], Y[7]);
  and and_40 (XY7[3], X[3], Y[7]);
  and and_41 (XY0[2], X[2], Y[0]);
  and and_42 (XY1[2], X[2], Y[1]);
  and and_43 (XY2[2], X[2], Y[2]);
  and and_44 (XY3[2], X[2], Y[3]);
  and and_45 (XY4[2], X[2], Y[4]);
  and and_46 (XY5[2], X[2], Y[5]);
  and and_47 (XY6[2], X[2], Y[6]);
  and and_48 (XY7[2], X[2], Y[7]);
  and and_49 (XY0[1], X[1], Y[0]);
  and and_50 (XY1[1], X[1], Y[1]);
  and and_51 (XY2[1], X[1], Y[2]);
  and and_52 (XY3[1], X[1], Y[3]);
  and and_53 (XY4[1], X[1], Y[4]);
  and and_54 (XY5[1], X[1], Y[5]);
  and and_55 (XY6[1], X[1], Y[6]);
  and and_56 (XY7[1], X[1], Y[7]);
  and and_57 (XY0[0], X[0], Y[0]);
  and and_58 (XY1[0], X[0], Y[1]);
  and and_59 (XY2[0], X[0], Y[2]);
  and and_60 (XY3[0], X[0], Y[3]);
  and and_61 (XY4[0], X[0], Y[4]);
  and and_62 (XY5[0], X[0], Y[5]);
  and and_63 (XY6[0], X[0], Y[6]);
  and and_64 (XY7[0], X[0], Y[7]);

  // Other names for the same wires on the sheet: A1[7:0] = XY0; X0Y0 = XY0[0]; X1Y0 = XY0[1]; X2Y0 = XY0[2];
  //   X3Y0 = XY0[3]; X4Y0 = XY0[4]; X5Y0 = XY0[5]; X6Y0 = XY0[6]; X7Y0 = XY0[7]; X0Y1 = XY1[0]; X1Y1 = XY1[1];
  //   X2Y1 = XY1[2]; X3Y1 = XY1[3]; X4Y1 = XY1[4]; X5Y1 = XY1[5]; X6Y1 = XY1[6]; X7Y1 = XY1[7]; X0Y2 = XY2[0];
  //   X1Y2 = XY2[1]; X2Y2 = XY2[2]; X3Y2 = XY2[3]; X4Y2 = XY2[4]; X5Y2 = XY2[5]; X6Y2 = XY2[6]; X7Y2 = XY2[7];
  //   X0Y3 = XY3[0]; X1Y3 = XY3[1]; X2Y3 = XY3[2]; X3Y3 = XY3[3]; X4Y3 = XY3[4]; X5Y3 = XY3[5]; X6Y3 = XY3[6];
  //   X7Y3 = XY3[7]; X0Y4 = XY4[0]; X1Y4 = XY4[1]; X2Y4 = XY4[2]; X3Y4 = XY4[3]; X4Y4 = XY4[4]; X5Y4 = XY4[5];
  //   X6Y4 = XY4[6]; X7Y4 = XY4[7]; X0Y5 = XY5[0]; X1Y5 = XY5[1]; X2Y5 = XY5[2]; X3Y5 = XY5[3]; X4Y5 = XY5[4];
  //   X5Y5 = XY5[5]; X6Y5 = XY5[6]; X7Y5 = XY5[7]; X0Y6 = XY6[0]; X1Y6 = XY6[1]; X2Y6 = XY6[2]; X3Y6 = XY6[3];
  //   X4Y6 = XY6[4]; X5Y6 = XY6[5]; X6Y6 = XY6[6]; X7Y6 = XY6[7]; X0Y7 = XY7[0]; X1Y7 = XY7[1]; X2Y7 = XY7[2];
  //   X3Y7 = XY7[3]; X4Y7 = XY7[4]; X5Y7 = XY7[5]; X6Y7 = XY7[6]; X7Y7 = XY7[7]
endmodule

module \_8位斜向进位阵列乘法器  (
  input  [7:0] X,
  input  [7:0] Y,
  output [15:0] \乘积 
);

  wire X0Y1, X0Y2, X0Y3, X0Y4, X0Y5, X0Y6, X0Y7, X1Y0, X1Y1, X1Y2, X1Y3, X1Y4, X1Y5, X1Y6, X1Y7, X2Y0, X2Y1,
       X2Y2, X2Y3, X2Y4, X2Y5, X2Y6, X2Y7, X3Y0, X3Y1, X3Y2, X3Y3, X3Y4, X3Y5, X3Y6, X3Y7, X4Y0, X4Y1, X4Y2,
       X4Y3, X4Y4, X4Y5, X4Y6, X4Y7, X5Y0, X5Y1, X5Y2, X5Y3, X5Y4, X5Y5, X5Y6, X5Y7, X6Y0, X6Y1, X6Y2, X6Y3,
       X6Y4, X6Y5, X6Y6, X6Y7, X7Y0, X7Y1, X7Y2, X7Y3, X7Y4, X7Y5, X7Y6, X7Y7, \一位全加器fa封装3_1_p2 ,
       \一位全加器fa封装3_22_cout , \一位全加器fa封装3_22_si , \一位全加器fa封装3_23_si , \一位全加器fa封装3_24_p2 ,
       \一位全加器fa封装3_29_cout , \一位全加器fa封装3_29_si , \一位全加器fa封装3_35_cout , \一位全加器fa封装3_36_p1 ,
       \一位全加器fa封装3_41_p1 , \一位全加器fa封装3_45_p1 , \一位全加器fa封装3_47_si , \一位全加器fa封装3_48_p2 ;

  // Probe on X
  // Probe on \乘积 
  // 一位全加器FA封装3 一位全加器fa封装3_1: pin names not known; wires that end beside it: X7Y6, \一位全加器fa封装3_1_p2 , X6Y7
  // 一位全加器FA封装3 一位全加器fa封装3_2: pin names not known; wires that end beside it: \一位全加器fa封装3_1_p2 , X7Y5, X6Y6
  // 一位全加器FA封装3 一位全加器fa封装3_3: pin names not known; wires that end beside it: X5Y7
  // Probe on Y
  // 一位全加器FA封装3 一位全加器fa封装3_4: pin names not known; wires that end beside it: X7Y4, X6Y5
  // 一位全加器FA封装3 一位全加器fa封装3_5: pin names not known; wires that end beside it: X5Y6
  // 一位全加器FA封装3 一位全加器fa封装3_6: pin names not known; wires that end beside it: X4Y7
  // 一位全加器FA封装3 一位全加器fa封装3_7: pin names not known; wires that end beside it: X7Y3, X6Y4
  // 一位全加器FA封装3 一位全加器fa封装3_8: pin names not known; wires that end beside it: X5Y5
  // 一位全加器FA封装3 一位全加器fa封装3_9: pin names not known; wires that end beside it: X4Y6
  // 一位全加器FA封装3 一位全加器fa封装3_10: pin names not known; wires that end beside it: X3Y7
  // 一位全加器FA封装3 一位全加器fa封装3_11: pin names not known; wires that end beside it: X7Y2, X6Y3
  // 一位全加器FA封装3 一位全加器fa封装3_12: pin names not known; wires that end beside it: X5Y4
  // 一位全加器FA封装3 一位全加器fa封装3_13: pin names not known; wires that end beside it: X4Y5
  // 一位全加器FA封装3 一位全加器fa封装3_14: pin names not known; wires that end beside it: X3Y6
  // 一位全加器FA封装3 一位全加器fa封装3_15: pin names not known; wires that end beside it: X2Y7
  \一位全加器FA封装3  \u_一位全加器fa封装3_16  (.Xi(X6Y2), .Yi(\一位全加器fa封装3_22_cout ));  // open: Cout, Si, Cin
  // 一位全加器FA封装3 一位全加器fa封装3_17: pin names not known; wires that end beside it: X5Y3
  // 一位全加器FA封装3 一位全加器fa封装3_18: pin names not known; wires that end beside it: X4Y4
  // 一位全加器FA封装3 一位全加器fa封装3_19: pin names not known; wires that end beside it: X3Y5
  // 一位全加器FA封装3 一位全加器fa封装3_20: pin names not known; wires that end beside it: X2Y6
  // 一位全加器FA封装3 一位全加器fa封装3_21: pin names not known; wires that end beside it: X1Y7
  \一位全加器FA封装3  \u_一位全加器fa封装3_22  (
    .Cout(\一位全加器fa封装3_22_cout ), .Si(\一位全加器fa封装3_22_si ), .Cin(1'b0), .Xi(X6Y1), .Yi(X7Y0));
  \一位全加器FA封装3  \u_一位全加器fa封装3_23  (
    .Si(\一位全加器fa封装3_23_si ), .Cin(\一位全加器fa封装3_29_cout ), .Xi(X5Y2), .Yi(\一位全加器fa封装3_22_si ));  // open: Cout
  // 一位全加器FA封装3 一位全加器fa封装3_24: pin names not known; wires that end beside it: \一位全加器fa封装3_23_si , \一位全加器fa封装3_24_p2 , X4Y3
  // 一位全加器FA封装3 一位全加器fa封装3_25: pin names not known; wires that end beside it: X3Y4
  // 一位全加器FA封装3 一位全加器fa封装3_26: pin names not known; wires that end beside it: X2Y5
  // 一位全加器FA封装3 一位全加器fa封装3_27: pin names not known; wires that end beside it: X1Y6
  // 一位全加器FA封装3 一位全加器fa封装3_28: pin names not known; wires that end beside it: X0Y7
  \一位全加器FA封装3  \u_一位全加器fa封装3_29  (
    .Cout(\一位全加器fa封装3_29_cout ), .Si(\一位全加器fa封装3_29_si ), .Cin(1'b0), .Xi(X5Y1), .Yi(X6Y0));
  \一位全加器FA封装3  \u_一位全加器fa封装3_30  (
    .Cout(\一位全加器fa封装3_24_p2 ), .Cin(\一位全加器fa封装3_35_cout ), .Xi(X4Y2), .Yi(\一位全加器fa封装3_29_si ));  // open: Si
  // 一位全加器FA封装3 一位全加器fa封装3_31: pin names not known; wires that end beside it: X3Y3
  // 一位全加器FA封装3 一位全加器fa封装3_32: pin names not known; wires that end beside it: X2Y4
  // 一位全加器FA封装3 一位全加器fa封装3_33: pin names not known; wires that end beside it: X1Y5
  // 一位全加器FA封装3 一位全加器fa封装3_34: pin names not known; wires that end beside it: X0Y6
  \一位全加器FA封装3  \u_一位全加器fa封装3_35  (.Cout(\一位全加器fa封装3_35_cout ), .Cin(1'b0), .Xi(X4Y1), .Yi(X5Y0));  // open: Si
  // 一位全加器FA封装3 一位全加器fa封装3_36: pin names not known; wires that end beside it: \一位全加器fa封装3_36_p1 , X3Y2
  // 一位全加器FA封装3 一位全加器fa封装3_37: pin names not known; wires that end beside it: X2Y3
  // 一位全加器FA封装3 一位全加器fa封装3_38: pin names not known; wires that end beside it: X1Y4
  // 一位全加器FA封装3 一位全加器fa封装3_39: pin names not known; wires that end beside it: X0Y5
  \一位全加器FA封装3  \u_一位全加器fa封装3_40  (.Cout(\一位全加器fa封装3_36_p1 ), .Cin(1'b0), .Xi(X3Y1), .Yi(X4Y0));  // open: Si
  // 一位全加器FA封装3 一位全加器fa封装3_41: pin names not known; wires that end beside it: \一位全加器fa封装3_41_p1 , X2Y2
  // 一位全加器FA封装3 一位全加器fa封装3_42: pin names not known; wires that end beside it: X1Y3
  // 一位全加器FA封装3 一位全加器fa封装3_43: pin names not known; wires that end beside it: X0Y4
  \一位全加器FA封装3  \u_一位全加器fa封装3_44  (.Cout(\一位全加器fa封装3_41_p1 ), .Cin(1'b0), .Xi(X2Y1), .Yi(X3Y0));  // open: Si
  // 一位全加器FA封装3 一位全加器fa封装3_45: pin names not known; wires that end beside it: \一位全加器fa封装3_45_p1 , X1Y2
  // 一位全加器FA封装3 一位全加器fa封装3_46: pin names not known; wires that end beside it: X0Y3
  \一位全加器FA封装3  \u_一位全加器fa封装3_47  (.Cout(\一位全加器fa封装3_45_p1 ), .Si(\一位全加器fa封装3_47_si ), .Cin(1'b0), .Xi(X1Y1), .Yi(X2Y0));
  // 一位全加器FA封装3 一位全加器fa封装3_48: pin names not known; wires that end beside it: \一位全加器fa封装3_47_si , \一位全加器fa封装3_48_p2 , X0Y2
  \一位全加器FA封装3  \u_一位全加器fa封装3_49  (.Cout(\一位全加器fa封装3_48_p2 ), .Si(\乘积 [1]), .Cin(1'b0), .Xi(X0Y1), .Yi(X1Y0));
  \_8位乘法与门阵列  \u_8位乘法与门阵列_1  (
    .X(X), .Y(Y), .XY7({X7Y7, X6Y7, X5Y7, X4Y7, X3Y7, X2Y7, X1Y7, X0Y7}),
    .XY6({X7Y6, X6Y6, X5Y6, X4Y6, X3Y6, X2Y6, X1Y6, X0Y6}),
    .XY5({X7Y5, X6Y5, X5Y5, X4Y5, X3Y5, X2Y5, X1Y5, X0Y5}),
    .XY4({X7Y4, X6Y4, X5Y4, X4Y4, X3Y4, X2Y4, X1Y4, X0Y4}),
    .XY3({X7Y3, X6Y3, X5Y3, X4Y3, X3Y3, X2Y3, X1Y3, X0Y3}),
    .XY2({X7Y2, X6Y2, X5Y2, X4Y2, X3Y2, X2Y2, X1Y2, X0Y2}),
    .XY1({X7Y1, X6Y1, X5Y1, X4Y1, X3Y1, X2Y1, X1Y1, X0Y1}),
    .XY0({X7Y0, X6Y0, X5Y0, X4Y0, X3Y0, X2Y0, X1Y0, \乘积 [0]}));

  // Other names for the same wires on the sheet: P[15:0] = \乘积 ; P1 = \乘积 [1]; P2 = \乘积 [2]; P3 = \乘积 [3];
  //   P4 = \乘积 [4]; P5 = \乘积 [5]; P6 = \乘积 [6]; P7 = \乘积 [7]; P8 = \乘积 [8]; P9 = \乘积 [9]; P10 = \乘积 [10];
  //   P11 = \乘积 [11]; P12 = \乘积 [12]; P13 = \乘积 [13]; P14 = \乘积 [14]; P15 = \乘积 [15]; P0 = \乘积 [0]; X0Y0 = \乘积 [0];
  //   XY0[7:0] = {X7Y0, X6Y0, X5Y0, X4Y0, X3Y0, X2Y0, X1Y0, \乘积 [0]};
  //   XY1[7:0] = {X7Y1, X6Y1, X5Y1, X4Y1, X3Y1, X2Y1, X1Y1, X0Y1};
  //   XY2[7:0] = {X7Y2, X6Y2, X5Y2, X4Y2, X3Y2, X2Y2, X1Y2, X0Y2};
  //   XY3[7:0] = {X7Y3, X6Y3, X5Y3, X4Y3, X3Y3, X2Y3, X1Y3, X0Y3};
  //   XY4[7:0] = {X7Y4, X6Y4, X5Y4, X4Y4, X3Y4, X2Y4, X1Y4, X0Y4};
  //   XY5[7:0] = {X7Y5, X6Y5, X5Y5, X4Y5, X3Y5, X2Y5, X1Y5, X0Y5};
  //   XY6[7:0] = {X7Y6, X6Y6, X5Y6, X4Y6, X3Y6, X2Y6, X1Y6, X0Y6};
  //   XY7[7:0] = {X7Y7, X6Y7, X5Y7, X4Y7, X3Y7, X2Y7, X1Y7, X0Y7}
endmodule

// ALU
module ALU (
  input  [31:0] X,
  input  [31:0] Y,
  input  [3:0] AluOP,
  output Signed_Overflow,
  output UnSigned_Overflow,
  output Equal,
  output [31:0] Result,
  output [31:0] Result_2
);

  wire undriven, YD;
  wire [0:0] comparator_2_eq;
  wire [31:0] adder_1_out, adder_2_out, and_1_out, divider_1_out, high, multiplier_1_out, not_1_out,
       not_2_out, or_1_out, shifter_1_out, shifter_2_out, shifter_3_out, temp, xor_1_out;

  // Probe on X
  // Probe on X
  assign not_1_out = ~Y;  // NOT_Gate not_1, 32 bits wide
  // Probe on Y
  // Probe on Y
  Adder #(.width(32)) adder_1 (.a(X), .b(Y), .out(adder_1_out), .cin(1'b0));  // open: cout
  Adder #(.width(32)) adder_2 (.a(X), .b(not_1_out), .out(adder_2_out), .cin(1'b1));  // open: cout
  assign and_1_out = X & Y;  // AND_Gate and_1, 32 bits wide
  assign or_1_out = X | Y;  // OR_Gate or_1, 32 bits wide
  assign xor_1_out = X ^ Y;  // XOR_Gate xor_1, 32 bits wide
  Comparator #(.width(32)) comparator_1 (.a(X), .b(Y), .lt(YD));  // open: gt, eq
  Comparator #(.width(32), .mode("unsigned")) comparator_2 (.a(X), .b(Y), .eq(comparator_2_eq[0]));  // open: gt, lt
  Shifter #(.width(32)) shifter_1 (.in(X), .\dist (Y[4:0]), .out(shifter_1_out));
  Shifter #(.width(32), .shift("ar")) shifter_2 (.in(X), .\dist (Y[4:0]), .out(shifter_2_out));
  Shifter #(.width(32), .shift("lr")) shifter_3 (.in(X), .\dist (Y[4:0]), .out(shifter_3_out));
  Multiplier #(.width(32)) multiplier_1 (.a(X), .b(Y), .out(multiplier_1_out), .cout(high));  // open: cin
  Divider #(.width(32)) divider_1 (.a(X), .b(Y), .out(divider_1_out), .rem(temp));  // open: upper
  // Probe on AluOP
  // Probe on Result
  // Probe on Result
  assign not_2_out = ~or_1_out;  // NOT_Gate not_2, 32 bits wide
  // Probe on {32{1'b0}}
  Multiplexer #(.select(4), .width(32)) multiplexer_1 (
    .in0(shifter_1_out), .in1(shifter_2_out), .in2(shifter_3_out), .in3(multiplier_1_out),
    .in4(divider_1_out), .in5(adder_1_out), .in6(adder_2_out), .in7(and_1_out), .in8(or_1_out),
    .in9(xor_1_out), .in10(not_2_out), .in11({{31{1'b0}}, YD}), .in12({{31{1'b0}}, comparator_2_eq[0]}),
    .in13({32{1'b0}}), .in14({32{1'b0}}), .in15({32{1'b0}}), .out(Result), .sel(AluOP), .en(undriven));
  Comparator #(.width(32)) comparator_3 (.a(X), .b(Y), .eq(Equal));  // open: gt, lt

  assign Result_2 = {32{1'b0}};
  assign Signed_Overflow = 1'b0;
  assign UnSigned_Overflow = 1'b0;

  // Other names for the same wires on the sheet: S[3:0] = AluOP

  // Notes on the sheet:
  //   不要改变此引脚区域内容，也不要改变ALU封装形式
  //   输入引脚
  //   请在下方利用上方输入输出引脚的隧道信号构建ALU电路，ctrl+d复制选择部件
  //   华中科技大学计算机学院 计算机组成原理，鸣谢加州大学伯克利CS61C课程
  //   无符号比较小于输出1
  //   输出引脚
  //   探测区域
endmodule

module \运算器测试电路  (
  input  [31:0] X,
  input  [31:0] Y,
  input  [3:0] ALUOP,
  output Signed_Overflow,
  output Unsigned_overflow,
  output [31:0] Result,
  output [31:0] Result_2,
  output Equal
);

  // Probe on X
  // Probe on X
  ALU alu_1 (
    .AluOP(ALUOP), .X(X), .Equal(Equal), .Result(Result), .Signed_Overflow(Signed_Overflow), .Y(Y),
    .Result_2(Result_2), .UnSigned_Overflow(Unsigned_overflow));
  // Probe on ALUOP
  // Probe on Y
  // Probe on Y
  // Probe on Result
  // Probe on Result
  // Probe on Result_2

  // Notes on the sheet:
  //   ALu电路无需调整位置即可连接在该电路中，并且不能出现蓝色线缆和三态输出
endmodule

module \华莱士树  (
);

  wire undriven, undriven_2, undriven_3, undriven_4, undriven_5, undriven_6, undriven_7, undriven_8,
       undriven_9, undriven_10, undriven_11, undriven_12, undriven_13, undriven_14, undriven_15, undriven_16,
       undriven_17, undriven_18, undriven_19, undriven_20, undriven_21, undriven_22, undriven_23,
       undriven_24, undriven_25, undriven_26, undriven_27, undriven_28, undriven_29, undriven_30,
       undriven_31, undriven_32, undriven_33, undriven_34, undriven_35, undriven_36, undriven_37,
       undriven_38, undriven_39, undriven_40, undriven_41, undriven_42, undriven_43, undriven_44,
       undriven_45, undriven_46, undriven_47, undriven_48, undriven_49, undriven_50, undriven_51,
       undriven_52, undriven_53, undriven_54, undriven_55, undriven_56, undriven_57, undriven_58,
       undriven_59, undriven_60, undriven_61, undriven_62, undriven_63, undriven_64, undriven_65,
       undriven_66, undriven_67, undriven_68, undriven_69, undriven_70, undriven_71, undriven_72,
       undriven_73, undriven_74, undriven_75, undriven_76, undriven_77, undriven_78, undriven_79,
       undriven_80, undriven_81, undriven_82, undriven_83, undriven_84, undriven_85, undriven_86,
       undriven_87, undriven_88, undriven_89, undriven_90, undriven_91, undriven_92, undriven_93,
       undriven_94, undriven_95, undriven_96, undriven_97, undriven_98, undriven_99, undriven_100,
       undriven_101, undriven_102, undriven_103, undriven_104, undriven_105, undriven_106, undriven_107,
       undriven_108, undriven_109, undriven_110, undriven_111, undriven_112, undriven_113, undriven_114,
       undriven_115, undriven_116, undriven_117, undriven_118, undriven_119, undriven_120, undriven_121,
       undriven_122, undriven_123, undriven_124, undriven_125, undriven_127, \一位全加器fa封装2_1_cout ,
       \一位全加器fa封装2_1_si , \一位全加器fa封装2_2_si , \一位全加器fa封装2_3_cout , \一位全加器fa封装2_3_si , \一位全加器fa封装2_4_si ,
       \一位全加器fa封装2_5_si , \一位全加器fa封装2_6_si , \一位全加器fa封装2_7_p2 , \一位全加器fa封装2_7_p3 , \一位全加器fa封装2_7_p4 ,
       \一位全加器fa封装2_7_p5 , \一位全加器fa封装2_8_si , \一位全加器fa封装2_9_cout , \一位全加器fa封装2_9_si , \一位全加器fa封装2_10_si ,
       \一位全加器fa封装2_11_cout , \一位全加器fa封装2_11_si , \一位全加器fa封装2_12_si , \一位全加器fa封装2_13_si , \一位全加器fa封装2_14_si ,
       \一位全加器fa封装2_15_cout , \一位全加器fa封装2_15_si , \一位全加器fa封装2_16_si , \一位全加器fa封装2_17_cout ,
       \一位全加器fa封装2_17_si , \一位全加器fa封装2_18_si , \一位全加器fa封装2_19_si , \一位全加器fa封装2_20_si , \一位全加器fa封装2_21_si ,
       \一位全加器fa封装2_22_si , \一位全加器fa封装2_23_cout , \一位全加器fa封装2_23_si , \一位全加器fa封装2_24_si ,
       \一位全加器fa封装2_25_cout , \一位全加器fa封装2_25_si , \一位全加器fa封装2_26_si , \一位全加器fa封装2_27_si , \一位全加器fa封装2_28_si ,
       \一位全加器fa封装2_29_cout , \一位全加器fa封装2_29_si , \一位全加器fa封装2_30_si , \一位全加器fa封装2_31_cout ,
       \一位全加器fa封装2_31_si , \一位全加器fa封装2_32_si , \一位全加器fa封装2_33_si , \一位全加器fa封装2_34_si , \一位全加器fa封装2_35_si ,
       \一位全加器fa封装2_36_si , \一位全加器fa封装2_37_cout , \一位全加器fa封装2_37_si , \一位全加器fa封装2_38_si ,
       \一位全加器fa封装2_39_cout , \一位全加器fa封装2_39_si , \一位全加器fa封装2_40_si , \一位全加器fa封装2_41_si , \一位全加器fa封装2_42_si ,
       \一位全加器fa封装2_43_cout , \一位全加器fa封装2_43_si , \一位全加器fa封装2_44_si , \一位全加器fa封装2_45_cout ,
       \一位全加器fa封装2_45_si , \一位全加器fa封装2_46_si , \一位全加器fa封装2_47_si , \一位全加器fa封装2_48_si , \一位全加器fa封装2_49_si ,
       \一位全加器fa封装2_50_si , \一位全加器fa封装2_51_cout , \一位全加器fa封装2_51_si , \一位全加器fa封装2_52_si ,
       \一位全加器fa封装2_53_cout , \一位全加器fa封装2_53_si , \一位全加器fa封装2_54_si , \一位全加器fa封装2_55_si , \一位全加器fa封装2_56_si ,
       \一位全加器fa封装2_57_cout , \一位全加器fa封装2_57_si , \一位全加器fa封装2_58_si , \一位全加器fa封装2_59_cout ,
       \一位全加器fa封装2_59_si , \一位全加器fa封装2_60_si , \一位全加器fa封装2_61_si , \一位全加器fa封装2_62_si , \一位全加器fa封装2_63_si ,
       \一位全加器fa封装2_64_si , \一位全加器fa封装2_65_cout , \一位全加器fa封装2_65_si , \一位全加器fa封装2_66_si , \一位全加器fa封装2_67_si ,
       \一位全加器fa封装2_68_cout , \一位全加器fa封装2_68_si , \一位全加器fa封装2_69_si , \一位全加器fa封装2_70_si ,
       \一位全加器fa封装2_71_cout , \一位全加器fa封装2_71_si , \一位全加器fa封装2_72_si , \一位全加器fa封装2_73_cout ,
       \一位全加器fa封装2_73_si , \一位全加器fa封装2_74_si , \一位全加器fa封装2_75_si , \一位全加器fa封装2_76_si , \一位全加器fa封装2_77_si ,
       \一位全加器fa封装2_78_si , \一位全加器fa封装2_79_cout , \一位全加器fa封装2_79_si , \一位全加器fa封装2_80_si ,
       \一位全加器fa封装2_81_cout , \一位全加器fa封装2_81_si , \一位全加器fa封装2_82_si , \一位全加器fa封装2_83_si , \一位全加器fa封装2_84_si ,
       \一位全加器fa封装2_85_cout , \一位全加器fa封装2_85_si , \一位全加器fa封装2_86_si , \一位全加器fa封装2_87_cout ,
       \一位全加器fa封装2_87_si , \一位全加器fa封装2_88_si , \一位全加器fa封装2_89_si , \一位全加器fa封装2_90_si , \一位全加器fa封装2_91_si ,
       \一位全加器fa封装2_92_si , \一位全加器fa封装2_93_cout , \一位全加器fa封装2_93_si , \一位全加器fa封装2_94_si ,
       \一位全加器fa封装2_95_cout , \一位全加器fa封装2_95_si , \一位全加器fa封装2_96_si , \一位全加器fa封装2_97_si , \一位全加器fa封装2_98_si ,
       \一位全加器fa封装2_99_cout , \一位全加器fa封装2_99_si , \一位全加器fa封装2_100_si , \一位全加器fa封装2_101_cout ,
       \一位全加器fa封装2_101_si , \一位全加器fa封装2_102_si , \一位全加器fa封装2_103_si , \一位全加器fa封装2_104_si ,
       \一位全加器fa封装2_105_si , \一位全加器fa封装2_106_si , \一位全加器fa封装2_107_cout , \一位全加器fa封装2_107_si ,
       \一位全加器fa封装2_108_si , \一位全加器fa封装2_109_cout , \一位全加器fa封装2_109_si , \一位全加器fa封装2_110_si ,
       \一位全加器fa封装2_111_si , \一位全加器fa封装2_112_si ;
  wire [1:0] undriven_128, \一位全加器fa封装2_4_cout , \一位全加器fa封装2_10_cout , \一位全加器fa封装2_16_cout ,
       \一位全加器fa封装2_22_cout , \一位全加器fa封装2_32_cout , \一位全加器fa封装2_38_cout , \一位全加器fa封装2_44_cout ,
       \一位全加器fa封装2_50_cout , \一位全加器fa封装2_60_cout , \一位全加器fa封装2_66_cout , \一位全加器fa封装2_72_cout ,
       \一位全加器fa封装2_78_cout , \一位全加器fa封装2_88_cout , \一位全加器fa封装2_94_cout , \一位全加器fa封装2_100_cout ,
       \一位全加器fa封装2_106_cout ;
  wire [2:0] undriven_126, \一位全加器fa封装2_6_cout , \一位全加器fa封装2_14_cout , \一位全加器fa封装2_21_cout ,
       \一位全加器fa封装2_28_cout , \一位全加器fa封装2_34_cout , \一位全加器fa封装2_42_cout , \一位全加器fa封装2_49_cout ,
       \一位全加器fa封装2_56_cout , \一位全加器fa封装2_63_cout , \一位全加器fa封装2_70_cout , \一位全加器fa封装2_77_cout ,
       \一位全加器fa封装2_83_cout , \一位全加器fa封装2_90_cout , \一位全加器fa封装2_98_cout , \一位全加器fa封装2_105_cout ,
       \一位全加器fa封装2_111_cout ;

  shape shape_1 ();
  \一位全加器FA封装2  \u_一位全加器fa封装2_1  (
    .Cout(\一位全加器fa封装2_1_cout ), .Si(\一位全加器fa封装2_1_si ), .Cin(\一位全加器fa封装2_6_si ), .Xi(\一位全加器fa封装2_2_si ),
    .Yi(\一位全加器fa封装2_7_p4 ));
  \一位全加器FA封装2  \u_一位全加器fa封装2_2  (
    .Cout(\一位全加器fa封装2_6_cout [2]), .Si(\一位全加器fa封装2_2_si ), .Cin(undriven_3), .Xi(undriven), .Yi(undriven_2));
  \一位全加器FA封装2  \u_一位全加器fa封装2_3  (
    .Cout(\一位全加器fa封装2_3_cout ), .Si(\一位全加器fa封装2_3_si ), .Cin(\一位全加器fa封装2_10_cout [0]),
    .Xi(\一位全加器fa封装2_4_si ), .Yi(\一位全加器fa封装2_10_cout [1]));
  \一位全加器FA封装2  \u_一位全加器fa封装2_4  (
    .Cout(\一位全加器fa封装2_4_cout [0]), .Si(\一位全加器fa封装2_4_si ), .Cin(\一位全加器fa封装2_11_cout ),
    .Xi(\一位全加器fa封装2_1_si ), .Yi(\一位全加器fa封装2_5_si ));
  \一位全加器FA封装2  \u_一位全加器fa封装2_5  (
    .Cout(\一位全加器fa封装2_4_cout [1]), .Si(\一位全加器fa封装2_5_si ), .Cin(\一位全加器fa封装2_14_cout [0]),
    .Xi(\一位全加器fa封装2_14_cout [2]), .Yi(\一位全加器fa封装2_14_cout [1]));
  \一位全加器FA封装2  \u_一位全加器fa封装2_6  (
    .Cout(\一位全加器fa封装2_6_cout [0]), .Si(\一位全加器fa封装2_6_si ), .Cin(1'b0), .Xi(undriven_4), .Yi(undriven_5));
  // 一位全加器FA封装2 一位全加器fa封装2_7: pin names not known; wires that end beside it: \一位全加器fa封装2_6_cout [1], \一位全加器fa封装2_7_p2 , \一位全加器fa封装2_7_p3 , \一位全加器fa封装2_7_p4 , \一位全加器fa封装2_7_p5 
  \一位全加器FA封装2  \u_一位全加器fa封装2_8  (
    .Cout(\一位全加器fa封装2_14_cout [2]), .Si(\一位全加器fa封装2_8_si ), .Cin(undriven_8), .Xi(undriven_6), .Yi(undriven_7));
  \一位全加器FA封装2  \u_一位全加器fa封装2_9  (
    .Cout(\一位全加器fa封装2_9_cout ), .Si(\一位全加器fa封装2_9_si ), .Cin(\一位全加器fa封装2_16_cout [0]),
    .Xi(\一位全加器fa封装2_10_si ), .Yi(\一位全加器fa封装2_16_cout [1]));
  \一位全加器FA封装2  \u_一位全加器fa封装2_10  (
    .Cout(\一位全加器fa封装2_10_cout [0]), .Si(\一位全加器fa封装2_10_si ), .Cin(\一位全加器fa封装2_17_cout ),
    .Xi(\一位全加器fa封装2_11_si ), .Yi(\一位全加器fa封装2_12_si ));
  \一位全加器FA封装2  \u_一位全加器fa封装2_11  (
    .Cout(\一位全加器fa封装2_11_cout ), .Si(\一位全加器fa封装2_11_si ), .Cin(\一位全加器fa封装2_14_si ), .Xi(\一位全加器fa封装2_8_si ),
    .Yi(\一位全加器fa封装2_13_si ));
  \一位全加器FA封装2  \u_一位全加器fa封装2_12  (
    .Cout(\一位全加器fa封装2_10_cout [1]), .Si(\一位全加器fa封装2_12_si ), .Cin(\一位全加器fa封装2_21_cout [0]),
    .Xi(\一位全加器fa封装2_21_cout [2]), .Yi(\一位全加器fa封装2_21_cout [1]));
  \一位全加器FA封装2  \u_一位全加器fa封装2_13  (
    .Cout(\一位全加器fa封装2_14_cout [1]), .Si(\一位全加器fa封装2_13_si ), .Cin(undriven_11), .Xi(undriven_9),
    .Yi(undriven_10));
  shape shape_2 ();
  \一位全加器FA封装2  \u_一位全加器fa封装2_14  (
    .Cout(\一位全加器fa封装2_14_cout [0]), .Si(\一位全加器fa封装2_14_si ), .Cin(1'b0), .Xi(undriven_12), .Yi(undriven_13));
  \一位全加器FA封装2  \u_一位全加器fa封装2_15  (
    .Cout(\一位全加器fa封装2_15_cout ), .Si(\一位全加器fa封装2_15_si ), .Cin(\一位全加器fa封装2_22_cout [0]),
    .Xi(\一位全加器fa封装2_16_si ), .Yi(\一位全加器fa封装2_22_cout [1]));
  \一位全加器FA封装2  \u_一位全加器fa封装2_16  (
    .Cout(\一位全加器fa封装2_16_cout [0]), .Si(\一位全加器fa封装2_16_si ), .Cin(\一位全加器fa封装2_23_cout ),
    .Xi(\一位全加器fa封装2_17_si ), .Yi(\一位全加器fa封装2_20_si ));
  \一位全加器FA封装2  \u_一位全加器fa封装2_17  (
    .Cout(\一位全加器fa封装2_17_cout ), .Si(\一位全加器fa封装2_17_si ), .Cin(\一位全加器fa封装2_21_si ), .Xi(\一位全加器fa封装2_18_si ),
    .Yi(\一位全加器fa封装2_19_si ));
  \一位全加器FA封装2  \u_一位全加器fa封装2_18  (
    .Cout(\一位全加器fa封装2_21_cout [2]), .Si(\一位全加器fa封装2_18_si ), .Cin(undriven_16), .Xi(undriven_14),
    .Yi(undriven_15));
  \一位全加器FA封装2  \u_一位全加器fa封装2_19  (
    .Cout(\一位全加器fa封装2_21_cout [1]), .Si(\一位全加器fa封装2_19_si ), .Cin(undriven_19), .Xi(undriven_17),
    .Yi(undriven_18));
  \一位全加器FA封装2  \u_一位全加器fa封装2_20  (
    .Cout(\一位全加器fa封装2_16_cout [1]), .Si(\一位全加器fa封装2_20_si ), .Cin(\一位全加器fa封装2_28_cout [0]),
    .Xi(\一位全加器fa封装2_28_cout [2]), .Yi(\一位全加器fa封装2_28_cout [1]));
  \一位全加器FA封装2  \u_一位全加器fa封装2_21  (
    .Cout(\一位全加器fa封装2_21_cout [0]), .Si(\一位全加器fa封装2_21_si ), .Cin(1'b0), .Xi(undriven_20), .Yi(undriven_21));
  \一位全加器FA封装2  \u_一位全加器fa封装2_22  (
    .Cout(\一位全加器fa封装2_22_cout [0]), .Si(\一位全加器fa封装2_22_si ), .Cin(\一位全加器fa封装2_29_cout ),
    .Xi(\一位全加器fa封装2_23_si ), .Yi(\一位全加器fa封装2_26_si ));
  \一位全加器FA封装2  \u_一位全加器fa封装2_23  (
    .Cout(\一位全加器fa封装2_23_cout ), .Si(\一位全加器fa封装2_23_si ), .Cin(\一位全加器fa封装2_28_si ), .Xi(\一位全加器fa封装2_24_si ),
    .Yi(\一位全加器fa封装2_27_si ));
  \一位全加器FA封装2  \u_一位全加器fa封装2_24  (
    .Cout(\一位全加器fa封装2_28_cout [2]), .Si(\一位全加器fa封装2_24_si ), .Cin(undriven_24), .Xi(undriven_22),
    .Yi(undriven_23));
  shape shape_3 ();
  \一位全加器FA封装2  \u_一位全加器fa封装2_25  (
    .Cout(\一位全加器fa封装2_25_cout ), .Si(\一位全加器fa封装2_25_si ), .Cin(\一位全加器fa封装2_32_cout [0]),
    .Xi(\一位全加器fa封装2_22_si ), .Yi(\一位全加器fa封装2_32_cout [1]));
  \一位全加器FA封装2  \u_一位全加器fa封装2_26  (
    .Cout(\一位全加器fa封装2_22_cout [1]), .Si(\一位全加器fa封装2_26_si ), .Cin(\一位全加器fa封装2_34_cout [0]),
    .Xi(\一位全加器fa封装2_34_cout [2]), .Yi(\一位全加器fa封装2_34_cout [1]));
  \一位全加器FA封装2  \u_一位全加器fa封装2_27  (
    .Cout(\一位全加器fa封装2_28_cout [1]), .Si(\一位全加器fa封装2_27_si ), .Cin(undriven_27), .Xi(undriven_25),
    .Yi(undriven_26));
  \一位全加器FA封装2  \u_一位全加器fa封装2_28  (
    .Cout(\一位全加器fa封装2_28_cout [0]), .Si(\一位全加器fa封装2_28_si ), .Cin(1'b0), .Xi(undriven_28), .Yi(undriven_29));
  \一位全加器FA封装2  \u_一位全加器fa封装2_29  (
    .Cout(\一位全加器fa封装2_29_cout ), .Si(\一位全加器fa封装2_29_si ), .Cin(\一位全加器fa封装2_34_si ), .Xi(\一位全加器fa封装2_30_si ),
    .Yi(\一位全加器fa封装2_35_si ));
  \一位全加器FA封装2  \u_一位全加器fa封装2_30  (
    .Cout(\一位全加器fa封装2_34_cout [2]), .Si(\一位全加器fa封装2_30_si ), .Cin(undriven_32), .Xi(undriven_30),
    .Yi(undriven_31));
  \一位全加器FA封装2  \u_一位全加器fa封装2_31  (
    .Cout(\一位全加器fa封装2_31_cout ), .Si(\一位全加器fa封装2_31_si ), .Cin(\一位全加器fa封装2_38_cout [0]),
    .Xi(\一位全加器fa封装2_32_si ), .Yi(\一位全加器fa封装2_38_cout [1]));
  \一位全加器FA封装2  \u_一位全加器fa封装2_32  (
    .Cout(\一位全加器fa封装2_32_cout [0]), .Si(\一位全加器fa封装2_32_si ), .Cin(\一位全加器fa封装2_39_cout ),
    .Xi(\一位全加器fa封装2_29_si ), .Yi(\一位全加器fa封装2_33_si ));
  \一位全加器FA封装2  \u_一位全加器fa封装2_33  (
    .Cout(\一位全加器fa封装2_32_cout [1]), .Si(\一位全加器fa封装2_33_si ), .Cin(\一位全加器fa封装2_42_cout [0]),
    .Xi(\一位全加器fa封装2_42_cout [2]), .Yi(\一位全加器fa封装2_42_cout [1]));
  \一位全加器FA封装2  \u_一位全加器fa封装2_34  (
    .Cout(\一位全加器fa封装2_34_cout [0]), .Si(\一位全加器fa封装2_34_si ), .Cin(1'b0), .Xi(undriven_36), .Yi(undriven_37));
  \一位全加器FA封装2  \u_一位全加器fa封装2_35  (
    .Cout(\一位全加器fa封装2_34_cout [1]), .Si(\一位全加器fa封装2_35_si ), .Cin(undriven_35), .Xi(undriven_33),
    .Yi(undriven_34));
  \一位全加器FA封装2  \u_一位全加器fa封装2_36  (
    .Cout(\一位全加器fa封装2_42_cout [2]), .Si(\一位全加器fa封装2_36_si ), .Cin(undriven_40), .Xi(undriven_38),
    .Yi(undriven_39));
  \一位全加器FA封装2  \u_一位全加器fa封装2_37  (
    .Cout(\一位全加器fa封装2_37_cout ), .Si(\一位全加器fa封装2_37_si ), .Cin(\一位全加器fa封装2_44_cout [0]),
    .Xi(\一位全加器fa封装2_38_si ), .Yi(\一位全加器fa封装2_44_cout [1]));
  \一位全加器FA封装2  \u_一位全加器fa封装2_38  (
    .Cout(\一位全加器fa封装2_38_cout [0]), .Si(\一位全加器fa封装2_38_si ), .Cin(\一位全加器fa封装2_45_cout ),
    .Xi(\一位全加器fa封装2_39_si ), .Yi(\一位全加器fa封装2_40_si ));
  \一位全加器FA封装2  \u_一位全加器fa封装2_39  (
    .Cout(\一位全加器fa封装2_39_cout ), .Si(\一位全加器fa封装2_39_si ), .Cin(\一位全加器fa封装2_42_si ), .Xi(\一位全加器fa封装2_36_si ),
    .Yi(\一位全加器fa封装2_41_si ));
  \一位全加器FA封装2  \u_一位全加器fa封装2_40  (
    .Cout(\一位全加器fa封装2_38_cout [1]), .Si(\一位全加器fa封装2_40_si ), .Cin(\一位全加器fa封装2_49_cout [0]),
    .Xi(\一位全加器fa封装2_49_cout [2]), .Yi(\一位全加器fa封装2_49_cout [1]));
  \一位全加器FA封装2  \u_一位全加器fa封装2_41  (
    .Cout(\一位全加器fa封装2_42_cout [1]), .Si(\一位全加器fa封装2_41_si ), .Cin(undriven_43), .Xi(undriven_41),
    .Yi(undriven_42));
  shape shape_4 ();
  \一位全加器FA封装2  \u_一位全加器fa封装2_42  (
    .Cout(\一位全加器fa封装2_42_cout [0]), .Si(\一位全加器fa封装2_42_si ), .Cin(1'b0), .Xi(undriven_44), .Yi(undriven_45));
  \一位全加器FA封装2  \u_一位全加器fa封装2_43  (
    .Cout(\一位全加器fa封装2_43_cout ), .Si(\一位全加器fa封装2_43_si ), .Cin(\一位全加器fa封装2_50_cout [0]),
    .Xi(\一位全加器fa封装2_44_si ), .Yi(\一位全加器fa封装2_50_cout [1]));
  \一位全加器FA封装2  \u_一位全加器fa封装2_44  (
    .Cout(\一位全加器fa封装2_44_cout [0]), .Si(\一位全加器fa封装2_44_si ), .Cin(\一位全加器fa封装2_51_cout ),
    .Xi(\一位全加器fa封装2_45_si ), .Yi(\一位全加器fa封装2_48_si ));
  \一位全加器FA封装2  \u_一位全加器fa封装2_45  (
    .Cout(\一位全加器fa封装2_45_cout ), .Si(\一位全加器fa封装2_45_si ), .Cin(\一位全加器fa封装2_49_si ), .Xi(\一位全加器fa封装2_47_si ),
    .Yi(\一位全加器fa封装2_46_si ));
  \一位全加器FA封装2  \u_一位全加器fa封装2_46  (
    .Cout(\一位全加器fa封装2_49_cout [1]), .Si(\一位全加器fa封装2_46_si ), .Cin(undriven_51), .Xi(undriven_49),
    .Yi(undriven_50));
  \一位全加器FA封装2  \u_一位全加器fa封装2_47  (
    .Cout(\一位全加器fa封装2_49_cout [2]), .Si(\一位全加器fa封装2_47_si ), .Cin(undriven_48), .Xi(undriven_46),
    .Yi(undriven_47));
  \一位全加器FA封装2  \u_一位全加器fa封装2_48  (
    .Cout(\一位全加器fa封装2_44_cout [1]), .Si(\一位全加器fa封装2_48_si ), .Cin(\一位全加器fa封装2_56_cout [0]),
    .Xi(\一位全加器fa封装2_56_cout [2]), .Yi(\一位全加器fa封装2_56_cout [1]));
  \一位全加器FA封装2  \u_一位全加器fa封装2_49  (
    .Cout(\一位全加器fa封装2_49_cout [0]), .Si(\一位全加器fa封装2_49_si ), .Cin(1'b0), .Xi(undriven_52), .Yi(undriven_53));
  \一位全加器FA封装2  \u_一位全加器fa封装2_50  (
    .Cout(\一位全加器fa封装2_50_cout [0]), .Si(\一位全加器fa封装2_50_si ), .Cin(\一位全加器fa封装2_57_cout ),
    .Xi(\一位全加器fa封装2_51_si ), .Yi(\一位全加器fa封装2_54_si ));
  \一位全加器FA封装2  \u_一位全加器fa封装2_51  (
    .Cout(\一位全加器fa封装2_51_cout ), .Si(\一位全加器fa封装2_51_si ), .Cin(\一位全加器fa封装2_56_si ), .Xi(\一位全加器fa封装2_52_si ),
    .Yi(\一位全加器fa封装2_55_si ));
  \一位全加器FA封装2  \u_一位全加器fa封装2_52  (
    .Cout(\一位全加器fa封装2_56_cout [2]), .Si(\一位全加器fa封装2_52_si ), .Cin(undriven_56), .Xi(undriven_54),
    .Yi(undriven_55));
  shape shape_5 ();
  \一位全加器FA封装2  \u_一位全加器fa封装2_53  (
    .Cout(\一位全加器fa封装2_53_cout ), .Si(\一位全加器fa封装2_53_si ), .Cin(\一位全加器fa封装2_60_cout [0]),
    .Xi(\一位全加器fa封装2_50_si ), .Yi(\一位全加器fa封装2_60_cout [1]));
  \一位全加器FA封装2  \u_一位全加器fa封装2_54  (
    .Cout(\一位全加器fa封装2_50_cout [1]), .Si(\一位全加器fa封装2_54_si ), .Cin(\一位全加器fa封装2_63_cout [0]),
    .Xi(\一位全加器fa封装2_63_cout [2]), .Yi(\一位全加器fa封装2_63_cout [1]));
  \一位全加器FA封装2  \u_一位全加器fa封装2_55  (
    .Cout(\一位全加器fa封装2_56_cout [1]), .Si(\一位全加器fa封装2_55_si ), .Cin(undriven_59), .Xi(undriven_57),
    .Yi(undriven_58));
  \一位全加器FA封装2  \u_一位全加器fa封装2_56  (
    .Cout(\一位全加器fa封装2_56_cout [0]), .Si(\一位全加器fa封装2_56_si ), .Cin(1'b0), .Xi(undriven_60), .Yi(undriven_61));
  \一位全加器FA封装2  \u_一位全加器fa封装2_57  (
    .Cout(\一位全加器fa封装2_57_cout ), .Si(\一位全加器fa封装2_57_si ), .Cin(\一位全加器fa封装2_63_si ), .Xi(\一位全加器fa封装2_58_si ),
    .Yi(\一位全加器fa封装2_62_si ));
  \一位全加器FA封装2  \u_一位全加器fa封装2_58  (
    .Cout(\一位全加器fa封装2_63_cout [2]), .Si(\一位全加器fa封装2_58_si ), .Cin(undriven_64), .Xi(undriven_62),
    .Yi(undriven_63));
  \一位全加器FA封装2  \u_一位全加器fa封装2_59  (
    .Cout(\一位全加器fa封装2_59_cout ), .Si(\一位全加器fa封装2_59_si ), .Cin(\一位全加器fa封装2_66_cout [0]),
    .Xi(\一位全加器fa封装2_60_si ), .Yi(\一位全加器fa封装2_66_cout [1]));
  \一位全加器FA封装2  \u_一位全加器fa封装2_60  (
    .Cout(\一位全加器fa封装2_60_cout [0]), .Si(\一位全加器fa封装2_60_si ), .Cin(\一位全加器fa封装2_68_cout ),
    .Xi(\一位全加器fa封装2_57_si ), .Yi(\一位全加器fa封装2_61_si ));
  \一位全加器FA封装2  \u_一位全加器fa封装2_61  (
    .Cout(\一位全加器fa封装2_60_cout [1]), .Si(\一位全加器fa封装2_61_si ), .Cin(\一位全加器fa封装2_70_cout [0]),
    .Xi(\一位全加器fa封装2_70_cout [2]), .Yi(\一位全加器fa封装2_70_cout [1]));
  \一位全加器FA封装2  \u_一位全加器fa封装2_62  (
    .Cout(\一位全加器fa封装2_63_cout [1]), .Si(\一位全加器fa封装2_62_si ), .Cin(undriven_67), .Xi(undriven_65),
    .Yi(undriven_66));
  \一位全加器FA封装2  \u_一位全加器fa封装2_63  (
    .Cout(\一位全加器fa封装2_63_cout [0]), .Si(\一位全加器fa封装2_63_si ), .Cin(1'b0), .Xi(undriven_68), .Yi(undriven_69));
  \一位全加器FA封装2  \u_一位全加器fa封装2_64  (
    .Cout(\一位全加器fa封装2_70_cout [2]), .Si(\一位全加器fa封装2_64_si ), .Cin(undriven_72), .Xi(undriven_70),
    .Yi(undriven_71));
  \一位全加器FA封装2  \u_一位全加器fa封装2_65  (
    .Cout(\一位全加器fa封装2_65_cout ), .Si(\一位全加器fa封装2_65_si ), .Cin(\一位全加器fa封装2_72_cout [0]),
    .Xi(\一位全加器fa封装2_66_si ), .Yi(\一位全加器fa封装2_72_cout [1]));
  \一位全加器FA封装2  \u_一位全加器fa封装2_66  (
    .Cout(\一位全加器fa封装2_66_cout [0]), .Si(\一位全加器fa封装2_66_si ), .Cin(\一位全加器fa封装2_73_cout ),
    .Xi(\一位全加器fa封装2_68_si ), .Yi(\一位全加器fa封装2_67_si ));
  \一位全加器FA封装2  \u_一位全加器fa封装2_67  (
    .Cout(\一位全加器fa封装2_66_cout [1]), .Si(\一位全加器fa封装2_67_si ), .Cin(\一位全加器fa封装2_77_cout [0]),
    .Xi(\一位全加器fa封装2_77_cout [2]), .Yi(\一位全加器fa封装2_77_cout [1]));
  \一位全加器FA封装2  \u_一位全加器fa封装2_68  (
    .Cout(\一位全加器fa封装2_68_cout ), .Si(\一位全加器fa封装2_68_si ), .Cin(\一位全加器fa封装2_70_si ), .Xi(\一位全加器fa封装2_64_si ),
    .Yi(\一位全加器fa封装2_69_si ));
  \一位全加器FA封装2  \u_一位全加器fa封装2_69  (
    .Cout(\一位全加器fa封装2_70_cout [1]), .Si(\一位全加器fa封装2_69_si ), .Cin(undriven_75), .Xi(undriven_73),
    .Yi(undriven_74));
  shape shape_6 ();
  \一位全加器FA封装2  \u_一位全加器fa封装2_70  (
    .Cout(\一位全加器fa封装2_70_cout [0]), .Si(\一位全加器fa封装2_70_si ), .Cin(1'b0), .Xi(undriven_76), .Yi(undriven_77));
  \一位全加器FA封装2  \u_一位全加器fa封装2_71  (
    .Cout(\一位全加器fa封装2_71_cout ), .Si(\一位全加器fa封装2_71_si ), .Cin(\一位全加器fa封装2_78_cout [0]),
    .Xi(\一位全加器fa封装2_72_si ), .Yi(\一位全加器fa封装2_78_cout [1]));
  \一位全加器FA封装2  \u_一位全加器fa封装2_72  (
    .Cout(\一位全加器fa封装2_72_cout [0]), .Si(\一位全加器fa封装2_72_si ), .Cin(\一位全加器fa封装2_79_cout ),
    .Xi(\一位全加器fa封装2_73_si ), .Yi(\一位全加器fa封装2_76_si ));
  \一位全加器FA封装2  \u_一位全加器fa封装2_73  (
    .Cout(\一位全加器fa封装2_73_cout ), .Si(\一位全加器fa封装2_73_si ), .Cin(\一位全加器fa封装2_77_si ), .Xi(\一位全加器fa封装2_74_si ),
    .Yi(\一位全加器fa封装2_75_si ));
  \一位全加器FA封装2  \u_一位全加器fa封装2_74  (
    .Cout(\一位全加器fa封装2_77_cout [2]), .Si(\一位全加器fa封装2_74_si ), .Cin(undriven_80), .Xi(undriven_78),
    .Yi(undriven_79));
  \一位全加器FA封装2  \u_一位全加器fa封装2_75  (
    .Cout(\一位全加器fa封装2_77_cout [1]), .Si(\一位全加器fa封装2_75_si ), .Cin(undriven_83), .Xi(undriven_81),
    .Yi(undriven_82));
  \一位全加器FA封装2  \u_一位全加器fa封装2_76  (
    .Cout(\一位全加器fa封装2_72_cout [1]), .Si(\一位全加器fa封装2_76_si ), .Cin(\一位全加器fa封装2_83_cout [0]),
    .Xi(\一位全加器fa封装2_83_cout [2]), .Yi(\一位全加器fa封装2_83_cout [1]));
  \一位全加器FA封装2  \u_一位全加器fa封装2_77  (
    .Cout(\一位全加器fa封装2_77_cout [0]), .Si(\一位全加器fa封装2_77_si ), .Cin(1'b0), .Xi(undriven_84), .Yi(undriven_85));
  \一位全加器FA封装2  \u_一位全加器fa封装2_78  (
    .Cout(\一位全加器fa封装2_78_cout [0]), .Si(\一位全加器fa封装2_78_si ), .Cin(\一位全加器fa封装2_85_cout ),
    .Xi(\一位全加器fa封装2_79_si ), .Yi(\一位全加器fa封装2_82_si ));
  \一位全加器FA封装2  \u_一位全加器fa封装2_79  (
    .Cout(\一位全加器fa封装2_79_cout ), .Si(\一位全加器fa封装2_79_si ), .Cin(\一位全加器fa封装2_83_si ), .Xi(\一位全加器fa封装2_80_si ),
    .Yi(\一位全加器fa封装2_84_si ));
  \一位全加器FA封装2  \u_一位全加器fa封装2_80  (
    .Cout(\一位全加器fa封装2_83_cout [2]), .Si(\一位全加器fa封装2_80_si ), .Cin(undriven_88), .Xi(undriven_86),
    .Yi(undriven_87));
  shape shape_7 ();
  \一位全加器FA封装2  \u_一位全加器fa封装2_81  (
    .Cout(\一位全加器fa封装2_81_cout ), .Si(\一位全加器fa封装2_81_si ), .Cin(\一位全加器fa封装2_88_cout [0]),
    .Xi(\一位全加器fa封装2_78_si ), .Yi(\一位全加器fa封装2_88_cout [1]));
  \一位全加器FA封装2  \u_一位全加器fa封装2_82  (
    .Cout(\一位全加器fa封装2_78_cout [1]), .Si(\一位全加器fa封装2_82_si ), .Cin(\一位全加器fa封装2_90_cout [0]),
    .Xi(\一位全加器fa封装2_90_cout [2]), .Yi(\一位全加器fa封装2_90_cout [1]));
  \一位全加器FA封装2  \u_一位全加器fa封装2_83  (
    .Cout(\一位全加器fa封装2_83_cout [0]), .Si(\一位全加器fa封装2_83_si ), .Cin(1'b0), .Xi(undriven_92), .Yi(undriven_93));
  \一位全加器FA封装2  \u_一位全加器fa封装2_84  (
    .Cout(\一位全加器fa封装2_83_cout [1]), .Si(\一位全加器fa封装2_84_si ), .Cin(undriven_91), .Xi(undriven_89),
    .Yi(undriven_90));
  \一位全加器FA封装2  \u_一位全加器fa封装2_85  (
    .Cout(\一位全加器fa封装2_85_cout ), .Si(\一位全加器fa封装2_85_si ), .Cin(\一位全加器fa封装2_90_si ), .Xi(\一位全加器fa封装2_86_si ),
    .Yi(\一位全加器fa封装2_91_si ));
  \一位全加器FA封装2  \u_一位全加器fa封装2_86  (
    .Cout(\一位全加器fa封装2_90_cout [2]), .Si(\一位全加器fa封装2_86_si ), .Cin(undriven_96), .Xi(undriven_94),
    .Yi(undriven_95));
  \一位全加器FA封装2  \u_一位全加器fa封装2_87  (
    .Cout(\一位全加器fa封装2_87_cout ), .Si(\一位全加器fa封装2_87_si ), .Cin(\一位全加器fa封装2_94_cout [0]),
    .Xi(\一位全加器fa封装2_88_si ), .Yi(\一位全加器fa封装2_94_cout [1]));
  \一位全加器FA封装2  \u_一位全加器fa封装2_88  (
    .Cout(\一位全加器fa封装2_88_cout [0]), .Si(\一位全加器fa封装2_88_si ), .Cin(\一位全加器fa封装2_95_cout ),
    .Xi(\一位全加器fa封装2_85_si ), .Yi(\一位全加器fa封装2_89_si ));
  \一位全加器FA封装2  \u_一位全加器fa封装2_89  (
    .Cout(\一位全加器fa封装2_88_cout [1]), .Si(\一位全加器fa封装2_89_si ), .Cin(\一位全加器fa封装2_98_cout [0]),
    .Xi(\一位全加器fa封装2_98_cout [2]), .Yi(\一位全加器fa封装2_98_cout [1]));
  \一位全加器FA封装2  \u_一位全加器fa封装2_90  (
    .Cout(\一位全加器fa封装2_90_cout [0]), .Si(\一位全加器fa封装2_90_si ), .Cin(1'b0), .Xi(undriven_100), .Yi(undriven_101));
  \一位全加器FA封装2  \u_一位全加器fa封装2_91  (
    .Cout(\一位全加器fa封装2_90_cout [1]), .Si(\一位全加器fa封装2_91_si ), .Cin(undriven_99), .Xi(undriven_97),
    .Yi(undriven_98));
  \一位全加器FA封装2  \u_一位全加器fa封装2_92  (
    .Cout(\一位全加器fa封装2_98_cout [2]), .Si(\一位全加器fa封装2_92_si ), .Cin(undriven_104), .Xi(undriven_102),
    .Yi(undriven_103));
  \一位全加器FA封装2  \u_一位全加器fa封装2_93  (
    .Cout(\一位全加器fa封装2_93_cout ), .Si(\一位全加器fa封装2_93_si ), .Cin(\一位全加器fa封装2_100_cout [0]),
    .Xi(\一位全加器fa封装2_94_si ), .Yi(\一位全加器fa封装2_100_cout [1]));
  \一位全加器FA封装2  \u_一位全加器fa封装2_94  (
    .Cout(\一位全加器fa封装2_94_cout [0]), .Si(\一位全加器fa封装2_94_si ), .Cin(\一位全加器fa封装2_101_cout ),
    .Xi(\一位全加器fa封装2_95_si ), .Yi(\一位全加器fa封装2_96_si ));
  \一位全加器FA封装2  \u_一位全加器fa封装2_95  (
    .Cout(\一位全加器fa封装2_95_cout ), .Si(\一位全加器fa封装2_95_si ), .Cin(\一位全加器fa封装2_98_si ), .Xi(\一位全加器fa封装2_92_si ),
    .Yi(\一位全加器fa封装2_97_si ));
  \一位全加器FA封装2  \u_一位全加器fa封装2_96  (
    .Cout(\一位全加器fa封装2_94_cout [1]), .Si(\一位全加器fa封装2_96_si ), .Cin(\一位全加器fa封装2_105_cout [0]),
    .Xi(\一位全加器fa封装2_105_cout [2]), .Yi(\一位全加器fa封装2_105_cout [1]));
  \一位全加器FA封装2  \u_一位全加器fa封装2_97  (
    .Cout(\一位全加器fa封装2_98_cout [1]), .Si(\一位全加器fa封装2_97_si ), .Cin(undriven_107), .Xi(undriven_105),
    .Yi(undriven_106));
  shape shape_8 ();
  \一位全加器FA封装2  \u_一位全加器fa封装2_98  (
    .Cout(\一位全加器fa封装2_98_cout [0]), .Si(\一位全加器fa封装2_98_si ), .Cin(1'b0), .Xi(undriven_108), .Yi(undriven_109));
  \一位全加器FA封装2  \u_一位全加器fa封装2_99  (
    .Cout(\一位全加器fa封装2_99_cout ), .Si(\一位全加器fa封装2_99_si ), .Cin(\一位全加器fa封装2_106_cout [0]),
    .Xi(\一位全加器fa封装2_100_si ), .Yi(\一位全加器fa封装2_106_cout [1]));
  \一位全加器FA封装2  \u_一位全加器fa封装2_100  (
    .Cout(\一位全加器fa封装2_100_cout [0]), .Si(\一位全加器fa封装2_100_si ), .Cin(\一位全加器fa封装2_107_cout ),
    .Xi(\一位全加器fa封装2_101_si ), .Yi(\一位全加器fa封装2_104_si ));
  \一位全加器FA封装2  \u_一位全加器fa封装2_101  (
    .Cout(\一位全加器fa封装2_101_cout ), .Si(\一位全加器fa封装2_101_si ), .Cin(\一位全加器fa封装2_105_si ),
    .Xi(\一位全加器fa封装2_102_si ), .Yi(\一位全加器fa封装2_103_si ));
  \一位全加器FA封装2  \u_一位全加器fa封装2_102  (
    .Cout(\一位全加器fa封装2_105_cout [2]), .Si(\一位全加器fa封装2_102_si ), .Cin(undriven_112), .Xi(undriven_110),
    .Yi(undriven_111));
  \一位全加器FA封装2  \u_一位全加器fa封装2_103  (
    .Cout(\一位全加器fa封装2_105_cout [1]), .Si(\一位全加器fa封装2_103_si ), .Cin(undriven_115), .Xi(undriven_113),
    .Yi(undriven_114));
  \一位全加器FA封装2  \u_一位全加器fa封装2_104  (
    .Cout(\一位全加器fa封装2_100_cout [1]), .Si(\一位全加器fa封装2_104_si ), .Cin(\一位全加器fa封装2_111_cout [0]),
    .Xi(\一位全加器fa封装2_111_cout [2]), .Yi(\一位全加器fa封装2_111_cout [1]));
  \一位全加器FA封装2  \u_一位全加器fa封装2_105  (
    .Cout(\一位全加器fa封装2_105_cout [0]), .Si(\一位全加器fa封装2_105_si ), .Cin(1'b0), .Xi(undriven_116),
    .Yi(undriven_117));
  \一位全加器FA封装2  \u_一位全加器fa封装2_106  (
    .Cout(\一位全加器fa封装2_106_cout [0]), .Si(\一位全加器fa封装2_106_si ), .Cin(undriven_122), .Xi(\一位全加器fa封装2_107_si ),
    .Yi(\一位全加器fa封装2_110_si ));
  \一位全加器FA封装2  \u_一位全加器fa封装2_107  (
    .Cout(\一位全加器fa封装2_107_cout ), .Si(\一位全加器fa封装2_107_si ), .Cin(\一位全加器fa封装2_111_si ),
    .Xi(\一位全加器fa封装2_108_si ), .Yi(\一位全加器fa封装2_112_si ));
  \一位全加器FA封装2  \u_一位全加器fa封装2_108  (
    .Cout(\一位全加器fa封装2_111_cout [2]), .Si(\一位全加器fa封装2_108_si ), .Cin(undriven_120), .Xi(undriven_118),
    .Yi(undriven_119));
  \一位全加器FA封装2  \u_一位全加器fa封装2_109  (
    .Cout(\一位全加器fa封装2_109_cout ), .Si(\一位全加器fa封装2_109_si ), .Cin(undriven_128[0]), .Xi(\一位全加器fa封装2_106_si ),
    .Yi(undriven_128[1]));
  \一位全加器FA封装2  \u_一位全加器fa封装2_110  (
    .Cout(\一位全加器fa封装2_106_cout [1]), .Si(\一位全加器fa封装2_110_si ), .Cin(undriven_126[0]), .Xi(undriven_126[2]),
    .Yi(undriven_126[1]));
  \一位全加器FA封装2  \u_一位全加器fa封装2_111  (
    .Cout(\一位全加器fa封装2_111_cout [0]), .Si(\一位全加器fa封装2_111_si ), .Cin(1'b0), .Xi(undriven_125),
    .Yi(undriven_127));
  \一位全加器FA封装2  \u_一位全加器fa封装2_112  (
    .Cout(\一位全加器fa封装2_111_cout [1]), .Si(\一位全加器fa封装2_112_si ), .Cin(undriven_124), .Xi(undriven_121),
    .Yi(undriven_123));
endmodule

module _74182 (
  input  G4,
  input  P4,
  input  G3,
  input  P3,
  input  G2,
  input  P2,
  input  G1,
  input  P1,
  input  C,
  output G,
  output P,
  output C4,
  output C3,
  output C2,
  output C1
);

  wire and_1_out, and_2_out, and_3_out, and_5_out, and_6_out, and_7_out, and_8_out, and_9_out, and_10_out,
       and_11_out, and_12_out, and_13_out, and_14_out;

  and and_1 (and_1_out, P4, P3, P2, G1);
  and and_2 (and_2_out, P4, P3, G2);
  and and_3 (and_3_out, P4, G3);
  and and_4 (P, P1, P2, P3, P4);
  and and_5 (and_5_out, P4, G3);
  and and_6 (and_6_out, P4, P3, G2);
  and and_7 (and_7_out, P4, P3, P2, G1);
  and and_8 (and_8_out, P4, P3, P1, P2, C);
  and and_9 (and_9_out, P3, P1, P2, C);
  and and_10 (and_10_out, P3, P2, G1);
  and and_11 (and_11_out, P3, G2);
  and and_12 (and_12_out, P1, P2, C);
  and and_13 (and_13_out, P2, G1);
  and and_14 (and_14_out, C, P1);
  or or_1 (G, and_1_out, and_2_out, and_3_out, G4);
  or or_2 (C4, G4, and_5_out, and_6_out, and_7_out, and_8_out);
  or or_3 (C3, and_9_out, and_10_out, and_11_out, G3);
  or or_4 (C2, and_12_out, and_13_out, G2);
  or or_5 (C1, and_14_out, G1);
endmodule

module \CLA74182封装2  (
  input  G4,
  input  P4,
  input  G3,
  input  P3,
  input  G2,
  input  P2,
  input  G1,
  input  P1,
  input  Cin,
  output C4,
  output C3,
  output C2,
  output C1,
  output G_star,
  output P_star
);

  _74182 u_74182_1 (
    .G4(G4), .P4(P4), .G(G_star), .G3(G3), .P3(P3), .P(P_star), .G2(G2), .P2(P2), .C4(C4), .G1(G1), .P1(P1),
    .C(Cin), .C3(C3), .C2(C2), .C1(C1));

  // Notes on the sheet:
  //   输入引脚区
  //   请根据以上引脚以及隧道信号设计完成74LS182先行进位电路
  //   输出引脚区
  //   请勿增改引脚定义
endmodule
