// Logisim project 多中断.circ as structural Verilog: 8 circuits, main circuit cpu
module cpu (
);

  wire and_1_out, and_2_out, and_3_out, and_4_out, clk, comparator_4_eq, comparator_5_eq, comparator_6_eq,
       comparator_7_eq, comparator_8_eq, comparator_9_eq, comparator_10_eq, comparator_11_eq,
       comparator_12_eq, CONTROL_a, CONTROL_w, CONTROL_we, eq, eret, halt, interupt1, interupt2, interupt3,
       IR1, IR2, IR3, le, mfc0, mtc0, not_1_out, not_2_out, not_3_out, or_1_out, or_2_out, or_3_out, RST,
       sys, W1, W2, W3, zhongduan;
  wire [1:0] CONTROL_b, CONTROL_din, CONTROL_rw, multiplexer_4_out, xy;
  wire [2:0] jump;
  wire [3:0] CONTROL_aluop;
  wire [4:0] multiplexer_6_out, multiplexer_8_out, registerfile_1_p6;
  wire [5:0] rom_1_data_3;
  wire [9:0] multiplexer_1_out, multiplexer_2_out, npc_1_pc11, PC_q, savepc, savepc1, savepc2, savepc3,
       yuanpc, zhongduanpc;
  wire [11:0] ALU_r_2, ALU_r_3;
  wire [15:0] incrementer_1_p2, incrementer_2_p2, incrementer_3_p2, incrementer_4_p2, multiplexer_13_out,
       multiplexer_14_out, multiplexer_15_out, multiplexer_16_out, rom_1_data, \总周期数 , \无条件分支指令数 ,
       \有条件分支成功跳转 , \有条件分支指令数 ;
  wire [19:0] ALU_r;
  wire [25:16] rom_1_data_2;
  wire [31:0] a0, bit_extender_1_out, bit_extender_2_out, bit_extender_3_out, mips_ram_1_p8,
       multiplexer_7_out, multiplexer_11_out, multiplexer_12_out, SyscallOut, v0;

  Button \u_总复位  (.out(RST));
  Button _1 (.out(IR1));
  Button _2 (.out(IR2));
  Button _3 (.out(IR3));
  LED led_1 (.in(W1));
  LED led_2 (.in(W2));
  LED led_3 (.in(W3));
  Clock clock_1 (.out(clk));
  not not_1 (not_1_out, halt);
  Multiplexer #(.width(10), .enable("false")) multiplexer_1 (
    .in0(multiplexer_2_out), .in1(zhongduanpc), .out(multiplexer_1_out), .sel(zhongduan));
  Register #(.width(10)) PC (.D(multiplexer_1_out), .en(not_1_out), .Q(PC_q), .clk(clk), .clr(RST));
  npc npc_1 (
    .pc(PC_q), .addr({rom_1_data_2, rom_1_data}), .p(jump), .rs(v0), .offset(rom_1_data), .less(le),
    .equ(eq), .out(yuanpc), .pc11(npc_1_pc11));
  Multiplexer #(.width(10), .enable("false")) multiplexer_2 (
    .in0(yuanpc), .in1(savepc), .out(multiplexer_2_out), .sel(eret));
  Hex_Digit_Display hex_digit_display_1 (.value(SyscallOut[27:24]));  // open: dp
  Hex_Digit_Display hex_digit_display_2 (.value(SyscallOut[31:28]));  // open: dp
  Multiplexer #(.select(2), .width(10), .enable("false")) multiplexer_3 (
    .in0({10{1'b0}}), .in1(10'hdb), .in2(10'hfb), .in3(10'h11b), .out(zhongduanpc), .sel(xy));
  Hex_Digit_Display hex_digit_display_3 (.value(SyscallOut[19:16]));  // open: dp
  Hex_Digit_Display hex_digit_display_4 (.value(SyscallOut[23:20]));  // open: dp
  aluctr CONTROL (
    .op(rom_1_data_3), .func(rom_1_data[5:0]), .rw(CONTROL_rw), .din(CONTROL_din), .A(CONTROL_a),
    .B(CONTROL_b), .WE(CONTROL_we), .pc(jump), .W(CONTROL_w), .syscall(sys), .aluop(CONTROL_aluop));  // open: addr, rtype
  Register #(.width(10)) register_1 (.D(yuanpc), .en(interupt1), .Q(savepc1), .clk(clk));  // open: clr
  Register #(.width(10)) register_2 (.D(yuanpc), .en(interupt2), .Q(savepc2), .clk(clk));  // open: clr
  Register #(.width(10)) register_3 (.D(yuanpc), .en(interupt3), .Q(savepc3), .clk(clk));  // open: clr
  Hex_Digit_Display hex_digit_display_5 (.value(SyscallOut[15:12]));  // open: dp
  Hex_Digit_Display hex_digit_display_6 (.value(SyscallOut[11:8]));  // open: dp
  ROM #(.addrWidth(10), .dataWidth(32)) rom_1 (
    .addr(PC_q), .data({rom_1_data_3, rom_1_data_2, rom_1_data}));  // open: sel
  assign bit_extender_1_out = {{22{1'b0}}, npc_1_pc11};  // Bit_Extender bit_extender_1
  Hex_Digit_Display hex_digit_display_7 (.value(SyscallOut[3:0]));  // open: dp
  Hex_Digit_Display hex_digit_display_8 (.value(SyscallOut[7:4]));  // open: dp
  Multiplexer #(.width(2), .enable("false")) multiplexer_4 (
    .in0(2'b00), .in1(xy), .out(multiplexer_4_out), .sel(zhongduan));
  Comparator #(.width(32)) comparator_1 (
    .a({rom_1_data_3, rom_1_data_2, rom_1_data}), .b(32'h42000018), .eq(eret));  // open: gt, lt
  Comparator #(.width(32)) comparator_2 (
    .a({rom_1_data_3, rom_1_data_2, rom_1_data}), .b(32'h409cf000), .eq(mtc0));  // open: gt, lt
  Comparator #(.width(32)) comparator_3 (
    .a({rom_1_data_3, rom_1_data_2, rom_1_data}), .b(32'h401cf000), .eq(mfc0));  // open: gt, lt
  Decoder #(.select(2), .enable("false")) decoder_1 (
    .out1(interupt1), .out2(interupt2), .out3(interupt3), .sel(multiplexer_4_out));  // open: out0
  Multiplexer #(.select(2), .width(10), .enable("false")) multiplexer_5 (
    .in0({10{1'b0}}), .in1(savepc1), .in2(savepc2), .in3(savepc3), .out(savepc), .sel(xy));
  Multiplexer #(.select(2), .width(5), .enable("false")) multiplexer_6 (
    .in0(rom_1_data[15:11]), .in1(rom_1_data_2[20:16]), .in2({5{1'b1}}), .in3(5'b11100),
    .out(multiplexer_6_out), .sel(CONTROL_rw));
  Comparator #(.width(32)) comparator_4 (.a(v0), .b(32'ha), .eq(comparator_4_eq));  // open: gt, lt
  // Probe on \总周期数 
  // Probe on \无条件分支指令数 
  // Probe on \有条件分支指令数 
  // Probe on \有条件分支成功跳转 
  Multiplexer #(.select(2), .width(32), .enable("false")) multiplexer_7 (
    .in0({ALU_r_3, ALU_r[19:14], ALU_r_2, ALU_r[1:0]}), .in1(mips_ram_1_p8), .in2(bit_extender_1_out),
    .in3({32{1'b0}}), .out(multiplexer_7_out), .sel(CONTROL_din));
  Multiplexer #(.width(5), .enable("false")) multiplexer_8 (
    .in0(rom_1_data_2[25:21]), .in1(5'b00010), .out(multiplexer_8_out), .sel(sys));
  Multiplexer #(.enable("false")) multiplexer_9 (.in0(1'b0), .in1(comparator_4_eq), .out(halt), .sel(sys));
  not not_2 (not_2_out, halt);
  and and_1 (and_1_out, not_2_out, sys);
  // RegisterFile registerfile_1: pin names not known; wires that end beside it: multiplexer_7_out, clk, CONTROL_we, multiplexer_6_out, multiplexer_8_out, registerfile_1_p6, v0, a0
  assign bit_extender_2_out = {{27{rom_1_data[10]}}, rom_1_data[10:6]};  // Bit_Extender bit_extender_2
  Multiplexer #(.width(5), .enable("false")) multiplexer_10 (
    .in0(rom_1_data_2[20:16]), .in1(5'b00100), .out(registerfile_1_p6), .sel(sys));
  assign bit_extender_3_out = {{16{rom_1_data[15]}}, rom_1_data};  // Bit_Extender bit_extender_3
  Register #(.width(32)) register_4 (.D(a0), .en(and_1_out), .Q(SyscallOut), .clk(clk), .clr(RST));
  Multiplexer #(.width(32), .enable("false")) multiplexer_11 (
    .in0(v0), .in1(a0), .out(multiplexer_11_out), .sel(CONTROL_a));
  alu ALU (
    .A(multiplexer_11_out), .B(multiplexer_12_out), .op(CONTROL_aluop),
    .R({ALU_r_3, ALU_r[19:14], ALU_r_2, ALU_r[1:0]}), .out_6(eq), .les(le));
  Multiplexer #(.select(2), .width(32), .enable("false")) multiplexer_12 (
    .in0(a0), .in1(bit_extender_2_out), .in2(bit_extender_3_out), .in3({32{1'b0}}), .out(multiplexer_12_out),
    .sel(CONTROL_b));
  // MIPS_RAM mips_ram_1: pin names not known; wires that end beside it: ALU_r_2, a0, CONTROL_w, 4'b1111, clk, 1'b1, RST, mips_ram_1_p8
  Comparator #(.width(3)) comparator_5 (.a(jump), .b(3'b001), .eq(comparator_5_eq));  // open: gt, lt
  Comparator #(.width(3)) comparator_6 (.a(jump), .b(3'b100), .eq(comparator_6_eq));  // open: gt, lt
  Comparator #(.width(3)) comparator_7 (.a(jump), .b(3'b101), .eq(comparator_7_eq));  // open: gt, lt
  // Incrementer incrementer_1: pin names not known; wires that end beside it: \有条件分支成功跳转 , incrementer_1_p2
  and and_2 (and_2_out, comparator_5_eq, le);
  and and_3 (and_3_out, comparator_6_eq, eq);
  and and_4 (and_4_out, comparator_7_eq, not_3_out);
  not not_3 (not_3_out, eq);
  \中断  \u_中断_1  (
    .ir2(IR2), .ir3(IR3), .clk(clk), .ir1(IR1), .xy(xy), .zhongduan(zhongduan), .eret(eret), .mtc0(mtc0),
    .mfc0(mfc0), .w3(W3), .w2(W2), .w1(W1));
  Multiplexer #(.width(16), .enable("false")) multiplexer_13 (
    .in0(\有条件分支成功跳转 ), .in1(incrementer_1_p2), .out(multiplexer_13_out), .sel(or_1_out));
  or or_1 (or_1_out, and_2_out, and_3_out, and_4_out);
  Counter #(.width(16), .max('hffff)) counter_1 (
    .load(1'b1), .D(multiplexer_13_out), .count(1'b0), .Q(\有条件分支成功跳转 ), .clk(clk), .clr(RST));  // open: carry
  // Incrementer incrementer_2: pin names not known; wires that end beside it: \总周期数 , incrementer_2_p2
  Multiplexer #(.width(16), .enable("false")) multiplexer_14 (
    .in0(incrementer_2_p2), .in1(\总周期数 ), .out(multiplexer_14_out), .sel(halt));
  Counter #(.width(16), .max('hffff)) counter_2 (
    .load(1'b1), .D(multiplexer_14_out), .count(1'b0), .Q(\总周期数 ), .clk(clk), .clr(RST));  // open: carry
  Comparator #(.width(3)) comparator_8 (.a(jump), .b(3'b001), .eq(comparator_8_eq));  // open: gt, lt
  Comparator #(.width(3)) comparator_9 (.a(jump), .b(3'b100), .eq(comparator_9_eq));  // open: gt, lt
  Comparator #(.width(3)) comparator_10 (.a(jump), .b(3'b101), .eq(comparator_10_eq));  // open: gt, lt
  // Incrementer incrementer_3: pin names not known; wires that end beside it: \无条件分支指令数 , incrementer_3_p2
  Comparator #(.width(3)) comparator_11 (.a(jump), .b(3'b010), .eq(comparator_11_eq));  // open: gt, lt
  Comparator #(.width(3)) comparator_12 (.a(jump), .b(3'b011), .eq(comparator_12_eq));  // open: gt, lt
  Multiplexer #(.width(16), .enable("false")) multiplexer_15 (
    .in0(\有条件分支指令数 ), .in1(incrementer_4_p2), .out(multiplexer_15_out), .sel(or_2_out));
  // Incrementer incrementer_4: pin names not known; wires that end beside it: \有条件分支指令数 , incrementer_4_p2
  or or_2 (or_2_out, comparator_8_eq, comparator_9_eq, comparator_10_eq);
  Multiplexer #(.width(16), .enable("false")) multiplexer_16 (
    .in0(\无条件分支指令数 ), .in1(incrementer_3_p2), .out(multiplexer_16_out), .sel(or_3_out));
  or or_3 (or_3_out, comparator_11_eq, comparator_12_eq);
  Counter #(.width(16), .max('hffff)) counter_3 (
    .load(1'b1), .D(multiplexer_15_out), .count(1'b0), .Q(\有条件分支指令数 ), .clk(clk), .clr(RST));  // open: carry
  Counter #(.width(16), .max('hffff)) counter_4 (
    .load(1'b1), .D(multiplexer_16_out), .count(1'b0), .Q(\无条件分支指令数 ), .clk(clk), .clr(RST));  // open: carry

  // Notes on the sheet:
  //   中断源
  //   中断等待指示
  //   数码管输出应该用寄存器锁存，否则显示数据只能一闪而过
  //   可以通过项目增加Logisim库的方式将前几次实验完成的电路作为子电路引入到本电路中使用
  //   指令存储器
  //   contents of rom_1 (hex, n*v repeats v):
  //   20110001 8000c05 20110001 20120002 20130003 8000c09 20110001 20120002 20130003 8000c0d 20110001
  //   20120002 20130003 8000c11 20110001 20120002 20130003 c000cb8 20100001 20110001 118fc0 112020
  //   20020022 c 118882 12200001 8000c15 112020 20020022 c 20110001 118880 112020 20020022 c 12200001
  //   8000c1f 20110001 118fc0 112020 20020022 c 1188c3 112020 20020022 c 118903 112020 20020022 c 118903
  //   112020 20020022 c 118903 112020 20020022 c 118903 112020 20020022 c 118903 112020 20020022 c 118903
  //   112020 20020022 c 118903 112020 20020022 c 20100001 109fc0 139fc3 8021 2012000c 24160003 26100001
  //   3210000f 20080008 20090001 139900 2709825 132020 20020022 c 1094022 1500fff9 22100001 2018000f
  //   2188024 108700 20080008 20090001 139902 2709825 132021 20020022 c 1094022 1500fff9 108702 2c9b022
  //   12c00001 8000c50 4020 1084027 84400 3508ffff 82021 20020022 c 2010ffff 20110000 ae300000 22100001
  //   22310004 ae300000 22100001 22310004 ae300000 22100001 22310004 ae300000 22100001 22310004 ae300000
  //   22100001 22310004 ae300000 22100001 22310004 ae300000 22100001 22310004 ae300000 22100001 22310004
  //   ae300000 22100001 22310004 ae300000 22100001 22310004 ae300000 22100001 22310004 ae300000 22100001
  //   22310004 ae300000 22100001 22310004 ae300000 22100001 22310004 ae300000 22100001 22310004 ae300000
  //   22100001 22310004 22100001 8020 2011003c 8e130000 8e340000 274402a 11000002 ae330000 ae140000
  //   2231fffc 1611fff8 102020 20020022 c 22100004 2011003c 1611fff2 2002000a c 20100000 22100001 102020
  //   20020022 c 22100002 102020 20020022 c 22100003 102020 20020022 c 22100004 102020 20020022 c 22100005
  //   102020 20020022 c 22100006 102020 20020022 c 22100007 102020 20020022 c 22100008 102020 20020022
  //   20020022 c 3e00008 241d0050 27bdfffc afb00000 27bdfffc afb10000 27bdfffc afa20000 27bdfffc afa40000
  //   409cf000 20100001 20110001 118f00 112020 20020022 c 118902 12200001 8000ce8 112020 20020022 c
  //   401cf000 201d0040 8fa40000 23bd0004 8fa20000 23bd0004 8fb10000 23bd0004 8fb00000 42000018 241d00a0
  //   27bdfffc afb00000 27bdfffc afb10000 27bdfffc afa20000 27bdfffc afa40000 409cf000 20100001 20110001
  //   118f40 112020 20020022 c 118902 12200001 8000d08 112020 20020022 c 401cf000 201d0090 8fa40000
  //   23bd0004 8fa20000 23bd0004 8fb10000 23bd0004 8fb00000 42000018 241d0140 27bdfffc afb00000 27bdfffc
  //   afb10000 27bdfffc afa20000 27bdfffc afa40000 409cf000 20100001 20110003 118f00 112020 20020022 c
  //   118902 12200001 8000d28 112020 20020022 c 401cf000 201d0130 8fa40000 23bd0004 8fa20000 23bd0004
  //   8fb10000 23bd0004 8fb00000 42000018
  //   数码管输出
  //   总复位信号应将除ROM以外所有存储组件全部清零
  //   寄存器文件
endmodule

module aluctr (
  input  [5:0] op,
  input  [5:0] func,
  output [1:0] rw,
  output [1:0] din,
  output A,
  output [1:0] B,
  output addr,
  output WE,
  output [2:0] pc,
  output W,
  output syscall,
  output [3:0] aluop,
  output rtype
);

  wire and_3_out, and_4_out, comparator_1_eq, jr, r, sll, WE_t;
  wire [1:0] b_t;
  wire [2:0] pc_t;
  wire [3:0] funcctr_1_alu1, opctr_1_alu1;

  and and_1 (A, sll, rtype);
  Comparator #(.width(6)) comparator_1 (.a(func), .b(6'b001100), .eq(comparator_1_eq));  // open: gt, lt
  Multiplexer #(.width(2), .enable("false")) multiplexer_1 (.in0(b_t), .in1(2'b01), .out(B), .sel(A));
  and and_2 (syscall, comparator_1_eq, rtype);
  Comparator #(.width(6)) comparator_2 (.a(op), .b({6{1'b0}}), .eq(rtype));  // open: gt, lt
  Multiplexer #(.width(3), .enable("false")) multiplexer_2 (.in0(pc_t), .in1(3'b010), .out(pc), .sel(and_3_out));
  and and_3 (and_3_out, jr, rtype);
  funcctr funcctr_1 (
    .func6(func[5]), .func5(func[4]), .func4(func[3]), .func3(func[2]), .func2(func[1]), .func1(func[0]),
    .alu4(funcctr_1_alu1[3]), .alu3(funcctr_1_alu1[2]), .alu2(funcctr_1_alu1[1]), .alu1(funcctr_1_alu1[0]),
    .sll(sll), .jr(jr), .r(r));
  opctr opctr_1 (
    .op6(op[5]), .op5(op[4]), .op4(op[3]), .op3(op[2]), .op2(op[1]), .op1(op[0]), .alu4(opctr_1_alu1[3]),
    .alu3(opctr_1_alu1[2]), .alu2(opctr_1_alu1[1]), .alu1(opctr_1_alu1[0]));
  we we_1 (
    .op6(op[5]), .op5(op[4]), .op4(op[3]), .op3(op[2]), .op2(op[1]), .op1(op[0]), .pc3(pc_t[2]),
    .pc2(pc_t[1]), .pc1(pc_t[0]), .rw2(rw[1]), .rw1(rw[0]), .din2(din[1]), .din1(din[0]), .b2(b_t[0]),
    .B(b_t[1]), .addr(addr), .w(WE_t), .rw(W));
  Multiplexer #(.enable("false")) multiplexer_3 (.in0(WE_t), .in1(1'b1), .out(WE), .sel(and_4_out));
  and and_4 (and_4_out, r, rtype);
  Multiplexer #(.width(4), .enable("false")) multiplexer_4 (
    .in0(opctr_1_alu1), .in1(funcctr_1_alu1), .out(aluop), .sel(rtype));
endmodule

module opctr (
  input  op6,
  input  op5,
  input  op4,
  input  op3,
  input  op2,
  input  op1,
  output alu4,
  output alu3,
  output alu2,
  output alu1
);

  wire and_1_out, and_2_out, and_3_out, and_4_out, and_5_out, and_6_out, and_7_out, and_8_out, and_9_out,
       and_10_out, and_11_out, and_12_out, and_13_out, and_14_out, and_15_out, not_1_out, not_2_out,
       not_3_out, not_4_out, not_5_out, not_6_out, not_7_out, not_8_out, not_9_out, not_10_out, not_11_out,
       not_12_out, not_13_out, not_14_out, not_15_out, not_16_out, not_17_out, not_18_out, not_19_out,
       not_20_out, not_21_out, not_22_out, not_23_out;

  not not_1 (not_1_out, op6);
  not not_2 (not_2_out, op5);
  not not_3 (not_3_out, op4);
  not not_4 (not_4_out, op6);
  not not_5 (not_5_out, op1);
  not not_6 (not_6_out, op2);
  not not_7 (not_7_out, op1);
  not not_8 (not_8_out, op3);
  not not_9 (not_9_out, op2);
  not not_10 (not_10_out, op3);
  not not_11 (not_11_out, op2);
  not not_12 (not_12_out, op5);
  not not_13 (not_13_out, op3);
  not not_14 (not_14_out, op5);
  not not_15 (not_15_out, op4);
  not not_16 (not_16_out, op3);
  not not_17 (not_17_out, op2);
  not not_18 (not_18_out, op2);
  not not_19 (not_19_out, op1);
  not not_20 (not_20_out, op2);
  not not_21 (not_21_out, op1);
  not not_22 (not_22_out, op3);
  not not_23 (not_23_out, op1);
  and and_1 (and_1_out, not_1_out, not_2_out, not_3_out, op1);
  and and_2 (and_2_out, not_4_out, op2);
  and and_3 (and_3_out, op2, not_5_out);
  and and_4 (and_4_out, op3, op1);
  and and_5 (and_5_out, op5, op2);
  and and_6 (and_6_out, not_6_out, not_7_out);
  and and_7 (and_7_out, op4, not_8_out, not_9_out);
  and and_8 (and_8_out, op5, not_10_out, not_11_out);
  and and_9 (and_9_out, op6, not_12_out, not_13_out, op1);
  and and_10 (and_10_out, not_14_out, not_15_out, not_16_out, not_17_out, op1);
  and and_11 (and_11_out, op3, not_18_out, not_19_out);
  and and_12 (and_12_out, op6, not_20_out);
  and and_13 (and_13_out, op6, not_21_out);
  and and_14 (and_14_out, op6, op3);
  and and_15 (and_15_out, op6, op5);
  or or_1 (alu1, not_22_out, not_23_out);
  or or_2 (alu4, and_1_out, and_2_out, and_3_out, and_4_out, and_5_out);
  or or_3 (alu3, and_6_out, and_7_out, and_8_out, and_9_out);
  or or_4 (alu2, and_10_out, and_11_out, and_12_out, and_13_out, and_14_out, and_15_out);
endmodule

module funcctr (
  input  func6,
  input  func5,
  input  func4,
  input  func3,
  input  func2,
  input  func1,
  output alu4,
  output alu3,
  output alu2,
  output alu1,
  output sll,
  output jr,
  output r
);

  wire and_1_out, and_2_out, and_3_out, and_4_out, and_5_out, and_6_out, and_7_out, and_8_out, and_9_out,
       and_10_out, and_11_out, and_12_out, and_13_out, and_14_out, and_15_out, and_16_out, and_17_out,
       and_18_out, and_20_out, and_21_out, and_22_out, and_23_out, and_24_out, not_1_out, not_2_out,
       not_3_out, not_4_out, not_5_out, not_6_out, not_7_out, not_8_out, not_9_out, not_10_out, not_11_out,
       not_12_out, not_13_out, not_14_out, not_15_out, not_16_out, not_17_out, not_18_out, not_19_out,
       not_20_out, not_21_out, not_22_out, not_23_out, not_24_out, not_25_out, not_26_out, not_27_out,
       not_28_out, not_29_out, not_30_out, not_31_out, not_32_out, not_33_out, not_34_out, not_35_out,
       not_36_out, not_37_out, not_38_out, not_39_out, not_40_out, not_41_out, not_42_out, not_43_out,
       not_44_out, not_45_out, not_46_out, not_47_out, not_48_out, not_49_out, not_50_out, not_51_out,
       not_52_out, not_53_out, not_54_out, not_55_out;

  and and_1 (and_1_out, func3, func1);
  and and_2 (and_2_out, func3, func2);
  not not_1 (not_1_out, func4);
  not not_2 (not_2_out, func3);
  not not_3 (not_3_out, func2);
  not not_4 (not_4_out, func1);
  not not_5 (not_5_out, func5);
  not not_6 (not_6_out, func4);
  not not_7 (not_7_out, func3);
  not not_8 (not_8_out, func1);
  not not_9 (not_9_out, func2);
  not not_10 (not_10_out, func1);
  not not_11 (not_11_out, func4);
  not not_12 (not_12_out, func4);
  not not_13 (not_13_out, func4);
  not not_14 (not_14_out, func3);
  not not_15 (not_15_out, func3);
  not not_16 (not_16_out, func1);
  not not_17 (not_17_out, func6);
  not not_18 (not_18_out, func5);
  not not_19 (not_19_out, func4);
  not not_20 (not_20_out, func3);
  not not_21 (not_21_out, func1);
  not not_22 (not_22_out, func1);
  not not_23 (not_23_out, func6);
  not not_24 (not_24_out, func1);
  not not_25 (not_25_out, func3);
  not not_26 (not_26_out, func2);
  not not_27 (not_27_out, func6);
  not not_28 (not_28_out, func5);
  not not_29 (not_29_out, func4);
  not not_30 (not_30_out, func3);
  not not_31 (not_31_out, func1);
  not not_32 (not_32_out, func6);
  not not_33 (not_33_out, func5);
  not not_34 (not_34_out, func4);
  not not_35 (not_35_out, func3);
  not not_36 (not_36_out, func6);
  not not_37 (not_37_out, func5);
  not not_38 (not_38_out, func3);
  not not_39 (not_39_out, func2);
  not not_40 (not_40_out, func1);
  not not_41 (not_41_out, func5);
  not not_42 (not_42_out, func4);
  not not_43 (not_43_out, func3);
  not not_44 (not_44_out, func1);
  not not_45 (not_45_out, func6);
  not not_46 (not_46_out, func5);
  not not_47 (not_47_out, func4);
  not not_48 (not_48_out, func3);
  not not_49 (not_49_out, func5);
  not not_50 (not_50_out, func4);
  not not_51 (not_51_out, func2);
  not not_52 (not_52_out, func5);
  not not_53 (not_53_out, func4);
  not not_54 (not_54_out, func5);
  not not_55 (not_55_out, func3);
  or or_1 (alu4, and_1_out, and_2_out, func4);
  and and_3 (and_3_out, func4, func1);
  and and_4 (and_4_out, func6, not_1_out, not_2_out);
  and and_5 (and_5_out, func6, not_3_out, not_4_out);
  and and_6 (and_6_out, not_5_out, not_6_out, not_7_out, func2, not_8_out);
  and and_7 (and_7_out, func3, not_9_out, not_10_out);
  and and_8 (and_8_out, not_11_out, func3, func2, func1);
  and and_9 (and_9_out, func5, not_12_out, func2, func1);
  and and_10 (and_10_out, func6, not_13_out, not_14_out, func2);
  and and_11 (and_11_out, func6, not_15_out, func2, not_16_out);
  and and_12 (and_12_out, not_17_out, not_18_out, not_19_out, not_20_out, func2, func1);
  and and_13 (and_13_out, func3, not_21_out);
  and and_14 (and_14_out, func4, not_22_out);
  and and_15 (and_15_out, not_23_out, func5, func2, not_24_out);
  and and_16 (and_16_out, func6, not_25_out, not_26_out);
  and and_17 (and_17_out, not_27_out, not_28_out, not_29_out, not_30_out, not_31_out);
  and and_18 (and_18_out, not_32_out, not_33_out, not_34_out, not_35_out, func2);
  and and_19 (jr, not_36_out, not_37_out, func4, not_38_out, not_39_out, not_40_out);
  and and_20 (and_20_out, not_41_out, not_42_out, not_43_out, not_44_out);
  and and_21 (and_21_out, not_45_out, not_46_out, not_47_out, not_48_out, func2);
  and and_22 (and_22_out, func6, not_49_out, not_50_out, not_51_out);
  and and_23 (and_23_out, func6, not_52_out, not_53_out, func3);
  and and_24 (and_24_out, func6, not_54_out, func4, not_55_out, func2);
  or or_2 (alu3, and_3_out, and_4_out, and_5_out);
  or or_3 (alu2, and_6_out, and_7_out, and_8_out, and_9_out, and_10_out, and_11_out);
  or or_4 (alu1, and_12_out, and_13_out, and_14_out, and_15_out, and_16_out);
  or or_5 (sll, and_17_out, and_18_out);
  or or_6 (r, and_20_out, and_21_out, and_22_out, and_23_out, and_24_out);
endmodule

module alu (
  input  [31:0] A,
  input  [31:0] B,
  input  [3:0] op,
  output [31:0] R,
  output les,
  output out_6
);

  ALU alu_1 (
    .AluOP(op), .X(A), .Equal(out_6), .Result(R), .Y(B));  // open: Signed_Overflow, Result_2, UnSigned_Overflow

  assign les = A[31];

  // Other names for the same wires on the sheet: aluop[3:0] = op
endmodule

module we (
  input  op6,
  input  op5,
  input  op4,
  input  op3,
  input  op2,
  input  op1,
  output pc3,
  output pc2,
  output pc1,
  output rw2,
  output rw1,
  output din2,
  output din1,
  output b2,
  output B,
  output addr,
  output w,
  output rw
);

  wire and_3_out, and_4_out, and_5_out, and_6_out, and_7_out, and_8_out, and_9_out, and_13_out, and_15_out,
       and_16_out, and_17_out, and_18_out, not_1_out, not_2_out, not_3_out, not_4_out, not_5_out, not_6_out,
       not_7_out, not_8_out, not_9_out, not_10_out, not_11_out, not_12_out, not_13_out, not_14_out,
       not_15_out, not_16_out, not_17_out, not_18_out, not_19_out, not_20_out, not_21_out, not_22_out,
       not_23_out, not_24_out, not_25_out, not_26_out, not_27_out, not_28_out, not_29_out, not_30_out,
       not_31_out, not_32_out, not_33_out, not_34_out, not_35_out, not_36_out, not_37_out, not_38_out,
       not_39_out, not_40_out, not_41_out, not_42_out, not_43_out, not_44_out, not_45_out, not_46_out,
       not_47_out, not_48_out;

  not not_1 (not_1_out, op6);
  not not_2 (not_2_out, op5);
  not not_3 (not_3_out, op4);
  not not_4 (not_4_out, op2);
  not not_5 (not_5_out, op6);
  not not_6 (not_6_out, op5);
  not not_7 (not_7_out, op4);
  not not_8 (not_8_out, op3);
  not not_9 (not_9_out, op6);
  not not_10 (not_10_out, op5);
  not not_11 (not_11_out, op4);
  not not_12 (not_12_out, op2);
  not not_13 (not_13_out, op6);
  not not_14 (not_14_out, op5);
  not not_15 (not_15_out, op4);
  not not_16 (not_16_out, op3);
  not not_17 (not_17_out, op6);
  not not_18 (not_18_out, op5);
  not not_19 (not_19_out, op3);
  not not_20 (not_20_out, op6);
  not not_21 (not_21_out, op5);
  not not_22 (not_22_out, op4);
  not not_23 (not_23_out, op3);
  not not_24 (not_24_out, op4);
  not not_25 (not_25_out, op6);
  not not_26 (not_26_out, op5);
  not not_27 (not_27_out, op4);
  not not_28 (not_28_out, op3);
  not not_29 (not_29_out, op2);
  not not_30 (not_30_out, op6);
  not not_31 (not_31_out, op5);
  not not_32 (not_32_out, op3);
  not not_33 (not_33_out, op5);
  not not_34 (not_34_out, op3);
  not not_35 (not_35_out, op5);
  not not_36 (not_36_out, op4);
  not not_37 (not_37_out, op3);
  not not_38 (not_38_out, op6);
  not not_39 (not_39_out, op5);
  not not_40 (not_40_out, op2);
  not not_41 (not_41_out, op6);
  not not_42 (not_42_out, op5);
  not not_43 (not_43_out, op1);
  not not_44 (not_44_out, op5);
  not not_45 (not_45_out, op3);
  not not_46 (not_46_out, op1);
  not not_47 (not_47_out, op5);
  not not_48 (not_48_out, op3);
  and and_1 (pc3, not_1_out, not_2_out, not_3_out, op3, not_4_out);
  and and_2 (pc2, not_5_out, not_6_out, not_7_out, not_8_out, op2);
  and and_3 (and_3_out, not_9_out, not_10_out, not_11_out, not_12_out, op1);
  and and_4 (and_4_out, not_13_out, not_14_out, not_15_out, not_16_out, op2);
  and and_5 (and_5_out, not_17_out, op2, op1);
  and and_6 (and_6_out, op3, op2, op1);
  and and_7 (and_7_out, op4, op2, op1);
  and and_8 (and_8_out, op5, op2, op1);
  and and_9 (and_9_out, op6, not_18_out, not_19_out, op2, op1);
  and and_10 (din2, not_20_out, not_21_out, not_22_out, not_23_out, op2);
  and and_11 (din1, op6, not_24_out);
  and and_12 (b2, not_25_out, not_26_out, not_27_out, not_28_out, not_29_out, op1);
  and and_13 (and_13_out, not_30_out, not_31_out, not_32_out, op1);
  and and_14 (addr, op6, not_33_out, op4, not_34_out, op2, op1);
  and and_15 (and_15_out, not_35_out, not_36_out, not_37_out, op2, op1);
  and and_16 (and_16_out, not_38_out, not_39_out, op4, not_40_out);
  and and_17 (and_17_out, not_41_out, not_42_out, op4, op3, not_43_out);
  and and_18 (and_18_out, op6, not_44_out, op4, not_45_out, op2, not_46_out);
  and and_19 (rw, op6, not_47_out, op4, not_48_out, op2, op1);
  or or_1 (pc1, and_3_out, and_4_out);
  or or_2 (rw2, and_5_out, and_6_out, and_7_out, and_8_out);
  or or_3 (rw1, op4, and_9_out);
  or or_4 (B, and_13_out, op2, op4);
  or or_5 (w, and_15_out, and_16_out, and_17_out, and_18_out);
endmodule

module npc (
  input  [9:0] pc,
  input  [25:0] addr,
  input  [2:0] p,
  input  [31:0] rs,
  input  [15:0] offset,
  input  less,
  input  equ,
  output [9:0] out,
  output [9:0] pc11
);

  wire not_1_out;
  wire [9:0] adder_1_out, adder_2_out, incrementer_1_p2, multiplexer_1_out, multiplexer_2_out,
       multiplexer_3_out, multiplexer_4_out, multiplexer_5_out;

  Multiplexer #(.width(10), .enable("false")) multiplexer_1 (
    .in0(10'h1), .in1(offset[9:0]), .out(multiplexer_1_out));  // open: sel
  Adder #(.width(10)) adder_1 (.a(pc), .b(offset[9:0]), .out(adder_1_out));  // open: cin, cout
  Adder #(.width(10)) adder_2 (.a(pc), .b(multiplexer_1_out), .out(adder_2_out));  // open: cin, cout
  // Incrementer incrementer_1: pin names not known; wires that end beside it: adder_1_out, incrementer_1_p2
  Multiplexer #(.width(10), .enable("false")) multiplexer_2 (
    .in0(pc11), .in1(incrementer_1_p2), .out(multiplexer_2_out), .sel(equ));
  Multiplexer #(.width(10), .enable("false")) multiplexer_3 (
    .in0(pc11), .in1(incrementer_1_p2), .out(multiplexer_3_out), .sel(not_1_out));
  not not_1 (not_1_out, equ);
  Multiplexer #(.width(10), .enable("false")) multiplexer_4 (
    .in0(rs[9:0]), .in1(addr[9:0]), .out(multiplexer_4_out));  // open: sel
  Multiplexer #(.width(10), .enable("false")) multiplexer_5 (
    .in0(pc11), .in1(adder_1_out), .out(multiplexer_5_out), .sel(less));
  Multiplexer #(.width(10), .enable("false")) multiplexer_6 (
    .in0(adder_2_out), .in1(multiplexer_4_out), .out(out));  // open: sel
  // Incrementer incrementer_2: pin names not known; wires that end beside it: pc, pc11
  Multiplexer #(.select(3), .width(10), .enable("false")) multiplexer_7 (
    .in0(pc11), .in1(multiplexer_5_out), .in2(rs[9:0]), .in3(addr[9:0]), .in4(multiplexer_2_out),
    .in5(multiplexer_3_out), .in6(pc11), .in7(pc11), .out(out), .sel(p));

  // Other names for the same wires on the sheet: p11[9:0] = pc11
endmodule

module \中断  (
  input  clk,
  input  ir1,
  input  ir2,
  input  ir3,
  input  eret,
  input  mtc0,
  input  mfc0,
  output [1:0] xy,
  output w1,
  output zhongduan,
  output w2,
  output w3
);

  wire and_1_out, and_2_out, and_3_out, and_4_out, and_5_out, and_6_out, and_7_out, and_8_out, and_9_out,
       and_13_out, and_14_out, and_15_out, d_ff_1_q, d_ff_2_q, d_ff_3_q, d_ff_7_q, d_ff_9_q, d_ff_10_q,
       d_ff_11_q, ie, Ir1_t, Ir2_t, Ir3_t, multiplexer_2_out, not_1_out, not_2_out, not_3_out, not_4_out,
       not_5_out, not_6_out, not_7_out, not_8_out, not_9_out, not_10_out, not_11_out, not_12_out, not_13_out,
       not_14_out, not_15_out, not_16_out, or_1_out, or_2_out, or_3_out, or_4_out, or_5_out, or_6_out,
       or_11_out, or_12_out, or_13_out, or_14_out, or_15_out, or_16_out, z1, z2, z3, zero1, zero2, zero3,
       zhongduan1, zhongduan2, zhongduan3;
  wire [1:0] multiplexer_1_out;

  not not_1 (not_1_out, w3);
  D_Flip_Flop d_ff_1 (.clk(ir1), .D(1'b1), .Q(d_ff_1_q), .reset(Ir1_t));  // open: Qn, preset, en
  and and_1 (and_1_out, zero1, not_2_out);
  not not_2 (not_2_out, w1);
  D_Flip_Flop d_ff_2 (.clk(ir2), .D(1'b1), .Q(d_ff_2_q), .reset(Ir2_t));  // open: Qn, preset, en
  not not_3 (not_3_out, w2);
  D_Flip_Flop d_ff_3 (.clk(ir3), .D(1'b1), .Q(d_ff_3_q), .reset(Ir3_t));  // open: Qn, preset, en
  and and_2 (and_2_out, zero3, not_1_out);
  or or_1 (or_1_out, d_ff_1_q, Ir1_t);
  not not_4 (not_4_out, and_1_out);
  or or_2 (or_2_out, d_ff_2_q, Ir2_t);
  not not_5 (not_5_out, and_3_out);
  and and_3 (and_3_out, zero2, not_3_out);
  or or_3 (or_3_out, d_ff_3_q, Ir3_t);
  not not_6 (not_6_out, and_2_out);
  Demultiplexer #(.select(2), .enable("false")) demultiplexer_1 (
    .out1(zero1), .out2(zero2), .out3(zero3), .in(1'b1), .sel(multiplexer_1_out));  // open: out0
  Multiplexer #(.width(2), .enable("false")) multiplexer_1 (.in0(2'b00), .in1(xy), .out(multiplexer_1_out), .sel(eret));
  and and_4 (and_4_out, or_1_out, not_4_out);
  and and_5 (and_5_out, or_2_out, not_5_out);
  and and_6 (and_6_out, or_3_out, not_6_out);
  D_Flip_Flop d_ff_4 (.clk(clk), .D(and_4_out), .Q(Ir1_t));  // open: Qn, preset, en, reset
  D_Flip_Flop d_ff_5 (.clk(clk), .D(and_5_out), .Q(Ir2_t));  // open: Qn, preset, en, reset
  D_Flip_Flop d_ff_6 (.clk(clk), .D(and_6_out), .Q(Ir3_t));  // open: Qn, preset, en, reset
  or or_4 (or_4_out, mfc0, zhongduan);
  not not_7 (not_7_out, ie);
  D_Flip_Flop d_ff_7 (.clk(or_4_out), .D(1'b1), .Q(d_ff_7_q), .reset(ie));  // open: Qn, preset, en
  or or_5 (or_5_out, d_ff_7_q, ie);
  Priority_Encoder #(.select(2)) priority_encoder_1 (
    .in0(1'b1), .in1(Ir1_t), .in2(Ir2_t), .in3(Ir3_t), .out(xy), .en_in(not_7_out));  // open: gs, en_out
  and and_7 (and_7_out, zhongduan1, z1);
  and and_8 (and_8_out, zhongduan2, z2);
  and and_9 (and_9_out, zhongduan3, z3);
  Multiplexer #(.enable("false")) multiplexer_2 (.in0(or_5_out), .in1(1'b0), .out(multiplexer_2_out), .sel(or_6_out));
  or or_6 (or_6_out, eret, mtc0);
  not not_8 (not_8_out, Ir3_t);
  not not_9 (not_9_out, Ir2_t);
  not not_10 (not_10_out, Ir3_t);
  or or_7 (zhongduan, and_7_out, and_8_out, and_9_out);
  D_Flip_Flop d_ff_8 (.clk(clk), .D(multiplexer_2_out), .Q(ie));  // open: Qn, preset, en, reset
  and and_10 (zhongduan1, Ir1_t, not_8_out, not_9_out, not_7_out);
  and and_11 (zhongduan2, Ir2_t, not_10_out, not_7_out);
  and and_12 (zhongduan3, Ir3_t, not_7_out);
  or or_8 (w2, d_ff_11_q, z2);
  D_Flip_Flop d_ff_9 (.clk(ir1), .D(1'b1), .Q(d_ff_9_q), .reset(z1));  // open: Qn, preset, en
  or or_9 (w1, d_ff_9_q, z1);
  D_Flip_Flop d_ff_10 (.clk(ir3), .D(1'b1), .Q(d_ff_10_q), .reset(z3));  // open: Qn, preset, en
  or or_10 (w3, d_ff_10_q, z3);
  not not_11 (not_11_out, zhongduan1);
  not not_12 (not_12_out, zhongduan2);
  D_Flip_Flop d_ff_11 (.clk(ir2), .D(1'b1), .Q(d_ff_11_q), .reset(z2));  // open: Qn, preset, en
  not not_13 (not_13_out, zhongduan3);
  or or_11 (or_11_out, not_11_out, zhongduan);
  or or_12 (or_12_out, d_ff_9_q, z1);
  and and_13 (and_13_out, or_12_out, not_14_out);
  not not_14 (not_14_out, zhongduan);
  or or_13 (or_13_out, not_12_out, zhongduan);
  or or_14 (or_14_out, d_ff_11_q, z2);
  and and_14 (and_14_out, or_14_out, not_15_out);
  not not_15 (not_15_out, zhongduan);
  or or_15 (or_15_out, not_13_out, zhongduan);
  or or_16 (or_16_out, d_ff_10_q, z3);
  and and_15 (and_15_out, or_16_out, not_16_out);
  not not_16 (not_16_out, zhongduan);
  D_Flip_Flop d_ff_12 (.clk(clk), .D(and_13_out), .Q(z1), .en(or_11_out));  // open: Qn, preset, reset
  D_Flip_Flop d_ff_13 (.clk(clk), .D(and_14_out), .Q(z2), .en(or_13_out));  // open: Qn, preset, reset
  D_Flip_Flop d_ff_14 (.clk(clk), .D(and_15_out), .Q(z3), .en(or_15_out));  // open: Qn, preset, reset

  // Other names for the same wires on the sheet: zd = zhongduan
endmodule
