// Logisim project 气泡流水线.circ as structural Verilog: 14 circuits, main circuit cpu
module cpu (
);

  wire and_1_out, and_2_out, and_3_out, and_4_out, clk, comparator_1_eq, comparator_2_eq, comparator_3_eq,
       comparator_4_eq, comparator_5_eq, comparator_6_eq, CONTROL_a, CONTROL_syscall, CONTROL_w, CONTROL_we,
       eq, ex_mem_1_selout, ex_mem_1_sysout, \ex_mem_1_传输状态out , halt, id_ex_1_aout, id_ex_1_sysout,
       id_ex_1_wout, \id_ex_1_传输状态out , \if_id_1_传输状态out , IR1, IR2, IR3, le, multiplexer_5_out,
       multiplexer_14_out, multiplexer_16_out, multiplexer_17_out, not_1_out, not_2_out, not_3_out,
       not_4_out, not_5_out, or_1_out, or_3_out, or_4_out, or_5_out, or_6_out, or_7_out, pipajump, qipao,
       qipao2, qipaoall, qipaodelay, RST, sys, W1, W2, W3, we, we2, wee;
  wire [1:0] CONTROL_b, CONTROL_din, CONTROL_rw, din, ex_mem_1_dinout, id_ex_1_bout, id_ex_1_dinout;
  wire [2:0] CONTROL_pc, jump;
  wire [3:0] CONTROL_aluop, id_ex_1_aluopout;
  wire [4:0] multiplexer_10_out, raa, rbb, rw, rw2, rww;
  wire [9:0] ex_mem_1_pcout_2, id_ex_1_pcout, if_id_1_pcout, incrementer_3_p2, mem_wb_1_pcout,
       multiplexer_1_out, multiplexer_2_out, npc_1_pc11, PC_q, pcp1;
  wire [15:0] adder_1_out, incrementer_1_p2, incrementer_2_p2, incrementer_4_p2, incrementer_5_p2,
       incrementer_6_p2, \load_use次数 , multiplexer_3_out, multiplexer_4_out, multiplexer_8_out,
       multiplexer_11_out, multiplexer_15_out, \总周期数 , \插入气泡 , \插入气泡delay , \插入气泡数 , \无条件分支指令数 , \有条件分支成功跳转 ;
  wire [31:0] a0, ALU_r, aluout, bit_extender_1_out, bit_extender_2_out, bit_extender_3_out,
       ex_mem_1_addrout, ex_mem_1_dataout, ex_mem_1_pcout, ex_mem_1_v0out, id_ex_1_a_3, id_ex_1_b_3,
       id_ex_1_immeout, mips_ram_1_p8, multiplexer_9_out, multiplexer_12_out, multiplexer_13_out, opp, pcrw,
       ramout, regfile_1_a, regfile_1_b, rom_1_data, SyscallOut, v0;

  Button \u_总复位  (.out(RST));
  Button _1 (.out(IR1));
  Button _2 (.out(IR2));
  Button _3 (.out(IR3));
  LED led_1 (.in(W1));
  LED led_2 (.in(W2));
  LED led_3 (.in(W3));
  Multiplexer #(.width(10), .enable("false")) multiplexer_1 (
    .in0(multiplexer_2_out), .in1(pcp1), .out(multiplexer_1_out), .sel(pipajump));
  pipaine pipaine_1 (
    .ra(raa), .rb(rbb), .op(opp), .rw(rww), .we(wee), .insert(qipao), .rw2(rw2), .we2(we2),
    .insert2(qipaodelay));
  Hex_Digit_Display hex_digit_display_1 (.value(SyscallOut[31:28]));  // open: dp
  Multiplexer #(.width(10), .enable("false")) multiplexer_2 (
    .in0(incrementer_3_p2), .in1(PC_q), .out(multiplexer_2_out), .sel(qipaoall));
  Register #(.width(10)) PC (.D(multiplexer_1_out), .en(not_1_out), .Q(PC_q), .clk(clk), .clr(RST));
  not not_1 (not_1_out, halt);
  // Incrementer incrementer_1: pin names not known; wires that end beside it: \插入气泡 , incrementer_1_p2
  Hex_Digit_Display hex_digit_display_2 (.value(SyscallOut[23:20]));  // open: dp
  Hex_Digit_Display hex_digit_display_3 (.value(SyscallOut[27:24]));  // open: dp
  jump jump_1 (.jump(jump), .eq(eq), .le(le), .jumpctr(pipajump));
  // Incrementer incrementer_2: pin names not known; wires that end beside it: \插入气泡delay , incrementer_2_p2
  Multiplexer #(.width(16), .enable("false")) multiplexer_3 (
    .in0(\插入气泡delay ), .in1(incrementer_2_p2), .out(multiplexer_3_out), .sel(qipaodelay));
  Multiplexer #(.width(16), .enable("false")) multiplexer_4 (
    .in0(\插入气泡 ), .in1(incrementer_1_p2), .out(multiplexer_4_out), .sel(qipao));
  Hex_Digit_Display hex_digit_display_4 (.value(SyscallOut[15:12]));  // open: dp
  Hex_Digit_Display hex_digit_display_5 (.value(SyscallOut[19:16]));  // open: dp
  // Incrementer incrementer_3: pin names not known; wires that end beside it: PC_q, incrementer_3_p2
  Hex_Digit_Display hex_digit_display_6 (.value(SyscallOut[11:8]));  // open: dp
  Hex_Digit_Display hex_digit_display_7 (.value(SyscallOut[7:4]));  // open: dp
  ROM #(.addrWidth(10), .dataWidth(32)) rom_1 (.addr(PC_q), .data(rom_1_data));  // open: sel
  Multiplexer #(.enable("false")) multiplexer_5 (.in0(1'b1), .in1(1'b0), .out(multiplexer_5_out), .sel(qipaoall));
  Register #(.width(16)) register_1 (.D(multiplexer_3_out), .Q(\插入气泡delay ), .clk(clk), .clr(RST));  // open: en
  Register #(.width(16)) register_2 (.D(multiplexer_4_out), .Q(\插入气泡 ), .clk(clk), .clr(RST));  // open: en
  Hex_Digit_Display hex_digit_display_8 (.value(SyscallOut[3:0]));  // open: dp
  Clock clock_1 (.out(clk));
  or or_1 (or_1_out, pipajump, or_7_out);
  if_id if_id_1 (
    .pc(PC_q), .pcout(if_id_1_pcout), .\传输状态In (multiplexer_5_out), .\传输状态Out (\if_id_1_传输状态out ), .CLK(clk),
    .\同步清零 (or_1_out), .instrucion(rom_1_data), .insout(opp));
  // Probe on opp
  // Probe on \插入气泡delay 
  // Probe on \插入气泡 
  // Probe on if_id_1_pcout
  // Probe on \总周期数 
  // Probe on \无条件分支指令数 
  // Probe on \有条件分支成功跳转 
  // Probe on \load_use次数 
  // Probe on \插入气泡数 
  aluctr CONTROL (
    .op(opp[31:26]), .func(opp[5:0]), .rw(CONTROL_rw), .din(CONTROL_din), .A(CONTROL_a), .B(CONTROL_b),
    .WE(CONTROL_we), .pc(CONTROL_pc), .W(CONTROL_w), .syscall(CONTROL_syscall), .aluop(CONTROL_aluop));  // open: addr
  or or_2 (qipaoall, qipao, qipaodelay);
  // Incrementer incrementer_4: pin names not known; wires that end beside it: \插入气泡数 , incrementer_4_p2
  // Probe on CONTROL_we
  // Probe on CONTROL_syscall
  Multiplexer #(.width(5), .enable("false")) multiplexer_6 (
    .in0(opp[25:21]), .in1(5'b00010), .out(raa), .sel(CONTROL_syscall));
  Multiplexer #(.width(5), .enable("false")) multiplexer_7 (
    .in0(opp[20:16]), .in1(5'b00100), .out(rbb), .sel(CONTROL_syscall));
  Multiplexer #(.width(16), .enable("false")) multiplexer_8 (
    .in0(\插入气泡数 ), .in1(incrementer_4_p2), .out(multiplexer_8_out), .sel(or_3_out));
  or or_3 (or_3_out, qipao, qipaodelay);
  Multiplexer #(.select(2), .width(32), .enable("false")) multiplexer_9 (
    .in0(aluout), .in1(ramout), .in2(pcrw), .in3({32{1'b0}}), .out(multiplexer_9_out), .sel(din));
  Register #(.width(1)) register_3 (.D(qipao), .Q(qipao2), .clk(clk));  // open: en, clr
  Multiplexer #(.select(2), .width(5), .enable("false")) multiplexer_10 (
    .in0(opp[15:11]), .in1(opp[20:16]), .in2({5{1'b1}}), .in3(5'b11100), .out(multiplexer_10_out),
    .sel(CONTROL_rw));
  // Probe on CONTROL_aluop
  regfile regfile_1 (
    .clk(clk), .we(we), .rw(rw), .ra(raa), .rb(rbb), .w(multiplexer_9_out), .a(regfile_1_a), .b(regfile_1_b));
  Register #(.width(16)) register_4 (.D(multiplexer_8_out), .Q(\插入气泡数 ), .clk(clk), .clr(RST));  // open: en
  Comparator #(.width(3)) comparator_1 (.a(jump), .b(3'b001), .eq(comparator_1_eq));  // open: gt, lt
  Comparator #(.width(3)) comparator_2 (.a(jump), .b(3'b100), .eq(comparator_2_eq));  // open: gt, lt
  Comparator #(.width(3)) comparator_3 (.a(jump), .b(3'b101), .eq(comparator_3_eq));  // open: gt, lt
  not not_2 (not_2_out, halt);
  // Incrementer incrementer_5: pin names not known; wires that end beside it: \有条件分支成功跳转 , incrementer_5_p2
  and and_1 (and_1_out, comparator_1_eq, le);
  and and_2 (and_2_out, comparator_2_eq, eq);
  and and_3 (and_3_out, comparator_3_eq, not_3_out);
  not not_3 (not_3_out, eq);
  Register #(.width(16)) register_5 (.D(adder_1_out), .en(not_2_out), .Q(\总周期数 ), .clk(clk), .clr(RST));
  // Probe on \总周期数 
  or or_4 (or_4_out, pipajump, qipaodelay, qipao, or_7_out);
  id_ex id_ex_1 (
    .\传输状态In (\if_id_1_传输状态out ), .CLK(clk), .a_3(id_ex_1_a_3), .\传输状态Out (\id_ex_1_传输状态out ),
    .\同步清零 (or_4_out), .a(regfile_1_a), .b(regfile_1_b), .b_3(id_ex_1_b_3), .aluop(CONTROL_aluop),
    .aluopout(id_ex_1_aluopout), .imme(opp), .immeout(id_ex_1_immeout), .pc(if_id_1_pcout),
    .pcout(id_ex_1_pcout), .W(CONTROL_w), .Wout(id_ex_1_wout), .We(CONTROL_we), .Weout(wee),
    .sys(CONTROL_syscall), .sysout(id_ex_1_sysout), .A_2(CONTROL_a), .Aout(id_ex_1_aout), .B_2(CONTROL_b),
    .Bout(id_ex_1_bout), .din(CONTROL_din), .pcctr(CONTROL_pc), .pcctrout(jump), .dinout(id_ex_1_dinout),
    .rw(multiplexer_10_out), .rwout(rww));
  Multiplexer #(.width(16), .enable("false")) multiplexer_11 (
    .in0(\有条件分支成功跳转 ), .in1(incrementer_5_p2), .out(multiplexer_11_out), .sel(or_5_out));
  or or_5 (or_5_out, and_1_out, and_2_out, and_3_out);
  Adder #(.width(16)) adder_1 (.a(\总周期数 ), .b(16'h1), .out(adder_1_out));  // open: cin, cout
  // Probe on id_ex_1_immeout
  Counter #(.width(16), .max('hffff)) counter_1 (
    .load(1'b1), .D(multiplexer_11_out), .count(1'b0), .Q(\有条件分支成功跳转 ), .clk(clk), .clr(RST));  // open: carry
  assign bit_extender_1_out = {{27{id_ex_1_immeout[10]}}, id_ex_1_immeout[10:6]};  // Bit_Extender bit_extender_1
  assign bit_extender_2_out = {{16{id_ex_1_immeout[15]}}, id_ex_1_immeout[15:0]};  // Bit_Extender bit_extender_2
  // Probe on id_ex_1_pcout
  Multiplexer #(.select(2), .width(32), .enable("false")) multiplexer_12 (
    .in0(id_ex_1_b_3), .in1(bit_extender_1_out), .in2(bit_extender_2_out), .in3({32{1'b0}}),
    .out(multiplexer_12_out), .sel(id_ex_1_bout));
  Multiplexer #(.width(32), .enable("false")) multiplexer_13 (
    .in0(id_ex_1_a_3), .in1(id_ex_1_b_3), .out(multiplexer_13_out), .sel(id_ex_1_aout));
  npc npc_1 (
    .pc(id_ex_1_pcout), .addr(id_ex_1_immeout[25:0]), .p(jump), .rs(id_ex_1_a_3),
    .offset(id_ex_1_immeout[15:0]), .less(le), .equ(eq), .out(pcp1), .pc11(npc_1_pc11));
  alu ALU (.A(multiplexer_13_out), .B(multiplexer_12_out), .op(id_ex_1_aluopout), .R(ALU_r), .out_6(eq), .les(le));
  Multiplexer #(.enable("false")) multiplexer_14 (
    .in0(\id_ex_1_传输状态out ), .in1(1'b1), .out(multiplexer_14_out), .sel(qipaodelay));
  ex_mem ex_mem_1 (
    .addr(ALU_r), .addrout(ex_mem_1_addrout), .data(id_ex_1_b_3), .dataout(ex_mem_1_dataout),
    .\传输状态In (multiplexer_14_out), .\传输状态Out (\ex_mem_1_传输状态out ), .CLK(clk), .\同步清零 (or_7_out),
    .sel(id_ex_1_wout), .selout(ex_mem_1_selout), .we(wee), .weout(we2), .sys(id_ex_1_sysout),
    .sysout(ex_mem_1_sysout), .v0(id_ex_1_a_3), .v0out(ex_mem_1_v0out), .rw(rww), .rwout(rw2),
    .din(id_ex_1_dinout), .dinout(ex_mem_1_dinout), .pc(bit_extender_3_out), .pcout(ex_mem_1_pcout),
    .pcins(id_ex_1_pcout), .pcout_2(ex_mem_1_pcout_2));
  assign bit_extender_3_out = {{22{1'b0}}, npc_1_pc11};  // Bit_Extender bit_extender_3
  // Probe on ex_mem_1_pcout_2
  // Incrementer incrementer_6: pin names not known; wires that end beside it: \无条件分支指令数 , incrementer_6_p2
  Comparator #(.width(3)) comparator_4 (.a(jump), .b(3'b010), .eq(comparator_4_eq));  // open: gt, lt
  or or_6 (or_6_out, comparator_4_eq, comparator_5_eq);
  Comparator #(.width(3)) comparator_5 (.a(jump), .b(3'b011), .eq(comparator_5_eq));  // open: gt, lt
  Multiplexer #(.width(16), .enable("false")) multiplexer_15 (
    .in0(\无条件分支指令数 ), .in1(incrementer_6_p2), .out(multiplexer_15_out), .sel(or_6_out));
  Counter #(.width(16), .max('hffff)) counter_2 (
    .load(1'b1), .D(multiplexer_15_out), .count(1'b0), .Q(\无条件分支指令数 ), .clk(clk), .clr(RST));  // open: carry
  // MIPS_RAM mips_ram_1: pin names not known; wires that end beside it: ex_mem_1_addrout[13:2], ex_mem_1_dataout, ex_mem_1_selout, 4'b1111, clk, 1'b1, RST, mips_ram_1_p8
  Multiplexer #(.enable("false")) multiplexer_16 (
    .in0(\ex_mem_1_传输状态out ), .in1(1'b0), .out(multiplexer_16_out), .sel(halt));
  or or_7 (or_7_out, halt, RST);
  mem_wb mem_wb_1 (
    .instrucion(ex_mem_1_pcout), .insout(pcrw), .sys(ex_mem_1_sysout), .sysout(sys),
    .\传输状态In (multiplexer_16_out), .CLK(clk), .\同步清零 (or_7_out), .we(we2), .weout(we), .data(mips_ram_1_p8),
    .dataout(ramout), .alu(ex_mem_1_addrout), .aluout(aluout), .v0out(v0), .v0(ex_mem_1_v0out),
    .a0(ex_mem_1_dataout), .a0out(a0), .rw(rw2), .rwout(rw), .din(ex_mem_1_dinout), .dinout(din),
    .pc(ex_mem_1_pcout_2), .pcout(mem_wb_1_pcout));  // open: 传输状态Out
  // Probe on mem_wb_1_pcout
  Comparator #(.width(32)) comparator_6 (.a(v0), .b(32'ha), .eq(comparator_6_eq));  // open: gt, lt
  Multiplexer #(.enable("false")) multiplexer_17 (
    .in0(1'b0), .in1(comparator_6_eq), .out(multiplexer_17_out), .sel(sys));
  not not_4 (not_4_out, halt);
  Register #(.width(1)) register_6 (.D(multiplexer_17_out), .en(not_4_out), .Q(halt), .clk(clk), .clr(RST));
  not not_5 (not_5_out, multiplexer_17_out);
  and and_4 (and_4_out, not_5_out, sys);
  Register #(.width(32)) register_7 (.D(a0), .en(and_4_out), .Q(SyscallOut), .clk(clk), .clr(RST));

  // Notes on the sheet:
  //   中断源
  //   中断等待指示
  //   指令存储器
  //   数码管输出
  //   contents of rom_1 (hex, n*v repeats v):
  //   20110001 8000c05 20110001 20120002 20130003 8000c09 20110001 20120002 20130003 8000c0d 20110001
  //   20120002 20130003 8000c11 20110001 20120002 20130003 c000cb8 20100001 20110001 118fc0 112020
  //   20020022 c 118882 12200001 8000c15 112020 20020022 c 20110001 118880 112020 20020022 c 12200001
  //   8000c1f 20110001 118fc0 112020 20020022 c 1188c3 112020 20020022 c 118903 112020 20020022 c 118903
  //   112020 20020022 c 118903 112020 20020022 c 118903 112020 20020022 c 118903 112020 20020022 c 118903
  //   112020 20020022 c 118903 112020 20020022 c 20100001 109fc0 139fc3 8021 2012000c 24160003 26100001
  //   3210000f 20080008 20090001 139900 2709825 132020 20020022 c 1094022 1500fff9 22100001 2018000f
  //   2188024 108700 20080008 20090001 139902 2709825 132021 20020022 c 1094022 1500fff9 108702 2c9b022
  //   12c00001 8000c50 4020 1084027 84400 3508ffff 82021 20020022 c 2010ffff 20110000 ae300000 22100001
  //   22310004 ae300000 22100001 22310004 ae300000 22100001 22310004 ae300000 22100001 22310004 ae300000
  //   22100001 22310004 ae300000 22100001 22310004 ae300000 22100001 22310004 ae300000 22100001 22310004
  //   ae300000 22100001 22310004 ae300000 22100001 22310004 ae300000 22100001 22310004 ae300000 22100001
  //   22310004 ae300000 22100001 22310004 ae300000 22100001 22310004 ae300000 22100001 22310004 ae300000
  //   22100001 22310004 22100001 8020 2011003c 8e130000 8e340000 274402a 11000002 ae330000 ae140000
  //   2231fffc 1611fff8 102020 20020022 c 22100004 2011003c 1611fff2 2002000a c 20100000 22100001 102020
  //   20020022 c 22100002 102020 20020022 c 22100003 102020 20020022 c 22100004 102020 20020022 c 22100005
  //   102020 20020022 c 22100006 102020 20020022 c 22100007 102020 20020022 c 22100008 102020 20020022
  //   20020022 c 3e00008
  //   寄存器文件
endmodule

module aluctr (
  input  [5:0] op,
  input  [5:0] func,
  output [1:0] rw,
  output [1:0] din,
  output A,
  output [1:0] B,
  output addr,
  output WE,
  output [2:0] pc,
  output W,
  output syscall,
  output [3:0] aluop
);

  wire and_3_out, and_4_out, comparator_1_eq, jr, r, rtype, sll, WE_t;
  wire [1:0] b_t;
  wire [2:0] pc_t;
  wire [3:0] funcctr_1_alu1, opctr_1_alu1;

  and and_1 (A, sll, rtype);
  Comparator #(.width(6)) comparator_1 (.a(func), .b(6'b001100), .eq(comparator_1_eq));  // open: gt, lt
  Multiplexer #(.width(2), .enable("false")) multiplexer_1 (.in0(b_t), .in1(2'b01), .out(B), .sel(A));
  and and_2 (syscall, comparator_1_eq, rtype);
  Comparator #(.width(6)) comparator_2 (.a(op), .b({6{1'b0}}), .eq(rtype));  // open: gt, lt
  Multiplexer #(.width(3), .enable("false")) multiplexer_2 (.in0(pc_t), .in1(3'b010), .out(pc), .sel(and_3_out));
  and and_3 (and_3_out, jr, rtype);
  funcctr funcctr_1 (
    .func6(func[5]), .func5(func[4]), .func4(func[3]), .func3(func[2]), .func2(func[1]), .func1(func[0]),
    .alu4(funcctr_1_alu1[3]), .alu3(funcctr_1_alu1[2]), .alu2(funcctr_1_alu1[1]), .alu1(funcctr_1_alu1[0]),
    .sll(sll), .jr(jr), .r(r));
  opctr opctr_1 (
    .op6(op[5]), .op5(op[4]), .op4(op[3]), .op3(op[2]), .op2(op[1]), .op1(op[0]), .alu4(opctr_1_alu1[3]),
    .alu3(opctr_1_alu1[2]), .alu2(opctr_1_alu1[1]), .alu1(opctr_1_alu1[0]));
  we we_1 (
    .op6(op[5]), .op5(op[4]), .op4(op[3]), .op3(op[2]), .op2(op[1]), .op1(op[0]), .pc3(pc_t[2]),
    .pc2(pc_t[1]), .pc1(pc_t[0]), .rw2(rw[1]), .rw1(rw[0]), .din2(din[1]), .din1(din[0]), .b2(b_t[0]),
    .B(b_t[1]), .addr(addr), .w(WE_t), .rw(W));
  Multiplexer #(.enable("false")) multiplexer_3 (.in0(WE_t), .in1(1'b1), .out(WE), .sel(and_4_out));
  and and_4 (and_4_out, r, rtype);
  Multiplexer #(.width(4), .enable("false")) multiplexer_4 (
    .in0(opctr_1_alu1), .in1(funcctr_1_alu1), .out(aluop), .sel(rtype));
endmodule

module opctr (
  input  op6,
  input  op5,
  input  op4,
  input  op3,
  input  op2,
  input  op1,
  output alu4,
  output alu3,
  output alu2,
  output alu1
);

  wire and_1_out, and_2_out, and_3_out, and_4_out, and_5_out, and_6_out, and_7_out, and_8_out, and_9_out,
       and_10_out, and_11_out, and_12_out, and_13_out, and_14_out, and_15_out, not_1_out, not_2_out,
       not_3_out, not_4_out, not_5_out, not_6_out, not_7_out, not_8_out, not_9_out, not_10_out, not_11_out,
       not_12_out, not_13_out, not_14_out, not_15_out, not_16_out, not_17_out, not_18_out, not_19_out,
       not_20_out, not_21_out, not_22_out, not_23_out;

  not not_1 (not_1_out, op6);
  not not_2 (not_2_out, op5);
  not not_3 (not_3_out, op4);
  not not_4 (not_4_out, op6);
  not not_5 (not_5_out, op1);
  not not_6 (not_6_out, op2);
  not not_7 (not_7_out, op1);
  not not_8 (not_8_out, op3);
  not not_9 (not_9_out, op2);
  not not_10 (not_10_out, op3);
  not not_11 (not_11_out, op2);
  not not_12 (not_12_out, op5);
  not not_13 (not_13_out, op3);
  not not_14 (not_14_out, op5);
  not not_15 (not_15_out, op4);
  not not_16 (not_16_out, op3);
  not not_17 (not_17_out, op2);
  not not_18 (not_18_out, op2);
  not not_19 (not_19_out, op1);
  not not_20 (not_20_out, op2);
  not not_21 (not_21_out, op1);
  not not_22 (not_22_out, op3);
  not not_23 (not_23_out, op1);
  and and_1 (and_1_out, not_1_out, not_2_out, not_3_out, op1);
  and and_2 (and_2_out, not_4_out, op2);
  and and_3 (and_3_out, op2, not_5_out);
  and and_4 (and_4_out, op3, op1);
  and and_5 (and_5_out, op5, op2);
  and and_6 (and_6_out, not_6_out, not_7_out);
  and and_7 (and_7_out, op4, not_8_out, not_9_out);
  and and_8 (and_8_out, op5, not_10_out, not_11_out);
  and and_9 (and_9_out, op6, not_12_out, not_13_out, op1);
  and and_10 (and_10_out, not_14_out, not_15_out, not_16_out, not_17_out, op1);
  and and_11 (and_11_out, op3, not_18_out, not_19_out);
  and and_12 (and_12_out, op6, not_20_out);
  and and_13 (and_13_out, op6, not_21_out);
  and and_14 (and_14_out, op6, op3);
  and and_15 (and_15_out, op6, op5);
  or or_1 (alu1, not_22_out, not_23_out);
  or or_2 (alu4, and_1_out, and_2_out, and_3_out, and_4_out, and_5_out);
  or or_3 (alu3, and_6_out, and_7_out, and_8_out, and_9_out);
  or or_4 (alu2, and_10_out, and_11_out, and_12_out, and_13_out, and_14_out, and_15_out);
endmodule

module funcctr (
  input  func6,
  input  func5,
  input  func4,
  input  func3,
  input  func2,
  input  func1,
  output alu4,
  output alu3,
  output alu2,
  output alu1,
  output sll,
  output jr,
  output r
);

  wire and_1_out, and_2_out, and_3_out, and_4_out, and_5_out, and_6_out, and_7_out, and_8_out, and_9_out,
       and_10_out, and_11_out, and_12_out, and_13_out, and_14_out, and_15_out, and_16_out, and_17_out,
       and_18_out, and_20_out, and_21_out, and_22_out, and_23_out, and_24_out, not_1_out, not_2_out,
       not_3_out, not_4_out, not_5_out, not_6_out, not_7_out, not_8_out, not_9_out, not_10_out, not_11_out,
       not_12_out, not_13_out, not_14_out, not_15_out, not_16_out, not_17_out, not_18_out, not_19_out,
       not_20_out, not_21_out, not_22_out, not_23_out, not_24_out, not_25_out, not_26_out, not_27_out,
       not_28_out, not_29_out, not_30_out, not_31_out, not_32_out, not_33_out, not_34_out, not_35_out,
       not_36_out, not_37_out, not_38_out, not_39_out, not_40_out, not_41_out, not_42_out, not_43_out,
       not_44_out, not_45_out, not_46_out, not_47_out, not_48_out, not_49_out, not_50_out, not_51_out,
       not_52_out, not_53_out, not_54_out, not_55_out;

  and and_1 (and_1_out, func3, func1);
  and and_2 (and_2_out, func3, func2);
  not not_1 (not_1_out, func4);
  not not_2 (not_2_out, func3);
  not not_3 (not_3_out, func2);
  not not_4 (not_4_out, func1);
  not not_5 (not_5_out, func5);
  not not_6 (not_6_out, func4);
  not not_7 (not_7_out, func3);
  not not_8 (not_8_out, func1);
  not not_9 (not_9_out, func2);
  not not_10 (not_10_out, func1);
  not not_11 (not_11_out, func4);
  not not_12 (not_12_out, func4);
  not not_13 (not_13_out, func4);
  not not_14 (not_14_out, func3);
  not not_15 (not_15_out, func3);
  not not_16 (not_16_out, func1);
  not not_17 (not_17_out, func6);
  not not_18 (not_18_out, func5);
  not not_19 (not_19_out, func4);
  not not_20 (not_20_out, func3);
  not not_21 (not_21_out, func1);
  not not_22 (not_22_out, func1);
  not not_23 (not_23_out, func6);
  not not_24 (not_24_out, func1);
  not not_25 (not_25_out, func3);
  not not_26 (not_26_out, func2);
  not not_27 (not_27_out, func6);
  not not_28 (not_28_out, func5);
  not not_29 (not_29_out, func4);
  not not_30 (not_30_out, func3);
  not not_31 (not_31_out, func1);
  not not_32 (not_32_out, func6);
  not not_33 (not_33_out, func5);
  not not_34 (not_34_out, func4);
  not not_35 (not_35_out, func3);
  not not_36 (not_36_out, func6);
  not not_37 (not_37_out, func5);
  not not_38 (not_38_out, func3);
  not not_39 (not_39_out, func2);
  not not_40 (not_40_out, func1);
  not not_41 (not_41_out, func5);
  not not_42 (not_42_out, func4);
  not not_43 (not_43_out, func3);
  not not_44 (not_44_out, func1);
  not not_45 (not_45_out, func6);
  not not_46 (not_46_out, func5);
  not not_47 (not_47_out, func4);
  not not_48 (not_48_out, func3);
  not not_49 (not_49_out, func5);
  not not_50 (not_50_out, func4);
  not not_51 (not_51_out, func2);
  not not_52 (not_52_out, func5);
  not not_53 (not_53_out, func4);
  not not_54 (not_54_out, func5);
  not not_55 (not_55_out, func3);
  or or_1 (alu4, and_1_out, and_2_out, func4);
  and and_3 (and_3_out, func4, func1);
  and and_4 (and_4_out, func6, not_1_out, not_2_out);
  and and_5 (and_5_out, func6, not_3_out, not_4_out);
  and and_6 (and_6_out, not_5_out, not_6_out, not_7_out, func2, not_8_out);
  and and_7 (and_7_out, func3, not_9_out, not_10_out);
  and and_8 (and_8_out, not_11_out, func3, func2, func1);
  and and_9 (and_9_out, func5, not_12_out, func2, func1);
  and and_10 (and_10_out, func6, not_13_out, not_14_out, func2);
  and and_11 (and_11_out, func6, not_15_out, func2, not_16_out);
  and and_12 (and_12_out, not_17_out, not_18_out, not_19_out, not_20_out, func2, func1);
  and and_13 (and_13_out, func3, not_21_out);
  and and_14 (and_14_out, func4, not_22_out);
  and and_15 (and_15_out, not_23_out, func5, func2, not_24_out);
  and and_16 (and_16_out, func6, not_25_out, not_26_out);
  and and_17 (and_17_out, not_27_out, not_28_out, not_29_out, not_30_out, not_31_out);
  and and_18 (and_18_out, not_32_out, not_33_out, not_34_out, not_35_out, func2);
  and and_19 (jr, not_36_out, not_37_out, func4, not_38_out, not_39_out, not_40_out);
  and and_20 (and_20_out, not_41_out, not_42_out, not_43_out, not_44_out);
  and and_21 (and_21_out, not_45_out, not_46_out, not_47_out, not_48_out, func2);
  and and_22 (and_22_out, func6, not_49_out, not_50_out, not_51_out);
  and and_23 (and_23_out, func6, not_52_out, not_53_out, func3);
  and and_24 (and_24_out, func6, not_54_out, func4, not_55_out, func2);
  or or_2 (alu3, and_3_out, and_4_out, and_5_out);
  or or_3 (alu2, and_6_out, and_7_out, and_8_out, and_9_out, and_10_out, and_11_out);
  or or_4 (alu1, and_12_out, and_13_out, and_14_out, and_15_out, and_16_out);
  or or_5 (sll, and_17_out, and_18_out);
  or or_6 (r, and_20_out, and_21_out, and_22_out, and_23_out, and_24_out);
endmodule

module alu (
  input  [31:0] A,
  input  [31:0] B,
  input  [3:0] op,
  output [31:0] R,
  output les,
  output out_6
);

  ALU alu_1 (
    .AluOP(op), .X(A), .Equal(out_6), .Result(R), .Y(B));  // open: Signed_Overflow, Result_2, UnSigned_Overflow

  assign les = A[31];

  // Other names for the same wires on the sheet: aluop[3:0] = op
endmodule

module we (
  input  op6,
  input  op5,
  input  op4,
  input  op3,
  input  op2,
  input  op1,
  output pc3,
  output pc2,
  output pc1,
  output rw2,
  output rw1,
  output din2,
  output din1,
  output b2,
  output B,
  output addr,
  output w,
  output rw
);

  wire and_3_out, and_4_out, and_5_out, and_6_out, and_7_out, and_8_out, and_9_out, and_13_out, and_15_out,
       and_16_out, and_17_out, and_18_out, not_1_out, not_2_out, not_3_out, not_4_out, not_5_out, not_6_out,
       not_7_out, not_8_out, not_9_out, not_10_out, not_11_out, not_12_out, not_13_out, not_14_out,
       not_15_out, not_16_out, not_17_out, not_18_out, not_19_out, not_20_out, not_21_out, not_22_out,
       not_23_out, not_24_out, not_25_out, not_26_out, not_27_out, not_28_out, not_29_out, not_30_out,
       not_31_out, not_32_out, not_33_out, not_34_out, not_35_out, not_36_out, not_37_out, not_38_out,
       not_39_out, not_40_out, not_41_out, not_42_out, not_43_out, not_44_out, not_45_out, not_46_out,
       not_47_out, not_48_out;

  not not_1 (not_1_out, op6);
  not not_2 (not_2_out, op5);
  not not_3 (not_3_out, op4);
  not not_4 (not_4_out, op2);
  not not_5 (not_5_out, op6);
  not not_6 (not_6_out, op5);
  not not_7 (not_7_out, op4);
  not not_8 (not_8_out, op3);
  not not_9 (not_9_out, op6);
  not not_10 (not_10_out, op5);
  not not_11 (not_11_out, op4);
  not not_12 (not_12_out, op2);
  not not_13 (not_13_out, op6);
  not not_14 (not_14_out, op5);
  not not_15 (not_15_out, op4);
  not not_16 (not_16_out, op3);
  not not_17 (not_17_out, op6);
  not not_18 (not_18_out, op5);
  not not_19 (not_19_out, op3);
  not not_20 (not_20_out, op6);
  not not_21 (not_21_out, op5);
  not not_22 (not_22_out, op4);
  not not_23 (not_23_out, op3);
  not not_24 (not_24_out, op4);
  not not_25 (not_25_out, op6);
  not not_26 (not_26_out, op5);
  not not_27 (not_27_out, op4);
  not not_28 (not_28_out, op3);
  not not_29 (not_29_out, op2);
  not not_30 (not_30_out, op6);
  not not_31 (not_31_out, op5);
  not not_32 (not_32_out, op3);
  not not_33 (not_33_out, op5);
  not not_34 (not_34_out, op3);
  not not_35 (not_35_out, op5);
  not not_36 (not_36_out, op4);
  not not_37 (not_37_out, op3);
  not not_38 (not_38_out, op6);
  not not_39 (not_39_out, op5);
  not not_40 (not_40_out, op2);
  not not_41 (not_41_out, op6);
  not not_42 (not_42_out, op5);
  not not_43 (not_43_out, op1);
  not not_44 (not_44_out, op5);
  not not_45 (not_45_out, op3);
  not not_46 (not_46_out, op1);
  not not_47 (not_47_out, op5);
  not not_48 (not_48_out, op3);
  and and_1 (pc3, not_1_out, not_2_out, not_3_out, op3, not_4_out);
  and and_2 (pc2, not_5_out, not_6_out, not_7_out, not_8_out, op2);
  and and_3 (and_3_out, not_9_out, not_10_out, not_11_out, not_12_out, op1);
  and and_4 (and_4_out, not_13_out, not_14_out, not_15_out, not_16_out, op2);
  and and_5 (and_5_out, not_17_out, op2, op1);
  and and_6 (and_6_out, op3, op2, op1);
  and and_7 (and_7_out, op4, op2, op1);
  and and_8 (and_8_out, op5, op2, op1);
  and and_9 (and_9_out, op6, not_18_out, not_19_out, op2, op1);
  and and_10 (din2, not_20_out, not_21_out, not_22_out, not_23_out, op2);
  and and_11 (din1, op6, not_24_out);
  and and_12 (b2, not_25_out, not_26_out, not_27_out, not_28_out, not_29_out, op1);
  and and_13 (and_13_out, not_30_out, not_31_out, not_32_out, op1);
  and and_14 (addr, op6, not_33_out, op4, not_34_out, op2, op1);
  and and_15 (and_15_out, not_35_out, not_36_out, not_37_out, op2, op1);
  and and_16 (and_16_out, not_38_out, not_39_out, op4, not_40_out);
  and and_17 (and_17_out, not_41_out, not_42_out, op4, op3, not_43_out);
  and and_18 (and_18_out, op6, not_44_out, op4, not_45_out, op2, not_46_out);
  and and_19 (rw, op6, not_47_out, op4, not_48_out, op2, op1);
  or or_1 (pc1, and_3_out, and_4_out);
  or or_2 (rw2, and_5_out, and_6_out, and_7_out, and_8_out);
  or or_3 (rw1, op4, and_9_out);
  or or_4 (B, and_13_out, op2, op4);
  or or_5 (w, and_15_out, and_16_out, and_17_out, and_18_out);
endmodule

module npc (
  input  [9:0] pc,
  input  [25:0] addr,
  input  [2:0] p,
  input  [31:0] rs,
  input  [15:0] offset,
  input  less,
  input  equ,
  output [9:0] out,
  output [9:0] pc11
);

  wire not_1_out;
  wire [9:0] adder_1_out, incrementer_1_p2, multiplexer_1_out, multiplexer_2_out, multiplexer_3_out;

  Adder #(.width(10)) adder_1 (.a(pc), .b(offset[9:0]), .out(adder_1_out));  // open: cin, cout
  // Incrementer incrementer_1: pin names not known; wires that end beside it: adder_1_out, incrementer_1_p2
  Multiplexer #(.width(10), .enable("false")) multiplexer_1 (
    .in0(pc11), .in1(incrementer_1_p2), .out(multiplexer_1_out), .sel(equ));
  Multiplexer #(.width(10), .enable("false")) multiplexer_2 (
    .in0(pc11), .in1(incrementer_1_p2), .out(multiplexer_2_out), .sel(not_1_out));
  not not_1 (not_1_out, equ);
  Multiplexer #(.width(10), .enable("false")) multiplexer_3 (
    .in0(pc11), .in1(adder_1_out), .out(multiplexer_3_out), .sel(less));
  // Incrementer incrementer_2: pin names not known; wires that end beside it: pc, pc11
  Multiplexer #(.select(3), .width(10), .enable("false")) multiplexer_4 (
    .in0(pc11), .in1(multiplexer_3_out), .in2(rs[9:0]), .in3(addr[9:0]), .in4(multiplexer_1_out),
    .in5(multiplexer_2_out), .in6(pc11), .in7(pc11), .out(out), .sel(p));

  // Other names for the same wires on the sheet: p11[9:0] = pc11
endmodule

module regfile (
  input  [31:0] w,
  input  clk,
  input  we,
  input  [4:0] rw,
  input  [4:0] ra,
  input  [4:0] rb,
  output [31:0] a,
  output [31:0] b
);

  // Probe on a
  // RegisterFile registerfile_1: pin names not known; wires that end beside it: w, clk, we, rw, ra, rb, a, b
endmodule

module if_id (
  input  [31:0] instrucion,
  input  [9:0] pc,
  input  \传输状态In ,
  input  CLK,
  input  \同步清零 ,
  output [31:0] insout,
  output [9:0] pcout,
  output \传输状态Out 
);

  wire multiplexer_3_out;
  wire [9:0] multiplexer_2_out;
  wire [31:0] multiplexer_1_out;

  // Probe on pc
  Multiplexer #(.width(32), .enable("false")) multiplexer_1 (
    .in0(instrucion), .in1({32{1'b0}}), .out(multiplexer_1_out), .sel(\同步清零 ));
  Multiplexer #(.width(10), .enable("false")) multiplexer_2 (
    .in0(pc), .in1({10{1'b0}}), .out(multiplexer_2_out), .sel(\同步清零 ));
  Multiplexer #(.enable("false")) multiplexer_3 (.in0(\传输状态In ), .in1(1'b0), .out(multiplexer_3_out), .sel(\同步清零 ));
  Register #(.width(32)) register_1 (.D(multiplexer_1_out), .en(\传输状态In ), .Q(insout), .clk(CLK));  // open: clr
  Register #(.width(10)) register_2 (.D(multiplexer_2_out), .en(\传输状态In ), .Q(pcout), .clk(CLK));  // open: clr
  Register #(.width(1)) register_3 (.D(multiplexer_3_out), .en(\传输状态In ), .Q(\传输状态Out ), .clk(CLK));  // open: clr
endmodule

module id_ex (
  input  [9:0] pc,
  input  [31:0] a,
  input  [31:0] b,
  input  [3:0] aluop,
  input  [31:0] imme,
  input  W,
  input  We,
  input  sys,
  input  A_2,
  input  [1:0] B_2,
  input  [1:0] din,
  input  [2:0] pcctr,
  input  [4:0] rw,
  input  \传输状态In ,
  input  CLK,
  input  \同步清零 ,
  output [9:0] pcout,
  output [31:0] a_3,
  output [31:0] b_3,
  output [3:0] aluopout,
  output [31:0] immeout,
  output Wout,
  output Weout,
  output sysout,
  output Aout,
  output [1:0] Bout,
  output [1:0] dinout,
  output [2:0] pcctrout,
  output [4:0] rwout,
  output \传输状态Out 
);

  wire multiplexer_6_out, multiplexer_7_out, multiplexer_8_out, multiplexer_9_out, multiplexer_14_out;
  wire [1:0] multiplexer_10_out, multiplexer_11_out;
  wire [2:0] multiplexer_12_out;
  wire [3:0] multiplexer_4_out;
  wire [4:0] multiplexer_13_out;
  wire [9:0] multiplexer_1_out;
  wire [31:0] multiplexer_2_out, multiplexer_3_out, multiplexer_5_out;

  Multiplexer #(.width(10), .enable("false")) multiplexer_1 (
    .in0(pc), .in1({10{1'b0}}), .out(multiplexer_1_out), .sel(\同步清零 ));
  Multiplexer #(.width(32), .enable("false")) multiplexer_2 (
    .in0(a), .in1({32{1'b0}}), .out(multiplexer_2_out), .sel(\同步清零 ));
  Multiplexer #(.width(32), .enable("false")) multiplexer_3 (
    .in0(b), .in1({32{1'b0}}), .out(multiplexer_3_out), .sel(\同步清零 ));
  Multiplexer #(.width(4), .enable("false")) multiplexer_4 (
    .in0(aluop), .in1(4'b0000), .out(multiplexer_4_out), .sel(\同步清零 ));
  Multiplexer #(.width(32), .enable("false")) multiplexer_5 (
    .in0(imme), .in1({32{1'b0}}), .out(multiplexer_5_out), .sel(\同步清零 ));
  Multiplexer #(.enable("false")) multiplexer_6 (.in0(W), .in1(1'b0), .out(multiplexer_6_out), .sel(\同步清零 ));
  Multiplexer #(.enable("false")) multiplexer_7 (.in0(We), .in1(1'b0), .out(multiplexer_7_out), .sel(\同步清零 ));
  Multiplexer #(.enable("false")) multiplexer_8 (.in0(sys), .in1(1'b0), .out(multiplexer_8_out), .sel(\同步清零 ));
  Multiplexer #(.enable("false")) multiplexer_9 (.in0(A_2), .in1(1'b0), .out(multiplexer_9_out), .sel(\同步清零 ));
  Multiplexer #(.width(2), .enable("false")) multiplexer_10 (
    .in0(B_2), .in1(2'b00), .out(multiplexer_10_out), .sel(\同步清零 ));
  Multiplexer #(.width(2), .enable("false")) multiplexer_11 (
    .in0(din), .in1(2'b00), .out(multiplexer_11_out), .sel(\同步清零 ));
  Multiplexer #(.width(3), .enable("false")) multiplexer_12 (
    .in0(pcctr), .in1(3'b000), .out(multiplexer_12_out), .sel(\同步清零 ));
  Multiplexer #(.width(5), .enable("false")) multiplexer_13 (
    .in0(rw), .in1({5{1'b0}}), .out(multiplexer_13_out), .sel(\同步清零 ));
  Multiplexer #(.enable("false")) multiplexer_14 (.in0(\传输状态In ), .in1(1'b0), .out(multiplexer_14_out), .sel(\同步清零 ));
  Register #(.width(10)) register_1 (.D(multiplexer_1_out), .en(\传输状态In ), .Q(pcout), .clk(CLK));  // open: clr
  Register #(.width(32)) register_2 (.D(multiplexer_2_out), .en(\传输状态In ), .Q(a_3), .clk(CLK));  // open: clr
  Register #(.width(32)) register_3 (.D(multiplexer_3_out), .en(\传输状态In ), .Q(b_3), .clk(CLK));  // open: clr
  Register #(.width(4)) register_4 (.D(multiplexer_4_out), .en(\传输状态In ), .Q(aluopout), .clk(CLK));  // open: clr
  Register #(.width(32)) register_5 (.D(multiplexer_5_out), .en(\传输状态In ), .Q(immeout), .clk(CLK));  // open: clr
  Register #(.width(1)) register_6 (.D(multiplexer_6_out), .en(\传输状态In ), .Q(Wout), .clk(CLK));  // open: clr
  Register #(.width(1)) register_7 (.D(multiplexer_7_out), .en(\传输状态In ), .Q(Weout), .clk(CLK));  // open: clr
  Register #(.width(1)) register_8 (.D(multiplexer_8_out), .en(\传输状态In ), .Q(sysout), .clk(CLK));  // open: clr
  Register #(.width(1)) register_9 (.D(multiplexer_9_out), .en(\传输状态In ), .Q(Aout), .clk(CLK));  // open: clr
  Register #(.width(2)) register_10 (.D(multiplexer_10_out), .en(\传输状态In ), .Q(Bout), .clk(CLK));  // open: clr
  Register #(.width(2)) register_11 (.D(multiplexer_11_out), .en(\传输状态In ), .Q(dinout), .clk(CLK));  // open: clr
  Register #(.width(3)) register_12 (.D(multiplexer_12_out), .en(\传输状态In ), .Q(pcctrout), .clk(CLK));  // open: clr
  Register #(.width(5)) register_13 (.D(multiplexer_13_out), .en(\传输状态In ), .Q(rwout), .clk(CLK));  // open: clr
  Register #(.width(1)) register_14 (.D(multiplexer_14_out), .en(\传输状态In ), .Q(\传输状态Out ), .clk(CLK));  // open: clr
endmodule

module ex_mem (
  input  [31:0] addr,
  input  [31:0] data,
  input  sel,
  input  we,
  input  sys,
  input  [31:0] v0,
  input  [1:0] din,
  input  [4:0] rw,
  input  [31:0] pc,
  input  [9:0] pcins,
  input  \传输状态In ,
  input  CLK,
  input  \同步清零 ,
  output [31:0] addrout,
  output [31:0] dataout,
  output selout,
  output weout,
  output sysout,
  output [31:0] v0out,
  output [1:0] dinout,
  output [4:0] rwout,
  output [31:0] pcout,
  output [9:0] pcout_2,
  output \传输状态Out 
);

  wire multiplexer_3_out, multiplexer_4_out, multiplexer_5_out, multiplexer_11_out;
  wire [1:0] multiplexer_7_out;
  wire [4:0] multiplexer_8_out;
  wire [9:0] multiplexer_10_out;
  wire [31:0] multiplexer_1_out, multiplexer_2_out, multiplexer_6_out, multiplexer_9_out;

  Multiplexer #(.width(32), .enable("false")) multiplexer_1 (
    .in0(addr), .in1({32{1'b0}}), .out(multiplexer_1_out), .sel(\同步清零 ));
  Multiplexer #(.width(32), .enable("false")) multiplexer_2 (
    .in0(data), .in1({32{1'b0}}), .out(multiplexer_2_out), .sel(\同步清零 ));
  Multiplexer #(.enable("false")) multiplexer_3 (.in0(sel), .in1(1'b0), .out(multiplexer_3_out), .sel(\同步清零 ));
  Multiplexer #(.enable("false")) multiplexer_4 (.in0(we), .in1(1'b0), .out(multiplexer_4_out), .sel(\同步清零 ));
  Multiplexer #(.enable("false")) multiplexer_5 (.in0(sys), .in1(1'b0), .out(multiplexer_5_out), .sel(\同步清零 ));
  Multiplexer #(.width(32), .enable("false")) multiplexer_6 (
    .in0(v0), .in1({32{1'b0}}), .out(multiplexer_6_out), .sel(\同步清零 ));
  Multiplexer #(.width(2), .enable("false")) multiplexer_7 (
    .in0(din), .in1(2'b00), .out(multiplexer_7_out), .sel(\同步清零 ));
  Multiplexer #(.width(5), .enable("false")) multiplexer_8 (
    .in0(rw), .in1({5{1'b0}}), .out(multiplexer_8_out), .sel(\同步清零 ));
  Multiplexer #(.width(32), .enable("false")) multiplexer_9 (
    .in0(pc), .in1({32{1'b0}}), .out(multiplexer_9_out), .sel(\同步清零 ));
  Multiplexer #(.width(10), .enable("false")) multiplexer_10 (
    .in0(pcins), .in1({10{1'b0}}), .out(multiplexer_10_out), .sel(\同步清零 ));
  Multiplexer #(.enable("false")) multiplexer_11 (.in0(\传输状态In ), .in1(1'b0), .out(multiplexer_11_out), .sel(\同步清零 ));
  Register #(.width(32)) register_1 (.D(multiplexer_1_out), .en(\传输状态In ), .Q(addrout), .clk(CLK));  // open: clr
  Register #(.width(32)) register_2 (.D(multiplexer_2_out), .en(\传输状态In ), .Q(dataout), .clk(CLK));  // open: clr
  Register #(.width(1)) register_3 (.D(multiplexer_3_out), .en(\传输状态In ), .Q(selout), .clk(CLK));  // open: clr
  Register #(.width(1)) register_4 (.D(multiplexer_4_out), .en(\传输状态In ), .Q(weout), .clk(CLK));  // open: clr
  Register #(.width(1)) register_5 (.D(multiplexer_5_out), .en(\传输状态In ), .Q(sysout), .clk(CLK));  // open: clr
  Register #(.width(32)) register_6 (.D(multiplexer_6_out), .en(\传输状态In ), .Q(v0out), .clk(CLK));  // open: clr
  Register #(.width(2)) register_7 (.D(multiplexer_7_out), .en(\传输状态In ), .Q(dinout), .clk(CLK));  // open: clr
  Register #(.width(5)) register_8 (.D(multiplexer_8_out), .en(\传输状态In ), .Q(rwout), .clk(CLK));  // open: clr
  Register #(.width(32)) register_9 (.D(multiplexer_9_out), .en(\传输状态In ), .Q(pcout), .clk(CLK));  // open: clr
  Register #(.width(10)) register_10 (.D(multiplexer_10_out), .en(\传输状态In ), .Q(pcout_2), .clk(CLK));  // open: clr
  Register #(.width(1)) register_11 (.D(multiplexer_11_out), .en(\传输状态In ), .Q(\传输状态Out ), .clk(CLK));  // open: clr
endmodule

module mem_wb (
  input  [31:0] instrucion,
  input  sys,
  input  we,
  input  [31:0] data,
  input  [31:0] alu,
  input  [31:0] v0,
  input  [31:0] a0,
  input  [4:0] rw,
  input  [1:0] din,
  input  [9:0] pc,
  input  \传输状态In ,
  input  CLK,
  input  \同步清零 ,
  output [31:0] insout,
  output sysout,
  output weout,
  output [31:0] dataout,
  output [31:0] aluout,
  output [31:0] v0out,
  output [31:0] a0out,
  output [4:0] rwout,
  output [1:0] dinout,
  output [9:0] pcout,
  output \传输状态Out 
);

  wire multiplexer_2_out, multiplexer_3_out, multiplexer_11_out;
  wire [1:0] multiplexer_9_out;
  wire [4:0] multiplexer_8_out;
  wire [9:0] multiplexer_10_out;
  wire [31:0] multiplexer_1_out, multiplexer_4_out, multiplexer_5_out, multiplexer_6_out, multiplexer_7_out;

  Multiplexer #(.width(32), .enable("false")) multiplexer_1 (
    .in0(instrucion), .in1({32{1'b0}}), .out(multiplexer_1_out), .sel(\同步清零 ));
  Multiplexer #(.enable("false")) multiplexer_2 (.in0(sys), .in1(1'b0), .out(multiplexer_2_out), .sel(\同步清零 ));
  Multiplexer #(.enable("false")) multiplexer_3 (.in0(we), .in1(1'b0), .out(multiplexer_3_out), .sel(\同步清零 ));
  Multiplexer #(.width(32), .enable("false")) multiplexer_4 (
    .in0(data), .in1({32{1'b0}}), .out(multiplexer_4_out), .sel(\同步清零 ));
  Multiplexer #(.width(32), .enable("false")) multiplexer_5 (
    .in0(alu), .in1({32{1'b0}}), .out(multiplexer_5_out), .sel(\同步清零 ));
  Multiplexer #(.width(32), .enable("false")) multiplexer_6 (
    .in0(v0), .in1({32{1'b0}}), .out(multiplexer_6_out), .sel(\同步清零 ));
  Multiplexer #(.width(32), .enable("false")) multiplexer_7 (
    .in0(a0), .in1({32{1'b0}}), .out(multiplexer_7_out), .sel(\同步清零 ));
  Multiplexer #(.width(5), .enable("false")) multiplexer_8 (
    .in0(rw), .in1({5{1'b0}}), .out(multiplexer_8_out), .sel(\同步清零 ));
  Multiplexer #(.width(2), .enable("false")) multiplexer_9 (
    .in0(din), .in1(2'b00), .out(multiplexer_9_out), .sel(\同步清零 ));
  Multiplexer #(.width(10), .enable("false")) multiplexer_10 (
    .in0(pc), .in1({10{1'b0}}), .out(multiplexer_10_out), .sel(\同步清零 ));
  Multiplexer #(.enable("false")) multiplexer_11 (.in0(\传输状态In ), .in1(1'b0), .out(multiplexer_11_out), .sel(\同步清零 ));
  Register #(.width(32)) register_1 (.D(multiplexer_1_out), .en(\传输状态In ), .Q(insout), .clk(CLK));  // open: clr
  Register #(.width(1)) register_2 (.D(multiplexer_2_out), .en(\传输状态In ), .Q(sysout), .clk(CLK));  // open: clr
  Register #(.width(1)) register_3 (.D(multiplexer_3_out), .en(\传输状态In ), .Q(weout), .clk(CLK));  // open: clr
  Register #(.width(32)) register_4 (.D(multiplexer_4_out), .en(\传输状态In ), .Q(dataout), .clk(CLK));  // open: clr
  Register #(.width(32)) register_5 (.D(multiplexer_5_out), .en(\传输状态In ), .Q(aluout), .clk(CLK));  // open: clr
  Register #(.width(32)) register_6 (.D(multiplexer_6_out), .en(\传输状态In ), .Q(v0out), .clk(CLK));  // open: clr
  Register #(.width(32)) register_7 (.D(multiplexer_7_out), .en(\传输状态In ), .Q(a0out), .clk(CLK));  // open: clr
  Register #(.width(5)) register_8 (.D(multiplexer_8_out), .en(\传输状态In ), .Q(rwout), .clk(CLK));  // open: clr
  Register #(.width(2)) register_9 (.D(multiplexer_9_out), .en(\传输状态In ), .Q(dinout), .clk(CLK));  // open: clr
  Register #(.width(10)) register_10 (.D(multiplexer_10_out), .en(\传输状态In ), .Q(pcout), .clk(CLK));  // open: clr
  Register #(.width(1)) register_11 (.D(multiplexer_11_out), .en(\传输状态In ), .Q(\传输状态Out ), .clk(CLK));  // open: clr
endmodule

module pipaine (
  input  [4:0] ra,
  input  [4:0] rb,
  input  [31:0] op,
  input  [4:0] rw,
  input  we,
  input  [4:0] rw2,
  input  we2,
  output insert,
  output insert2
);

  wire comparator_1_eq, comparator_2_eq, comparator_3_eq, comparator_4_eq, or_1_out, or_2_out;

  Comparator #(.width(5)) comparator_1 (.a(ra), .b(rw), .eq(comparator_1_eq));  // open: gt, lt
  Comparator #(.width(5)) comparator_2 (.a(rb), .b(rw), .eq(comparator_2_eq));  // open: gt, lt
  Comparator #(.width(5)) comparator_3 (.a(ra), .b(rw2), .eq(comparator_3_eq));  // open: gt, lt
  Comparator #(.width(5)) comparator_4 (.a(rb), .b(rw2), .eq(comparator_4_eq));  // open: gt, lt
  or or_1 (or_1_out, comparator_1_eq, comparator_2_eq);
  and and_1 (insert, or_1_out, we);
  or or_2 (or_2_out, comparator_3_eq, comparator_4_eq);
  and and_2 (insert2, or_2_out, we2);
endmodule

module jump (
  input  [2:0] jump,
  input  eq,
  input  le,
  output jumpctr
);

  wire and_1_out, and_2_out, and_3_out, comparator_1_eq, comparator_2_eq, comparator_3_eq, comparator_4_eq,
       comparator_5_eq, not_1_out, \无条件分支指令数 , \有条件分支成功跳转 ;

  or or_1 (jumpctr, \无条件分支指令数 , \有条件分支成功跳转 );
  Comparator #(.width(3)) comparator_1 (.a(jump), .b(3'b001), .eq(comparator_1_eq));  // open: gt, lt
  Comparator #(.width(3)) comparator_2 (.a(jump), .b(3'b100), .eq(comparator_2_eq));  // open: gt, lt
  Comparator #(.width(3)) comparator_3 (.a(jump), .b(3'b101), .eq(comparator_3_eq));  // open: gt, lt
  Comparator #(.width(3)) comparator_4 (.a(jump), .b(3'b010), .eq(comparator_4_eq));  // open: gt, lt
  Comparator #(.width(3)) comparator_5 (.a(jump), .b(3'b011), .eq(comparator_5_eq));  // open: gt, lt
  and and_1 (and_1_out, comparator_1_eq, le);
  and and_2 (and_2_out, comparator_2_eq, eq);
  and and_3 (and_3_out, comparator_3_eq, not_1_out);
  not not_1 (not_1_out, eq);
  or or_2 (\无条件分支指令数 , comparator_4_eq, comparator_5_eq);
  or or_3 (\有条件分支成功跳转 , and_1_out, and_2_out, and_3_out);
endmodule
