// Logisim project 流水中断.circ as structural Verilog: 15 circuits, main circuit cpu
module cpu (
);

  wire and_2_out, and_9_out, and_10_out, and_11_out, and_12_out, clk, comparator_1_eq, comparator_2_eq,
       comparator_3_eq, comparator_4_eq, comparator_5_eq, comparator_7_eq, CONTROL_a, CONTROL_syscall,
       CONTROL_w, CONTROL_we, eq, eret, ex_mem_1_selout, ex_mem_1_sysout, \ex_mem_1_传输状态out , halt,
       id_ex_1_aout, id_ex_1_sysout, id_ex_1_wout, \id_ex_1_传输状态out , \if_id_1_传输状态out , IR1, IR2, IR3, le,
       lw, lwdelay, lwdelay2, multiplexer_6_out, multiplexer_17_out, multiplexer_20_out, multiplexer_22_out,
       not_1_out, not_2_out, not_3_out, not_4_out, not_5_out, not_6_out, not_7_out, not_8_out, or_1_out,
       or_2_out, or_3_out, or_4_out, or_5_out, or_6_out, or_7_out, pipajump, redirection_1_lw,
       redirection_1_rw1a, register_1_q, RST, rw1a, rw1b, rw2a, rw2b, sys, W1, W2, W3, we, we1, wee,
       zhongduan;
  wire [1:0] CONTROL_b, CONTROL_din, CONTROL_rw, din, ex_mem_1_dinout, id_ex_1_bout, id_ex_1_dinout, xy;
  wire [2:0] CONTROL_pc, jump;
  wire [3:0] CONTROL_aluop, id_ex_1_aluopout;
  wire [4:0] multiplexer_11_out, ra, ra0, rb, rb0, rw, rw1, rww;
  wire [9:0] and_3_out, and_4_out, and_5_out, and_6_out, and_7_out, EX_PC, ID_PC, IF_PC, incrementer_1_p2,
       MEM_PC, multiplexer_2_out, multiplexer_3_out, multiplexer_4_out, npc_1_pc11, pcp1, savepc, WB_PC,
       yuanpc, zhongduanpc;
  wire [15:0] adder_1_out, Count, incrementer_2_p2, incrementer_3_p2, incrementer_4_p2, \load_use次数 ,
       multiplexer_10_out, multiplexer_12_out, multiplexer_21_out, \无条件分支指令数 , \有条件分支成功跳转 ;
  wire [31:0] a0, ALU_r, aluout, bit_extender_1_out, bit_extender_2_out, bit_extender_3_out,
       ex_mem_1_dataout, ex_mem_1_op_2, ex_mem_1_pcout, ex_mem_1_v0out, if_id_1_insout, mem_wb_1_op_2,
       mips_ram_1_p8, multiplexer_13_out, multiplexer_14_out, multiplexer_15_out, multiplexer_16_out, opp,
       pcrw, rain, ramout, raout, rbin, rbout, regfile_1_a, regfile_1_b, rom_1_data, SyscallOut, v0, wdata1,
       wdata2;

  Button \u_总复位  (.out(RST));
  Button _1 (.out(IR1));
  Button _2 (.out(IR2));
  Button _3 (.out(IR3));
  LED led_1 (.in(W1));
  LED led_2 (.in(W2));
  LED led_3 (.in(W3));
  Multiplexer #(.width(10), .enable("false")) multiplexer_1 (
    .in0(multiplexer_4_out), .in1(pcp1), .out(yuanpc), .sel(pipajump));
  Multiplexer #(.width(10), .enable("false")) multiplexer_2 (
    .in0(multiplexer_3_out), .in1(zhongduanpc), .out(multiplexer_2_out), .sel(zhongduan));
  Multiplexer #(.width(10), .enable("false")) multiplexer_3 (
    .in0(yuanpc), .in1(savepc), .out(multiplexer_3_out), .sel(eret));
  not not_1 (not_1_out, register_1_q);
  Register #(.width(1)) register_1 (.D(eret), .Q(register_1_q), .clk(clk));  // open: en, clr
  not not_2 (not_2_out, eret);
  and and_1 (rw1a, not_2_out, redirection_1_rw1a);
  Hex_Digit_Display hex_digit_display_1 (.value(SyscallOut[31:28]));  // open: dp
  Multiplexer #(.width(10), .enable("false")) multiplexer_4 (
    .in0(incrementer_1_p2), .in1(IF_PC), .out(multiplexer_4_out), .sel(lw));
  Register #(.width(10)) PC (.D(multiplexer_2_out), .en(not_3_out), .Q(IF_PC), .clk(clk), .clr(RST));
  not not_3 (not_3_out, halt);
  Multiplexer #(.select(2), .width(10), .enable("false")) multiplexer_5 (
    .in0({10{1'b0}}), .in1(10'hdb), .in2(10'hfa), .in3(10'h119), .out(zhongduanpc), .sel(xy));
  Register #(.width(10)) register_2 (.D(MEM_PC), .en(and_2_out), .Q(savepc), .clk(clk));  // open: clr
  and and_2 (and_2_out, zhongduan, not_1_out);
  redirection redirection_1 (
    .ra(ra), .rb(rb), .op(opp), .rw1(rw1), .we1(we1), .rw2(rw), .we2(we), .rw1a(redirection_1_rw1a),
    .rw1b(rw1b), .rw2a(rw2a), .rw2b(rw2b), .lw(redirection_1_lw), .ra0(ra0), .rb0(rb0), .rw0(rww));
  Hex_Digit_Display hex_digit_display_2 (.value(SyscallOut[27:24]));  // open: dp
  Hex_Digit_Display hex_digit_display_3 (.value(SyscallOut[23:20]));  // open: dp
  // Probe on Count
  // Probe on and_3_out
  assign and_3_out = IF_PC & {10{1'b1}};  // AND_Gate and_3, 10 bits wide
  assign and_4_out = ID_PC & {10{1'b1}};  // AND_Gate and_4, 10 bits wide
  // Probe on and_4_out
  // Probe on and_5_out
  assign and_5_out = EX_PC & {10{1'b1}};  // AND_Gate and_5, 10 bits wide
  assign and_6_out = MEM_PC & {10{1'b1}};  // AND_Gate and_6, 10 bits wide
  // Probe on and_6_out
  assign and_7_out = WB_PC & {10{1'b1}};  // AND_Gate and_7, 10 bits wide
  // Probe on and_7_out
  Hex_Digit_Display hex_digit_display_4 (.value(SyscallOut[15:12]));  // open: dp
  Hex_Digit_Display hex_digit_display_5 (.value(SyscallOut[19:16]));  // open: dp
  // Incrementer incrementer_1: pin names not known; wires that end beside it: IF_PC, incrementer_1_p2
  Multiplexer #(.enable("false")) multiplexer_6 (.in0(1'b1), .in1(1'b0), .out(multiplexer_6_out), .sel(lw));
  not not_4 (not_4_out, eret);
  and and_8 (lw, redirection_1_lw, not_4_out);
  Hex_Digit_Display hex_digit_display_6 (.value(SyscallOut[11:8]));  // open: dp
  Hex_Digit_Display hex_digit_display_7 (.value(SyscallOut[7:4]));  // open: dp
  ROM #(.addrWidth(10), .dataWidth(32)) rom_1 (.addr(IF_PC), .data(rom_1_data));  // open: sel
  jump jump_1 (.jump(jump), .eq(eq), .le(le), .jumpctr(pipajump));
  Hex_Digit_Display hex_digit_display_8 (.value(SyscallOut[3:0]));  // open: dp
  Clock clock_1 (.out(clk));
  or or_1 (or_1_out, pipajump, zhongduan, or_6_out);
  if_id if_id_1 (
    .pc(IF_PC), .pcout(ID_PC), .\传输状态In (multiplexer_6_out), .\传输状态Out (\if_id_1_传输状态out ), .CLK(clk),
    .\同步清零 (or_1_out), .instrucion(rom_1_data), .insout(if_id_1_insout));
  // Probe on if_id_1_insout
  // Probe on ID_PC
  // Probe on Count
  // Probe on \无条件分支指令数 
  // Probe on \有条件分支成功跳转 
  // Probe on \load_use次数 
  aluctr CONTROL (
    .op(if_id_1_insout[31:26]), .func(if_id_1_insout[5:0]), .rw(CONTROL_rw), .din(CONTROL_din),
    .A(CONTROL_a), .B(CONTROL_b), .WE(CONTROL_we), .pc(CONTROL_pc), .W(CONTROL_w), .syscall(CONTROL_syscall),
    .aluop(CONTROL_aluop));  // open: addr
  // Probe on CONTROL_syscall
  // Probe on CONTROL_we
  Multiplexer #(.width(5), .enable("false")) multiplexer_7 (
    .in0(if_id_1_insout[25:21]), .in1(5'b00010), .out(ra0), .sel(CONTROL_syscall));
  Multiplexer #(.width(5), .enable("false")) multiplexer_8 (
    .in0(if_id_1_insout[20:16]), .in1(5'b00100), .out(rb0), .sel(CONTROL_syscall));
  // Incrementer incrementer_2: pin names not known; wires that end beside it: \load_use次数 , incrementer_2_p2
  Multiplexer #(.select(2), .width(32), .enable("false")) multiplexer_9 (
    .in0(aluout), .in1(ramout), .in2(pcrw), .in3({32{1'b0}}), .out(wdata2), .sel(din));
  Register #(.width(16)) register_3 (.D(multiplexer_10_out), .Q(\load_use次数 ), .clk(clk), .clr(RST));  // open: en
  Multiplexer #(.width(16), .enable("false")) multiplexer_10 (
    .in0(\load_use次数 ), .in1(incrementer_2_p2), .out(multiplexer_10_out), .sel(lw));
  Multiplexer #(.select(2), .width(5), .enable("false")) multiplexer_11 (
    .in0(if_id_1_insout[15:11]), .in1(if_id_1_insout[20:16]), .in2({5{1'b1}}), .in3(5'b11100),
    .out(multiplexer_11_out), .sel(CONTROL_rw));
  // Probe on CONTROL_aluop
  regfile regfile_1 (.clk(clk), .we(we), .rw(rw), .ra(ra0), .rb(rb0), .w(wdata2), .a(regfile_1_a), .b(regfile_1_b));
  Comparator #(.width(3)) comparator_1 (.a(jump), .b(3'b001), .eq(comparator_1_eq));  // open: gt, lt
  Comparator #(.width(3)) comparator_2 (.a(jump), .b(3'b100), .eq(comparator_2_eq));  // open: gt, lt
  Comparator #(.width(3)) comparator_3 (.a(jump), .b(3'b101), .eq(comparator_3_eq));  // open: gt, lt
  not not_5 (not_5_out, halt);
  Register #(.width(1)) register_4 (.D(lw), .Q(lwdelay), .clk(clk));  // open: en, clr
  // Incrementer incrementer_3: pin names not known; wires that end beside it: \有条件分支成功跳转 , incrementer_3_p2
  and and_9 (and_9_out, comparator_1_eq, le);
  and and_10 (and_10_out, comparator_2_eq, eq);
  and and_11 (and_11_out, comparator_3_eq, not_6_out);
  not not_6 (not_6_out, eq);
  Register #(.width(16)) register_5 (.D(adder_1_out), .en(not_5_out), .Q(Count), .clk(clk), .clr(RST));
  // Probe on Count
  or or_2 (or_2_out, pipajump, lw, or_6_out, zhongduan);
  id_ex id_ex_1 (
    .\传输状态In (\if_id_1_传输状态out ), .CLK(clk), .a_3(rain), .\传输状态Out (\id_ex_1_传输状态out ), .\同步清零 (or_2_out),
    .a(regfile_1_a), .b(regfile_1_b), .b_3(rbin), .aluop(CONTROL_aluop), .aluopout(id_ex_1_aluopout),
    .imme(if_id_1_insout), .immeout(opp), .pc(ID_PC), .pcout(EX_PC), .W(CONTROL_w), .Wout(id_ex_1_wout),
    .We(CONTROL_we), .Weout(wee), .sys(CONTROL_syscall), .sysout(id_ex_1_sysout), .A_2(CONTROL_a),
    .Aout(id_ex_1_aout), .B_2(CONTROL_b), .Bout(id_ex_1_bout), .din(CONTROL_din), .pcctr(CONTROL_pc),
    .pcctrout(jump), .dinout(id_ex_1_dinout), .rw(multiplexer_11_out), .rwout(rww), .ra(ra0), .raout(ra),
    .rb(rb0), .rbout(rb));
  Register #(.width(1)) register_6 (.D(lwdelay), .Q(lwdelay2), .clk(clk));  // open: en, clr
  Multiplexer #(.width(16), .enable("false")) multiplexer_12 (
    .in0(\有条件分支成功跳转 ), .in1(incrementer_3_p2), .out(multiplexer_12_out), .sel(or_3_out));
  or or_3 (or_3_out, and_9_out, and_10_out, and_11_out);
  Adder #(.width(16)) adder_1 (.a(Count), .b(16'h1), .out(adder_1_out));  // open: cin, cout
  // Probe on EX_PC
  // Probe on opp
  Counter #(.width(16), .max('hffff)) counter_1 (
    .load(1'b1), .D(multiplexer_12_out), .count(1'b0), .Q(\有条件分支成功跳转 ), .clk(clk), .clr(RST));  // open: carry
  assign bit_extender_1_out = {{27{opp[10]}}, opp[10:6]};  // Bit_Extender bit_extender_1
  assign bit_extender_2_out = {{16{opp[15]}}, opp[15:0]};  // Bit_Extender bit_extender_2
  Multiplexer #(.select(2), .width(32), .enable("false")) multiplexer_13 (
    .in0(rbout), .in1(bit_extender_1_out), .in2(bit_extender_2_out), .in3({32{1'b0}}),
    .out(multiplexer_13_out), .sel(id_ex_1_bout));
  Multiplexer #(.width(32), .enable("false")) multiplexer_14 (
    .in0(rain), .in1(wdata2), .out(multiplexer_14_out), .sel(rw2a));
  Multiplexer #(.width(32), .enable("false")) multiplexer_15 (
    .in0(rbin), .in1(wdata2), .out(multiplexer_15_out), .sel(rw2b));
  Multiplexer #(.width(32), .enable("false")) multiplexer_16 (
    .in0(raout), .in1(rbout), .out(multiplexer_16_out), .sel(id_ex_1_aout));
  Multiplexer #(.enable("false")) multiplexer_17 (
    .in0(\id_ex_1_传输状态out ), .in1(1'b1), .out(multiplexer_17_out), .sel(lwdelay));
  Multiplexer #(.width(32), .enable("false")) multiplexer_18 (
    .in0(multiplexer_14_out), .in1(wdata1), .out(raout), .sel(rw1a));
  Multiplexer #(.width(32), .enable("false")) multiplexer_19 (
    .in0(multiplexer_15_out), .in1(wdata1), .out(rbout), .sel(rw1b));
  npc npc_1 (
    .pc(EX_PC), .addr(opp[25:0]), .p(jump), .rs(raout), .offset(opp[15:0]), .less(le), .equ(eq), .out(pcp1),
    .pc11(npc_1_pc11));
  alu ALU (.A(multiplexer_16_out), .B(multiplexer_13_out), .op(id_ex_1_aluopout), .R(ALU_r), .out_6(eq), .les(le));
  ex_mem ex_mem_1 (
    .addr(ALU_r), .addrout(wdata1), .data(rbout), .dataout(ex_mem_1_dataout), .\传输状态In (multiplexer_17_out),
    .\传输状态Out (\ex_mem_1_传输状态out ), .CLK(clk), .\同步清零 (or_4_out), .sel(id_ex_1_wout),
    .selout(ex_mem_1_selout), .we(wee), .weout(we1), .sys(id_ex_1_sysout), .sysout(ex_mem_1_sysout),
    .v0(raout), .v0out(ex_mem_1_v0out), .rw(rww), .rwout(rw1), .din(id_ex_1_dinout),
    .dinout(ex_mem_1_dinout), .pc(bit_extender_3_out), .pcout(ex_mem_1_pcout), .pcins(EX_PC),
    .pcout_2(MEM_PC), .op(opp), .op_2(ex_mem_1_op_2));
  assign bit_extender_3_out = {{22{1'b0}}, npc_1_pc11};  // Bit_Extender bit_extender_3
  or or_4 (or_4_out, zhongduan, or_6_out);
  // Probe on MEM_PC
  Multiplexer #(.enable("false")) multiplexer_20 (
    .in0(\ex_mem_1_传输状态out ), .in1(1'b1), .out(multiplexer_20_out), .sel(lwdelay2));
  // Incrementer incrementer_4: pin names not known; wires that end beside it: \无条件分支指令数 , incrementer_4_p2
  Comparator #(.width(3)) comparator_4 (.a(jump), .b(3'b010), .eq(comparator_4_eq));  // open: gt, lt
  or or_5 (or_5_out, comparator_4_eq, comparator_5_eq);
  Comparator #(.width(3)) comparator_5 (.a(jump), .b(3'b011), .eq(comparator_5_eq));  // open: gt, lt
  zhonduan zhonduan_1 (
    .clk(clk), .ir1(IR1), .xy(xy), .ir2(IR2), .w1(W1), .ir3(IR3), .eret(eret), .zhongduan(zhongduan),
    .w2(W2), .w3(W3));
  Counter #(.width(16), .max('hffff)) counter_2 (
    .load(1'b1), .D(multiplexer_21_out), .count(1'b0), .Q(\无条件分支指令数 ), .clk(clk), .clr(RST));  // open: carry
  Multiplexer #(.width(16), .enable("false")) multiplexer_21 (
    .in0(\无条件分支指令数 ), .in1(incrementer_4_p2), .out(multiplexer_21_out), .sel(or_5_out));
  // MIPS_RAM mips_ram_1: pin names not known; wires that end beside it: wdata1[13:2], ex_mem_1_dataout, ex_mem_1_selout, 4'b1111, clk, 1'b1, RST, mips_ram_1_p8
  or or_6 (or_6_out, halt, eret, RST);
  or or_7 (or_7_out, zhongduan, or_6_out);
  mem_wb mem_wb_1 (
    .instrucion(ex_mem_1_pcout), .insout(pcrw), .sys(ex_mem_1_sysout), .sysout(sys),
    .\传输状态In (multiplexer_20_out), .CLK(clk), .\同步清零 (or_7_out), .we(we1), .weout(we), .data(mips_ram_1_p8),
    .dataout(ramout), .alu(wdata1), .aluout(aluout), .v0out(v0), .v0(ex_mem_1_v0out), .a0(ex_mem_1_dataout),
    .a0out(a0), .rw(rw1), .rwout(rw), .din(ex_mem_1_dinout), .dinout(din), .pc(MEM_PC), .pcout(WB_PC),
    .op(ex_mem_1_op_2), .op_2(mem_wb_1_op_2));  // open: 传输状态Out
  // Probe on WB_PC
  Comparator #(.width(32)) comparator_6 (.a(mem_wb_1_op_2), .b(32'h42000018), .eq(eret));  // open: gt, lt
  Comparator #(.width(32)) comparator_7 (.a(v0), .b(32'ha), .eq(comparator_7_eq));  // open: gt, lt
  Multiplexer #(.enable("false")) multiplexer_22 (
    .in0(1'b0), .in1(comparator_7_eq), .out(multiplexer_22_out), .sel(sys));
  not not_7 (not_7_out, halt);
  Register #(.width(1)) register_7 (.D(multiplexer_22_out), .en(not_7_out), .Q(halt), .clk(clk), .clr(RST));
  not not_8 (not_8_out, multiplexer_22_out);
  and and_12 (and_12_out, not_8_out, sys);
  Register #(.width(32)) register_8 (.D(a0), .en(and_12_out), .Q(SyscallOut), .clk(clk), .clr(RST));

  // Other names for the same wires on the sheet: mempc[9:0] = MEM_PC; 总周期数[15:0] = Count

  // Notes on the sheet:
  //   中断源
  //   中断等待指示
  //   指令存储器
  //   数码管输出
  //   contents of rom_1 (hex, n*v repeats v):
  //   20110001 8000c05 20110001 20120002 20130003 8000c09 20110001 20120002 20130003 8000c0d 20110001
  //   20120002 20130003 8000c11 20110001 20120002 20130003 c000cb8 20100001 20110001 118fc0 112020
  //   20020022 c 118882 12200001 8000c15 112020 20020022 c 20110001 118880 112020 20020022 c 12200001
  //   8000c1f 20110001 118fc0 112020 20020022 c 1188c3 112020 20020022 c 118903 112020 20020022 c 118903
  //   112020 20020022 c 118903 112020 20020022 c 118903 112020 20020022 c 118903 112020 20020022 c 118903
  //   112020 20020022 c 118903 112020 20020022 c 20100001 109fc0 139fc3 8021 2012000c 24160003 26100001
  //   3210000f 20080008 20090001 139900 2709825 132020 20020022 c 1094022 1500fff9 22100001 2018000f
  //   2188024 108700 20080008 20090001 139902 2709825 132021 20020022 c 1094022 1500fff9 108702 2c9b022
  //   12c00001 8000c50 4020 1084027 84400 3508ffff 82021 20020022 c 2010ffff 20110000 ae300000 22100001
  //   22310004 ae300000 22100001 22310004 ae300000 22100001 22310004 ae300000 22100001 22310004 ae300000
  //   22100001 22310004 ae300000 22100001 22310004 ae300000 22100001 22310004 ae300000 22100001 22310004
  //   ae300000 22100001 22310004 ae300000 22100001 22310004 ae300000 22100001 22310004 ae300000 22100001
  //   22310004 ae300000 22100001 22310004 ae300000 22100001 22310004 ae300000 22100001 22310004 ae300000
  //   22100001 22310004 22100001 8020 2011003c 8e130000 8e340000 274402a 11000002 ae330000 ae140000
  //   2231fffc 1611fff8 102020 20020022 c 22100004 2011003c 1611fff2 2002000a c 20100000 22100001 102020
  //   20020022 c 22100002 102020 20020022 c 22100003 102020 20020022 c 22100004 102020 20020022 c 22100005
  //   102020 20020022 c 22100006 102020 20020022 c 22100007 102020 20020022 c 22100008 102020 20020022
  //   20020022 c 3e00008 241d0050 27bdfffc afb00000 27bdfffc afb10000 27bdfffc afa20000 27bdfffc afa40000
  //   27bdfffc 20100001 20110001 118f00 112020 20020022 c 118902 12200001 8000ce8 112020 20020022 c
  //   23bd0004 8fa40000 23bd0004 8fa20000 23bd0004 8fb10000 23bd0004 8fb00000 42000018 241d0050 27bdfffc
  //   afb00000 27bdfffc afb10000 27bdfffc afa20000 27bdfffc afa40000 27bdfffc 20100001 20110001 118f40
  //   112020 20020022 c 118902 12200001 8000d07 112020 20020022 c 23bd0004 8fa40000 23bd0004 8fa20000
  //   23bd0004 8fb10000 23bd0004 8fb00000 42000018 241d0050 27bdfffc afb00000 27bdfffc afb10000 27bdfffc
  //   afa20000 27bdfffc afa40000 27bdfffc 20100001 20110003 118f00 112020 20020022 c 118902 12200001
  //   8000d26 112020 20020022 c 23bd0004 8fa40000 23bd0004 8fa20000 23bd0004 8fb10000 23bd0004 8fb00000
  //   42000018
  //   寄存器文件
endmodule

module aluctr (
  input  [5:0] op,
  input  [5:0] func,
  output [1:0] rw,
  output [1:0] din,
  output A,
  output [1:0] B,
  output addr,
  output WE,
  output [2:0] pc,
  output W,
  output syscall,
  output [3:0] aluop
);

  wire and_3_out, and_4_out, comparator_1_eq, jr, r, rtype, sll, WE_t;
  wire [1:0] b_t;
  wire [2:0] pc_t;
  wire [3:0] funcctr_1_alu1, opctr_1_alu1;

  and and_1 (A, sll, rtype);
  Comparator #(.width(6)) comparator_1 (.a(func), .b(6'b001100), .eq(comparator_1_eq));  // open: gt, lt
  Multiplexer #(.width(2), .enable("false")) multiplexer_1 (.in0(b_t), .in1(2'b01), .out(B), .sel(A));
  and and_2 (syscall, comparator_1_eq, rtype);
  Comparator #(.width(6)) comparator_2 (.a(op), .b({6{1'b0}}), .eq(rtype));  // open: gt, lt
  Multiplexer #(.width(3), .enable("false")) multiplexer_2 (.in0(pc_t), .in1(3'b010), .out(pc), .sel(and_3_out));
  and and_3 (and_3_out, jr, rtype);
  funcctr funcctr_1 (
    .func6(func[5]), .func5(func[4]), .func4(func[3]), .func3(func[2]), .func2(func[1]), .func1(func[0]),
    .alu4(funcctr_1_alu1[3]), .alu3(funcctr_1_alu1[2]), .alu2(funcctr_1_alu1[1]), .alu1(funcctr_1_alu1[0]),
    .sll(sll), .jr(jr), .r(r));
  opctr opctr_1 (
    .op6(op[5]), .op5(op[4]), .op4(op[3]), .op3(op[2]), .op2(op[1]), .op1(op[0]), .alu4(opctr_1_alu1[3]),
    .alu3(opctr_1_alu1[2]), .alu2(opctr_1_alu1[1]), .alu1(opctr_1_alu1[0]));
  we we_1 (
    .op6(op[5]), .op5(op[4]), .op4(op[3]), .op3(op[2]), .op2(op[1]), .op1(op[0]), .pc3(pc_t[2]),
    .pc2(pc_t[1]), .pc1(pc_t[0]), .rw2(rw[1]), .rw1(rw[0]), .din2(din[1]), .din1(din[0]), .b2(b_t[0]),
    .B(b_t[1]), .addr(addr), .w(WE_t), .rw(W));
  Multiplexer #(.enable("false")) multiplexer_3 (.in0(WE_t), .in1(1'b1), .out(WE), .sel(and_4_out));
  and and_4 (and_4_out, r, rtype);
  Multiplexer #(.width(4), .enable("false")) multiplexer_4 (
    .in0(opctr_1_alu1), .in1(funcctr_1_alu1), .out(aluop), .sel(rtype));
endmodule

module opctr (
  input  op6,
  input  op5,
  input  op4,
  input  op3,
  input  op2,
  input  op1,
  output alu4,
  output alu3,
  output alu2,
  output alu1
);

  wire and_1_out, and_2_out, and_3_out, and_4_out, and_5_out, and_6_out, and_7_out, and_8_out, and_9_out,
       and_10_out, and_11_out, and_12_out, and_13_out, and_14_out, and_15_out, not_1_out, not_2_out,
       not_3_out, not_4_out, not_5_out, not_6_out, not_7_out, not_8_out, not_9_out, not_10_out, not_11_out,
       not_12_out, not_13_out, not_14_out, not_15_out, not_16_out, not_17_out, not_18_out, not_19_out,
       not_20_out, not_21_out, not_22_out, not_23_out;

  not not_1 (not_1_out, op6);
  not not_2 (not_2_out, op5);
  not not_3 (not_3_out, op4);
  not not_4 (not_4_out, op6);
  not not_5 (not_5_out, op1);
  not not_6 (not_6_out, op2);
  not not_7 (not_7_out, op1);
  not not_8 (not_8_out, op3);
  not not_9 (not_9_out, op2);
  not not_10 (not_10_out, op3);
  not not_11 (not_11_out, op2);
  not not_12 (not_12_out, op5);
  not not_13 (not_13_out, op3);
  not not_14 (not_14_out, op5);
  not not_15 (not_15_out, op4);
  not not_16 (not_16_out, op3);
  not not_17 (not_17_out, op2);
  not not_18 (not_18_out, op2);
  not not_19 (not_19_out, op1);
  not not_20 (not_20_out, op2);
  not not_21 (not_21_out, op1);
  not not_22 (not_22_out, op3);
  not not_23 (not_23_out, op1);
  and and_1 (and_1_out, not_1_out, not_2_out, not_3_out, op1);
  and and_2 (and_2_out, not_4_out, op2);
  and and_3 (and_3_out, op2, not_5_out);
  and and_4 (and_4_out, op3, op1);
  and and_5 (and_5_out, op5, op2);
  and and_6 (and_6_out, not_6_out, not_7_out);
  and and_7 (and_7_out, op4, not_8_out, not_9_out);
  and and_8 (and_8_out, op5, not_10_out, not_11_out);
  and and_9 (and_9_out, op6, not_12_out, not_13_out, op1);
  and and_10 (and_10_out, not_14_out, not_15_out, not_16_out, not_17_out, op1);
  and and_11 (and_11_out, op3, not_18_out, not_19_out);
  and and_12 (and_12_out, op6, not_20_out);
  and and_13 (and_13_out, op6, not_21_out);
  and and_14 (and_14_out, op6, op3);
  and and_15 (and_15_out, op6, op5);
  or or_1 (alu1, not_22_out, not_23_out);
  or or_2 (alu4, and_1_out, and_2_out, and_3_out, and_4_out, and_5_out);
  or or_3 (alu3, and_6_out, and_7_out, and_8_out, and_9_out);
  or or_4 (alu2, and_10_out, and_11_out, and_12_out, and_13_out, and_14_out, and_15_out);
endmodule

module funcctr (
  input  func6,
  input  func5,
  input  func4,
  input  func3,
  input  func2,
  input  func1,
  output alu4,
  output alu3,
  output alu2,
  output alu1,
  output sll,
  output jr,
  output r
);

  wire and_1_out, and_2_out, and_3_out, and_4_out, and_5_out, and_6_out, and_7_out, and_8_out, and_9_out,
       and_10_out, and_11_out, and_12_out, and_13_out, and_14_out, and_15_out, and_16_out, and_17_out,
       and_18_out, and_20_out, and_21_out, and_22_out, and_23_out, and_24_out, not_1_out, not_2_out,
       not_3_out, not_4_out, not_5_out, not_6_out, not_7_out, not_8_out, not_9_out, not_10_out, not_11_out,
       not_12_out, not_13_out, not_14_out, not_15_out, not_16_out, not_17_out, not_18_out, not_19_out,
       not_20_out, not_21_out, not_22_out, not_23_out, not_24_out, not_25_out, not_26_out, not_27_out,
       not_28_out, not_29_out, not_30_out, not_31_out, not_32_out, not_33_out, not_34_out, not_35_out,
       not_36_out, not_37_out, not_38_out, not_39_out, not_40_out, not_41_out, not_42_out, not_43_out,
       not_44_out, not_45_out, not_46_out, not_47_out, not_48_out, not_49_out, not_50_out, not_51_out,
       not_52_out, not_53_out, not_54_out, not_55_out;

  and and_1 (and_1_out, func3, func1);
  and and_2 (and_2_out, func3, func2);
  not not_1 (not_1_out, func4);
  not not_2 (not_2_out, func3);
  not not_3 (not_3_out, func2);
  not not_4 (not_4_out, func1);
  not not_5 (not_5_out, func5);
  not not_6 (not_6_out, func4);
  not not_7 (not_7_out, func3);
  not not_8 (not_8_out, func1);
  not not_9 (not_9_out, func2);
  not not_10 (not_10_out, func1);
  not not_11 (not_11_out, func4);
  not not_12 (not_12_out, func4);
  not not_13 (not_13_out, func4);
  not not_14 (not_14_out, func3);
  not not_15 (not_15_out, func3);
  not not_16 (not_16_out, func1);
  not not_17 (not_17_out, func6);
  not not_18 (not_18_out, func5);
  not not_19 (not_19_out, func4);
  not not_20 (not_20_out, func3);
  not not_21 (not_21_out, func1);
  not not_22 (not_22_out, func1);
  not not_23 (not_23_out, func6);
  not not_24 (not_24_out, func1);
  not not_25 (not_25_out, func3);
  not not_26 (not_26_out, func2);
  not not_27 (not_27_out, func6);
  not not_28 (not_28_out, func5);
  not not_29 (not_29_out, func4);
  not not_30 (not_30_out, func3);
  not not_31 (not_31_out, func1);
  not not_32 (not_32_out, func6);
  not not_33 (not_33_out, func5);
  not not_34 (not_34_out, func4);
  not not_35 (not_35_out, func3);
  not not_36 (not_36_out, func6);
  not not_37 (not_37_out, func5);
  not not_38 (not_38_out, func3);
  not not_39 (not_39_out, func2);
  not not_40 (not_40_out, func1);
  not not_41 (not_41_out, func5);
  not not_42 (not_42_out, func4);
  not not_43 (not_43_out, func3);
  not not_44 (not_44_out, func1);
  not not_45 (not_45_out, func6);
  not not_46 (not_46_out, func5);
  not not_47 (not_47_out, func4);
  not not_48 (not_48_out, func3);
  not not_49 (not_49_out, func5);
  not not_50 (not_50_out, func4);
  not not_51 (not_51_out, func2);
  not not_52 (not_52_out, func5);
  not not_53 (not_53_out, func4);
  not not_54 (not_54_out, func5);
  not not_55 (not_55_out, func3);
  or or_1 (alu4, and_1_out, and_2_out, func4);
  and and_3 (and_3_out, func4, func1);
  and and_4 (and_4_out, func6, not_1_out, not_2_out);
  and and_5 (and_5_out, func6, not_3_out, not_4_out);
  and and_6 (and_6_out, not_5_out, not_6_out, not_7_out, func2, not_8_out);
  and and_7 (and_7_out, func3, not_9_out, not_10_out);
  and and_8 (and_8_out, not_11_out, func3, func2, func1);
  and and_9 (and_9_out, func5, not_12_out, func2, func1);
  and and_10 (and_10_out, func6, not_13_out, not_14_out, func2);
  and and_11 (and_11_out, func6, not_15_out, func2, not_16_out);
  and and_12 (and_12_out, not_17_out, not_18_out, not_19_out, not_20_out, func2, func1);
  and and_13 (and_13_out, func3, not_21_out);
  and and_14 (and_14_out, func4, not_22_out);
  and and_15 (and_15_out, not_23_out, func5, func2, not_24_out);
  and and_16 (and_16_out, func6, not_25_out, not_26_out);
  and and_17 (and_17_out, not_27_out, not_28_out, not_29_out, not_30_out, not_31_out);
  and and_18 (and_18_out, not_32_out, not_33_out, not_34_out, not_35_out, func2);
  and and_19 (jr, not_36_out, not_37_out, func4, not_38_out, not_39_out, not_40_out);
  and and_20 (and_20_out, not_41_out, not_42_out, not_43_out, not_44_out);
  and and_21 (and_21_out, not_45_out, not_46_out, not_47_out, not_48_out, func2);
  and and_22 (and_22_out, func6, not_49_out, not_50_out, not_51_out);
  and and_23 (and_23_out, func6, not_52_out, not_53_out, func3);
  and and_24 (and_24_out, func6, not_54_out, func4, not_55_out, func2);
  or or_2 (alu3, and_3_out, and_4_out, and_5_out);
  or or_3 (alu2, and_6_out, and_7_out, and_8_out, and_9_out, and_10_out, and_11_out);
  or or_4 (alu1, and_12_out, and_13_out, and_14_out, and_15_out, and_16_out);
  or or_5 (sll, and_17_out, and_18_out);
  or or_6 (r, and_20_out, and_21_out, and_22_out, and_23_out, and_24_out);
endmodule

module alu (
  input  [31:0] A,
  input  [31:0] B,
  input  [3:0] op,
  output [31:0] R,
  output les,
  output out_6
);

  ALU alu_1 (
    .AluOP(op), .X(A), .Equal(out_6), .Result(R), .Y(B));  // open: Signed_Overflow, Result_2, UnSigned_Overflow

  assign les = A[31];

  // Other names for the same wires on the sheet: aluop[3:0] = op
endmodule

module we (
  input  op6,
  input  op5,
  input  op4,
  input  op3,
  input  op2,
  input  op1,
  output pc3,
  output pc2,
  output pc1,
  output rw2,
  output rw1,
  output din2,
  output din1,
  output b2,
  output B,
  output addr,
  output w,
  output rw
);

  wire and_3_out, and_4_out, and_5_out, and_6_out, and_7_out, and_8_out, and_9_out, and_13_out, and_15_out,
       and_16_out, and_17_out, and_18_out, not_1_out, not_2_out, not_3_out, not_4_out, not_5_out, not_6_out,
       not_7_out, not_8_out, not_9_out, not_10_out, not_11_out, not_12_out, not_13_out, not_14_out,
       not_15_out, not_16_out, not_17_out, not_18_out, not_19_out, not_20_out, not_21_out, not_22_out,
       not_23_out, not_24_out, not_25_out, not_26_out, not_27_out, not_28_out, not_29_out, not_30_out,
       not_31_out, not_32_out, not_33_out, not_34_out, not_35_out, not_36_out, not_37_out, not_38_out,
       not_39_out, not_40_out, not_41_out, not_42_out, not_43_out, not_44_out, not_45_out, not_46_out,
       not_47_out, not_48_out;

  not not_1 (not_1_out, op6);
  not not_2 (not_2_out, op5);
  not not_3 (not_3_out, op4);
  not not_4 (not_4_out, op2);
  not not_5 (not_5_out, op6);
  not not_6 (not_6_out, op5);
  not not_7 (not_7_out, op4);
  not not_8 (not_8_out, op3);
  not not_9 (not_9_out, op6);
  not not_10 (not_10_out, op5);
  not not_11 (not_11_out, op4);
  not not_12 (not_12_out, op2);
  not not_13 (not_13_out, op6);
  not not_14 (not_14_out, op5);
  not not_15 (not_15_out, op4);
  not not_16 (not_16_out, op3);
  not not_17 (not_17_out, op6);
  not not_18 (not_18_out, op5);
  not not_19 (not_19_out, op3);
  not not_20 (not_20_out, op6);
  not not_21 (not_21_out, op5);
  not not_22 (not_22_out, op4);
  not not_23 (not_23_out, op3);
  not not_24 (not_24_out, op4);
  not not_25 (not_25_out, op6);
  not not_26 (not_26_out, op5);
  not not_27 (not_27_out, op4);
  not not_28 (not_28_out, op3);
  not not_29 (not_29_out, op2);
  not not_30 (not_30_out, op6);
  not not_31 (not_31_out, op5);
  not not_32 (not_32_out, op3);
  not not_33 (not_33_out, op5);
  not not_34 (not_34_out, op3);
  not not_35 (not_35_out, op5);
  not not_36 (not_36_out, op4);
  not not_37 (not_37_out, op3);
  not not_38 (not_38_out, op6);
  not not_39 (not_39_out, op5);
  not not_40 (not_40_out, op2);
  not not_41 (not_41_out, op6);
  not not_42 (not_42_out, op5);
  not not_43 (not_43_out, op1);
  not not_44 (not_44_out, op5);
  not not_45 (not_45_out, op3);
  not not_46 (not_46_out, op1);
  not not_47 (not_47_out, op5);
  not not_48 (not_48_out, op3);
  and and_1 (pc3, not_1_out, not_2_out, not_3_out, op3, not_4_out);
  and and_2 (pc2, not_5_out, not_6_out, not_7_out, not_8_out, op2);
  and and_3 (and_3_out, not_9_out, not_10_out, not_11_out, not_12_out, op1);
  and and_4 (and_4_out, not_13_out, not_14_out, not_15_out, not_16_out, op2);
  and and_5 (and_5_out, not_17_out, op2, op1);
  and and_6 (and_6_out, op3, op2, op1);
  and and_7 (and_7_out, op4, op2, op1);
  and and_8 (and_8_out, op5, op2, op1);
  and and_9 (and_9_out, op6, not_18_out, not_19_out, op2, op1);
  and and_10 (din2, not_20_out, not_21_out, not_22_out, not_23_out, op2);
  and and_11 (din1, op6, not_24_out);
  and and_12 (b2, not_25_out, not_26_out, not_27_out, not_28_out, not_29_out, op1);
  and and_13 (and_13_out, not_30_out, not_31_out, not_32_out, op1);
  and and_14 (addr, op6, not_33_out, op4, not_34_out, op2, op1);
  and and_15 (and_15_out, not_35_out, not_36_out, not_37_out, op2, op1);
  and and_16 (and_16_out, not_38_out, not_39_out, op4, not_40_out);
  and and_17 (and_17_out, not_41_out, not_42_out, op4, op3, not_43_out);
  and and_18 (and_18_out, op6, not_44_out, op4, not_45_out, op2, not_46_out);
  and and_19 (rw, op6, not_47_out, op4, not_48_out, op2, op1);
  or or_1 (pc1, and_3_out, and_4_out);
  or or_2 (rw2, and_5_out, and_6_out, and_7_out, and_8_out);
  or or_3 (rw1, op4, and_9_out);
  or or_4 (B, and_13_out, op2, op4);
  or or_5 (w, and_15_out, and_16_out, and_17_out, and_18_out);
endmodule

module npc (
  input  [9:0] pc,
  input  [25:0] addr,
  input  [2:0] p,
  input  [31:0] rs,
  input  [15:0] offset,
  input  less,
  input  equ,
  output [9:0] out,
  output [9:0] pc11
);

  wire not_1_out;
  wire [9:0] adder_1_out, adder_2_out, incrementer_1_p2, multiplexer_1_out, multiplexer_2_out,
       multiplexer_3_out, multiplexer_4_out, multiplexer_5_out;

  Multiplexer #(.width(10), .enable("false")) multiplexer_1 (
    .in0(10'h1), .in1(offset[9:0]), .out(multiplexer_1_out));  // open: sel
  Adder #(.width(10)) adder_1 (.a(pc), .b(offset[9:0]), .out(adder_1_out));  // open: cin, cout
  Adder #(.width(10)) adder_2 (.a(pc), .b(multiplexer_1_out), .out(adder_2_out));  // open: cin, cout
  // Incrementer incrementer_1: pin names not known; wires that end beside it: adder_1_out, incrementer_1_p2
  Multiplexer #(.width(10), .enable("false")) multiplexer_2 (
    .in0(pc11), .in1(incrementer_1_p2), .out(multiplexer_2_out), .sel(equ));
  Multiplexer #(.width(10), .enable("false")) multiplexer_3 (
    .in0(pc11), .in1(incrementer_1_p2), .out(multiplexer_3_out), .sel(not_1_out));
  not not_1 (not_1_out, equ);
  Multiplexer #(.width(10), .enable("false")) multiplexer_4 (
    .in0(rs[9:0]), .in1(addr[9:0]), .out(multiplexer_4_out));  // open: sel
  Multiplexer #(.width(10), .enable("false")) multiplexer_5 (
    .in0(pc11), .in1(adder_1_out), .out(multiplexer_5_out), .sel(less));
  Multiplexer #(.width(10), .enable("false")) multiplexer_6 (
    .in0(adder_2_out), .in1(multiplexer_4_out), .out(out));  // open: sel
  // Incrementer incrementer_2: pin names not known; wires that end beside it: pc, pc11
  Multiplexer #(.select(3), .width(10), .enable("false")) multiplexer_7 (
    .in0(pc11), .in1(multiplexer_5_out), .in2(rs[9:0]), .in3(addr[9:0]), .in4(multiplexer_2_out),
    .in5(multiplexer_3_out), .in6(pc11), .in7(pc11), .out(out), .sel(p));

  // Other names for the same wires on the sheet: p11[9:0] = pc11
endmodule

module regfile (
  input  [31:0] w,
  input  clk,
  input  we,
  input  [4:0] rw,
  input  [4:0] ra,
  input  [4:0] rb,
  output [31:0] a,
  output [31:0] b
);

  // RegisterFile registerfile_1: pin names not known; wires that end beside it: w, clk, we, rw, ra, rb, a, b
endmodule

module if_id (
  input  [31:0] instrucion,
  input  [9:0] pc,
  input  \传输状态In ,
  input  CLK,
  input  \同步清零 ,
  output [31:0] insout,
  output [9:0] pcout,
  output \传输状态Out 
);

  wire multiplexer_3_out;
  wire [9:0] multiplexer_2_out;
  wire [31:0] multiplexer_1_out;

  // Probe on pc
  Multiplexer #(.width(32), .enable("false")) multiplexer_1 (
    .in0(instrucion), .in1({32{1'b0}}), .out(multiplexer_1_out), .sel(\同步清零 ));
  Multiplexer #(.width(10), .enable("false")) multiplexer_2 (
    .in0(pc), .in1({10{1'b0}}), .out(multiplexer_2_out), .sel(\同步清零 ));
  Multiplexer #(.enable("false")) multiplexer_3 (.in0(\传输状态In ), .in1(1'b0), .out(multiplexer_3_out), .sel(\同步清零 ));
  Register #(.width(32)) register_1 (.D(multiplexer_1_out), .en(\传输状态In ), .Q(insout), .clk(CLK));  // open: clr
  Register #(.width(10)) register_2 (.D(multiplexer_2_out), .en(\传输状态In ), .Q(pcout), .clk(CLK));  // open: clr
  Register #(.width(1)) register_3 (.D(multiplexer_3_out), .en(\传输状态In ), .Q(\传输状态Out ), .clk(CLK));  // open: clr
endmodule

module id_ex (
  input  [9:0] pc,
  input  [31:0] a,
  input  [31:0] b,
  input  [3:0] aluop,
  input  [31:0] imme,
  input  W,
  input  We,
  input  sys,
  input  A_2,
  input  [1:0] B_2,
  input  [1:0] din,
  input  [2:0] pcctr,
  input  [4:0] rw,
  input  [4:0] ra,
  input  [4:0] rb,
  input  \传输状态In ,
  input  CLK,
  input  \同步清零 ,
  output [9:0] pcout,
  output [31:0] a_3,
  output [31:0] b_3,
  output [3:0] aluopout,
  output [31:0] immeout,
  output Wout,
  output Weout,
  output sysout,
  output Aout,
  output [1:0] Bout,
  output [1:0] dinout,
  output [2:0] pcctrout,
  output [4:0] rwout,
  output [4:0] raout,
  output [4:0] rbout,
  output \传输状态Out 
);

  wire multiplexer_6_out, multiplexer_7_out, multiplexer_8_out, multiplexer_9_out, multiplexer_16_out;
  wire [1:0] multiplexer_10_out, multiplexer_11_out;
  wire [2:0] multiplexer_12_out;
  wire [3:0] multiplexer_4_out;
  wire [4:0] multiplexer_13_out, multiplexer_14_out, multiplexer_15_out;
  wire [9:0] multiplexer_1_out;
  wire [31:0] multiplexer_2_out, multiplexer_3_out, multiplexer_5_out;

  Multiplexer #(.width(10), .enable("false")) multiplexer_1 (
    .in0(pc), .in1({10{1'b0}}), .out(multiplexer_1_out), .sel(\同步清零 ));
  Multiplexer #(.width(32), .enable("false")) multiplexer_2 (
    .in0(a), .in1({32{1'b0}}), .out(multiplexer_2_out), .sel(\同步清零 ));
  Multiplexer #(.width(32), .enable("false")) multiplexer_3 (
    .in0(b), .in1({32{1'b0}}), .out(multiplexer_3_out), .sel(\同步清零 ));
  Multiplexer #(.width(4), .enable("false")) multiplexer_4 (
    .in0(aluop), .in1(4'b0000), .out(multiplexer_4_out), .sel(\同步清零 ));
  Multiplexer #(.width(32), .enable("false")) multiplexer_5 (
    .in0(imme), .in1({32{1'b0}}), .out(multiplexer_5_out), .sel(\同步清零 ));
  Multiplexer #(.enable("false")) multiplexer_6 (.in0(W), .in1(1'b0), .out(multiplexer_6_out), .sel(\同步清零 ));
  Multiplexer #(.enable("false")) multiplexer_7 (.in0(We), .in1(1'b0), .out(multiplexer_7_out), .sel(\同步清零 ));
  Multiplexer #(.enable("false")) multiplexer_8 (.in0(sys), .in1(1'b0), .out(multiplexer_8_out), .sel(\同步清零 ));
  Multiplexer #(.enable("false")) multiplexer_9 (.in0(A_2), .in1(1'b0), .out(multiplexer_9_out), .sel(\同步清零 ));
  Multiplexer #(.width(2), .enable("false")) multiplexer_10 (
    .in0(B_2), .in1(2'b00), .out(multiplexer_10_out), .sel(\同步清零 ));
  Multiplexer #(.width(2), .enable("false")) multiplexer_11 (
    .in0(din), .in1(2'b00), .out(multiplexer_11_out), .sel(\同步清零 ));
  Multiplexer #(.width(3), .enable("false")) multiplexer_12 (
    .in0(pcctr), .in1(3'b000), .out(multiplexer_12_out), .sel(\同步清零 ));
  Multiplexer #(.width(5), .enable("false")) multiplexer_13 (
    .in0(rw), .in1({5{1'b0}}), .out(multiplexer_13_out), .sel(\同步清零 ));
  Multiplexer #(.width(5), .enable("false")) multiplexer_14 (
    .in0(ra), .in1({5{1'b0}}), .out(multiplexer_14_out), .sel(\同步清零 ));
  Multiplexer #(.width(5), .enable("false")) multiplexer_15 (
    .in0(rb), .in1({5{1'b0}}), .out(multiplexer_15_out), .sel(\同步清零 ));
  Multiplexer #(.enable("false")) multiplexer_16 (.in0(\传输状态In ), .in1(1'b0), .out(multiplexer_16_out), .sel(\同步清零 ));
  Register #(.width(10)) register_1 (.D(multiplexer_1_out), .en(\传输状态In ), .Q(pcout), .clk(CLK));  // open: clr
  Register #(.width(32)) register_2 (.D(multiplexer_2_out), .en(\传输状态In ), .Q(a_3), .clk(CLK));  // open: clr
  Register #(.width(32)) register_3 (.D(multiplexer_3_out), .en(\传输状态In ), .Q(b_3), .clk(CLK));  // open: clr
  Register #(.width(4)) register_4 (.D(multiplexer_4_out), .en(\传输状态In ), .Q(aluopout), .clk(CLK));  // open: clr
  Register #(.width(32)) register_5 (.D(multiplexer_5_out), .en(\传输状态In ), .Q(immeout), .clk(CLK));  // open: clr
  Register #(.width(1)) register_6 (.D(multiplexer_6_out), .en(\传输状态In ), .Q(Wout), .clk(CLK));  // open: clr
  Register #(.width(1)) register_7 (.D(multiplexer_7_out), .en(\传输状态In ), .Q(Weout), .clk(CLK));  // open: clr
  Register #(.width(1)) register_8 (.D(multiplexer_8_out), .en(\传输状态In ), .Q(sysout), .clk(CLK));  // open: clr
  Register #(.width(1)) register_9 (.D(multiplexer_9_out), .en(\传输状态In ), .Q(Aout), .clk(CLK));  // open: clr
  Register #(.width(2)) register_10 (.D(multiplexer_10_out), .en(\传输状态In ), .Q(Bout), .clk(CLK));  // open: clr
  Register #(.width(2)) register_11 (.D(multiplexer_11_out), .en(\传输状态In ), .Q(dinout), .clk(CLK));  // open: clr
  Register #(.width(3)) register_12 (.D(multiplexer_12_out), .en(\传输状态In ), .Q(pcctrout), .clk(CLK));  // open: clr
  Register #(.width(5)) register_13 (.D(multiplexer_13_out), .en(\传输状态In ), .Q(rwout), .clk(CLK));  // open: clr
  Register #(.width(5)) register_14 (.D(multiplexer_14_out), .en(\传输状态In ), .Q(raout), .clk(CLK));  // open: clr
  Register #(.width(5)) register_15 (.D(multiplexer_15_out), .en(\传输状态In ), .Q(rbout), .clk(CLK));  // open: clr
  Register #(.width(1)) register_16 (.D(multiplexer_16_out), .en(\传输状态In ), .Q(\传输状态Out ), .clk(CLK));  // open: clr
endmodule

module ex_mem (
  input  [31:0] addr,
  input  [31:0] data,
  input  sel,
  input  we,
  input  sys,
  input  [31:0] v0,
  input  [1:0] din,
  input  [4:0] rw,
  input  [31:0] pc,
  input  [9:0] pcins,
  input  [31:0] op,
  input  \传输状态In ,
  input  CLK,
  input  \同步清零 ,
  output [31:0] addrout,
  output [31:0] dataout,
  output selout,
  output weout,
  output sysout,
  output [31:0] v0out,
  output [1:0] dinout,
  output [4:0] rwout,
  output [31:0] pcout,
  output [9:0] pcout_2,
  output [31:0] op_2,
  output \传输状态Out 
);

  wire multiplexer_3_out, multiplexer_4_out, multiplexer_5_out, multiplexer_12_out;
  wire [1:0] multiplexer_7_out;
  wire [4:0] multiplexer_8_out;
  wire [9:0] multiplexer_10_out;
  wire [31:0] multiplexer_1_out, multiplexer_2_out, multiplexer_6_out, multiplexer_9_out, multiplexer_11_out;

  Multiplexer #(.width(32), .enable("false")) multiplexer_1 (
    .in0(addr), .in1({32{1'b0}}), .out(multiplexer_1_out), .sel(\同步清零 ));
  Multiplexer #(.width(32), .enable("false")) multiplexer_2 (
    .in0(data), .in1({32{1'b0}}), .out(multiplexer_2_out), .sel(\同步清零 ));
  Multiplexer #(.enable("false")) multiplexer_3 (.in0(sel), .in1(1'b0), .out(multiplexer_3_out), .sel(\同步清零 ));
  Multiplexer #(.enable("false")) multiplexer_4 (.in0(we), .in1(1'b0), .out(multiplexer_4_out), .sel(\同步清零 ));
  Multiplexer #(.enable("false")) multiplexer_5 (.in0(sys), .in1(1'b0), .out(multiplexer_5_out), .sel(\同步清零 ));
  Multiplexer #(.width(32), .enable("false")) multiplexer_6 (
    .in0(v0), .in1({32{1'b0}}), .out(multiplexer_6_out), .sel(\同步清零 ));
  Multiplexer #(.width(2), .enable("false")) multiplexer_7 (
    .in0(din), .in1(2'b00), .out(multiplexer_7_out), .sel(\同步清零 ));
  Multiplexer #(.width(5), .enable("false")) multiplexer_8 (
    .in0(rw), .in1({5{1'b0}}), .out(multiplexer_8_out), .sel(\同步清零 ));
  Multiplexer #(.width(32), .enable("false")) multiplexer_9 (
    .in0(pc), .in1({32{1'b0}}), .out(multiplexer_9_out), .sel(\同步清零 ));
  Multiplexer #(.width(10), .enable("false")) multiplexer_10 (
    .in0(pcins), .in1({10{1'b0}}), .out(multiplexer_10_out), .sel(\同步清零 ));
  Multiplexer #(.width(32), .enable("false")) multiplexer_11 (
    .in0(op), .in1({32{1'b0}}), .out(multiplexer_11_out), .sel(\同步清零 ));
  Multiplexer #(.enable("false")) multiplexer_12 (.in0(\传输状态In ), .in1(1'b0), .out(multiplexer_12_out), .sel(\同步清零 ));
  Register #(.width(32)) register_1 (.D(multiplexer_1_out), .en(\传输状态In ), .Q(addrout), .clk(CLK));  // open: clr
  Register #(.width(32)) register_2 (.D(multiplexer_2_out), .en(\传输状态In ), .Q(dataout), .clk(CLK));  // open: clr
  Register #(.width(1)) register_3 (.D(multiplexer_3_out), .en(\传输状态In ), .Q(selout), .clk(CLK));  // open: clr
  Register #(.width(1)) register_4 (.D(multiplexer_4_out), .en(\传输状态In ), .Q(weout), .clk(CLK));  // open: clr
  Register #(.width(1)) register_5 (.D(multiplexer_5_out), .en(\传输状态In ), .Q(sysout), .clk(CLK));  // open: clr
  Register #(.width(32)) register_6 (.D(multiplexer_6_out), .en(\传输状态In ), .Q(v0out), .clk(CLK));  // open: clr
  Register #(.width(2)) register_7 (.D(multiplexer_7_out), .en(\传输状态In ), .Q(dinout), .clk(CLK));  // open: clr
  Register #(.width(5)) register_8 (.D(multiplexer_8_out), .en(\传输状态In ), .Q(rwout), .clk(CLK));  // open: clr
  Register #(.width(32)) register_9 (.D(multiplexer_9_out), .en(\传输状态In ), .Q(pcout), .clk(CLK));  // open: clr
  Register #(.width(10)) register_10 (.D(multiplexer_10_out), .en(\传输状态In ), .Q(pcout_2), .clk(CLK));  // open: clr
  Register #(.width(32)) register_11 (.D(multiplexer_11_out), .en(\传输状态In ), .Q(op_2), .clk(CLK));  // open: clr
  Register #(.width(1)) register_12 (.D(multiplexer_12_out), .en(\传输状态In ), .Q(\传输状态Out ), .clk(CLK));  // open: clr
endmodule

module mem_wb (
  input  [31:0] instrucion,
  input  sys,
  input  we,
  input  [31:0] data,
  input  [31:0] alu,
  input  [31:0] v0,
  input  [31:0] a0,
  input  [4:0] rw,
  input  [1:0] din,
  input  [9:0] pc,
  input  [31:0] op,
  input  \传输状态In ,
  input  CLK,
  input  \同步清零 ,
  output [31:0] insout,
  output sysout,
  output weout,
  output [31:0] dataout,
  output [31:0] aluout,
  output [31:0] v0out,
  output [31:0] a0out,
  output [4:0] rwout,
  output [1:0] dinout,
  output [9:0] pcout,
  output [31:0] op_2,
  output \传输状态Out 
);

  wire multiplexer_2_out, multiplexer_3_out, multiplexer_12_out;
  wire [1:0] multiplexer_9_out;
  wire [4:0] multiplexer_8_out;
  wire [9:0] multiplexer_10_out;
  wire [31:0] multiplexer_1_out, multiplexer_4_out, multiplexer_5_out, multiplexer_6_out, multiplexer_7_out,
       multiplexer_11_out;

  Multiplexer #(.width(32), .enable("false")) multiplexer_1 (
    .in0(instrucion), .in1({32{1'b0}}), .out(multiplexer_1_out), .sel(\同步清零 ));
  Multiplexer #(.enable("false")) multiplexer_2 (.in0(sys), .in1(1'b0), .out(multiplexer_2_out), .sel(\同步清零 ));
  Multiplexer #(.enable("false")) multiplexer_3 (.in0(we), .in1(1'b0), .out(multiplexer_3_out), .sel(\同步清零 ));
  Multiplexer #(.width(32), .enable("false")) multiplexer_4 (
    .in0(data), .in1({32{1'b0}}), .out(multiplexer_4_out), .sel(\同步清零 ));
  Multiplexer #(.width(32), .enable("false")) multiplexer_5 (
    .in0(alu), .in1({32{1'b0}}), .out(multiplexer_5_out), .sel(\同步清零 ));
  Multiplexer #(.width(32), .enable("false")) multiplexer_6 (
    .in0(v0), .in1({32{1'b0}}), .out(multiplexer_6_out), .sel(\同步清零 ));
  Multiplexer #(.width(32), .enable("false")) multiplexer_7 (
    .in0(a0), .in1({32{1'b0}}), .out(multiplexer_7_out), .sel(\同步清零 ));
  Multiplexer #(.width(5), .enable("false")) multiplexer_8 (
    .in0(rw), .in1({5{1'b0}}), .out(multiplexer_8_out), .sel(\同步清零 ));
  Multiplexer #(.width(2), .enable("false")) multiplexer_9 (
    .in0(din), .in1(2'b00), .out(multiplexer_9_out), .sel(\同步清零 ));
  Multiplexer #(.width(10), .enable("false")) multiplexer_10 (
    .in0(pc), .in1({10{1'b0}}), .out(multiplexer_10_out), .sel(\同步清零 ));
  Multiplexer #(.width(32), .enable("false")) multiplexer_11 (
    .in0(op), .in1({32{1'b0}}), .out(multiplexer_11_out), .sel(\同步清零 ));
  Multiplexer #(.enable("false")) multiplexer_12 (.in0(\传输状态In ), .in1(1'b0), .out(multiplexer_12_out), .sel(\同步清零 ));
  Register #(.width(32)) register_1 (.D(multiplexer_1_out), .en(\传输状态In ), .Q(insout), .clk(CLK));  // open: clr
  Register #(.width(1)) register_2 (.D(multiplexer_2_out), .en(\传输状态In ), .Q(sysout), .clk(CLK));  // open: clr
  Register #(.width(1)) register_3 (.D(multiplexer_3_out), .en(\传输状态In ), .Q(weout), .clk(CLK));  // open: clr
  Register #(.width(32)) register_4 (.D(multiplexer_4_out), .en(\传输状态In ), .Q(dataout), .clk(CLK));  // open: clr
  Register #(.width(32)) register_5 (.D(multiplexer_5_out), .en(\传输状态In ), .Q(aluout), .clk(CLK));  // open: clr
  Register #(.width(32)) register_6 (.D(multiplexer_6_out), .en(\传输状态In ), .Q(v0out), .clk(CLK));  // open: clr
  Register #(.width(32)) register_7 (.D(multiplexer_7_out), .en(\传输状态In ), .Q(a0out), .clk(CLK));  // open: clr
  Register #(.width(5)) register_8 (.D(multiplexer_8_out), .en(\传输状态In ), .Q(rwout), .clk(CLK));  // open: clr
  Register #(.width(2)) register_9 (.D(multiplexer_9_out), .en(\传输状态In ), .Q(dinout), .clk(CLK));  // open: clr
  Register #(.width(10)) register_10 (.D(multiplexer_10_out), .en(\传输状态In ), .Q(pcout), .clk(CLK));  // open: clr
  Register #(.width(32)) register_11 (.D(multiplexer_11_out), .en(\传输状态In ), .Q(op_2), .clk(CLK));  // open: clr
  Register #(.width(1)) register_12 (.D(multiplexer_12_out), .en(\传输状态In ), .Q(\传输状态Out ), .clk(CLK));  // open: clr
endmodule

module jump (
  input  [2:0] jump,
  input  eq,
  input  le,
  output jumpctr
);

  wire and_1_out, and_2_out, and_3_out, comparator_1_eq, comparator_2_eq, comparator_3_eq, comparator_4_eq,
       comparator_5_eq, not_1_out, \无条件分支指令数 , \有条件分支成功跳转 ;

  or or_1 (jumpctr, \无条件分支指令数 , \有条件分支成功跳转 );
  Comparator #(.width(3)) comparator_1 (.a(jump), .b(3'b010), .eq(comparator_1_eq));  // open: gt, lt
  Comparator #(.width(3)) comparator_2 (.a(jump), .b(3'b011), .eq(comparator_2_eq));  // open: gt, lt
  Comparator #(.width(3)) comparator_3 (.a(jump), .b(3'b001), .eq(comparator_3_eq));  // open: gt, lt
  Comparator #(.width(3)) comparator_4 (.a(jump), .b(3'b100), .eq(comparator_4_eq));  // open: gt, lt
  Comparator #(.width(3)) comparator_5 (.a(jump), .b(3'b101), .eq(comparator_5_eq));  // open: gt, lt
  or or_2 (\无条件分支指令数 , comparator_1_eq, comparator_2_eq);
  not not_1 (not_1_out, eq);
  and and_1 (and_1_out, comparator_3_eq, le);
  or or_3 (\有条件分支成功跳转 , and_1_out, and_2_out, and_3_out);
  and and_2 (and_2_out, comparator_4_eq, eq);
  and and_3 (and_3_out, comparator_5_eq, not_1_out);
endmodule

module redirection (
  input  [4:0] ra0,
  input  [4:0] rb0,
  input  [4:0] ra,
  input  [4:0] rb,
  input  [31:0] op,
  input  [4:0] rw1,
  input  we1,
  input  [4:0] rw2,
  input  we2,
  input  [4:0] rw0,
  output rw1a,
  output rw1b,
  output rw2a,
  output rw2b,
  output lw
);

  wire comparator_1_eq, comparator_2_eq, comparator_3_eq, comparator_4_eq, comparator_5_eq, comparator_6_eq,
       comparator_7_eq, or_1_out;

  Comparator #(.width(5)) comparator_1 (.a(ra), .b(rw1), .eq(comparator_1_eq));  // open: gt, lt
  Comparator #(.width(5)) comparator_2 (.a(rb), .b(rw1), .eq(comparator_2_eq));  // open: gt, lt
  Comparator #(.width(5)) comparator_3 (.a(ra), .b(rw2), .eq(comparator_3_eq));  // open: gt, lt
  Comparator #(.width(5)) comparator_4 (.a(rb), .b(rw2), .eq(comparator_4_eq));  // open: gt, lt
  Comparator #(.width(6)) comparator_5 (.a(op[31:26]), .b(6'b100011), .eq(comparator_5_eq));  // open: gt, lt
  and and_1 (rw1a, comparator_1_eq, we1);
  and and_2 (rw1b, we1, comparator_2_eq);
  and and_3 (rw2a, comparator_3_eq, we2);
  and and_4 (rw2b, we2, comparator_4_eq);
  Comparator #(.width(5)) comparator_6 (.a(ra0), .b(rw0), .eq(comparator_6_eq));  // open: gt, lt
  Comparator #(.width(5)) comparator_7 (.a(rw0), .b(rb0), .eq(comparator_7_eq));  // open: gt, lt
  or or_1 (or_1_out, comparator_6_eq, comparator_7_eq);
  and and_5 (lw, or_1_out, comparator_5_eq);
endmodule

module zhonduan (
  input  clk,
  input  ir1,
  input  ir2,
  input  ir3,
  input  eret,
  output [1:0] xy,
  output w1,
  output zhongduan,
  output w2,
  output w3
);

  wire and_1_out, and_2_out, and_3_out, d_ff_1_q, d_ff_2_q, d_ff_3_q, d_ff_7_q, ie, Ir1_t, Ir2_t, Ir3_t,
       multiplexer_2_out, not_1_out, not_2_out, not_3_out, not_4_out, or_4_out, or_5_out, or_6_out, or_7_out,
       or_8_out, zero1, zero2, zero3;
  wire [1:0] multiplexer_1_out;

  or or_1 (w1, Ir1_t, d_ff_1_q);
  or or_2 (w2, Ir2_t, d_ff_2_q);
  or or_3 (w3, Ir3_t, d_ff_3_q);
  D_Flip_Flop d_ff_1 (.clk(ir1), .D(1'b1), .Q(d_ff_1_q), .reset(Ir1_t));  // open: Qn, preset, en
  D_Flip_Flop d_ff_2 (.clk(ir2), .D(1'b1), .Q(d_ff_2_q), .reset(Ir2_t));  // open: Qn, preset, en
  D_Flip_Flop d_ff_3 (.clk(ir3), .D(1'b1), .Q(d_ff_3_q), .reset(Ir3_t));  // open: Qn, preset, en
  or or_4 (or_4_out, d_ff_1_q, Ir1_t);
  not not_1 (not_1_out, zero1);
  or or_5 (or_5_out, d_ff_2_q, Ir2_t);
  not not_2 (not_2_out, zero2);
  or or_6 (or_6_out, d_ff_3_q, Ir3_t);
  not not_3 (not_3_out, zero3);
  and and_1 (and_1_out, or_4_out, not_1_out);
  and and_2 (and_2_out, or_5_out, not_2_out);
  and and_3 (and_3_out, or_6_out, not_3_out);
  D_Flip_Flop d_ff_4 (.clk(clk), .D(and_1_out), .Q(Ir1_t));  // open: Qn, preset, en, reset
  D_Flip_Flop d_ff_5 (.clk(clk), .D(and_2_out), .Q(Ir2_t));  // open: Qn, preset, en, reset
  D_Flip_Flop d_ff_6 (.clk(clk), .D(and_3_out), .Q(Ir3_t));  // open: Qn, preset, en, reset
  Demultiplexer #(.select(2), .enable("false")) demultiplexer_1 (
    .out1(zero1), .out2(zero2), .out3(zero3), .in(1'b1), .sel(multiplexer_1_out));  // open: out0
  Multiplexer #(.width(2), .enable("false")) multiplexer_1 (
    .in0(2'b00), .in1(xy), .out(multiplexer_1_out), .sel(zhongduan));
  or or_7 (or_7_out, Ir1_t, Ir2_t, Ir3_t);
  D_Flip_Flop d_ff_7 (.clk(zhongduan), .D(1'b1), .Q(d_ff_7_q), .reset(ie));  // open: Qn, preset, en
  Priority_Encoder #(.select(2)) priority_encoder_1 (
    .in0(1'b1), .in1(Ir1_t), .in2(Ir2_t), .in3(Ir3_t), .out(xy));  // open: gs, en_out, en_in
  not not_4 (not_4_out, ie);
  or or_8 (or_8_out, d_ff_7_q, ie);
  and and_4 (zhongduan, or_7_out, not_4_out);
  Multiplexer #(.enable("false")) multiplexer_2 (.in0(or_8_out), .in1(1'b0), .out(multiplexer_2_out), .sel(eret));
  D_Flip_Flop d_ff_8 (.clk(clk), .D(multiplexer_2_out), .Q(ie));  // open: Qn, preset, en, reset

  // Other names for the same wires on the sheet: zd = zhongduan
endmodule
